// Logisim project Arxiu_Font_Final_V2.circ as structural Verilog: 17 circuits, main circuit GUI_REPTE_CENTRALITA
module GUI_REPTE_CENTRALITA (
  input  in_1,
  input  in_2,
  input  in_3,
  input  in_4,
  input  in_5,
  input  in_6,
  input  in_7,
  input  in_8,
  input  in_9
);

  wire a3_display_hm_1_a1, a3_display_hm_1_a2, a3_display_hm_1_a3, a3_display_hm_1_a4, a3_display_hm_1_b1,
       a3_display_hm_1_b2, a3_display_hm_1_b3, a3_display_hm_1_b4, a3_display_hm_1_c1, a3_display_hm_1_c2,
       a3_display_hm_1_c3, a3_display_hm_1_c4, a3_display_hm_1_d1, a3_display_hm_1_d2, a3_display_hm_1_d3,
       a3_display_hm_1_d4, a3_display_hm_1_e1, a3_display_hm_1_e2, a3_display_hm_1_e3, a3_display_hm_1_e4,
       a3_display_hm_1_f1, a3_display_hm_1_f2, a3_display_hm_1_f3, a3_display_hm_1_f4, a3_display_hm_1_g1,
       a3_display_hm_1_g2, a3_display_hm_1_g3, a3_display_hm_1_g4, a3_display_hm_1_out_31,
       a3_display_hm_1_out_33, a3_display_hm_1_out_34, a3_display_hm_1_p1, a3_display_hm_2_a1,
       a3_display_hm_2_a2, a3_display_hm_2_a3, a3_display_hm_2_a4, a3_display_hm_2_b1, a3_display_hm_2_b2,
       a3_display_hm_2_b3, a3_display_hm_2_b4, a3_display_hm_2_c1, a3_display_hm_2_c2, a3_display_hm_2_c3,
       a3_display_hm_2_c4, a3_display_hm_2_d1, a3_display_hm_2_d2, a3_display_hm_2_d3, a3_display_hm_2_d4,
       a3_display_hm_2_e1, a3_display_hm_2_e2, a3_display_hm_2_e3, a3_display_hm_2_e4, a3_display_hm_2_f1,
       a3_display_hm_2_f2, a3_display_hm_2_f3, a3_display_hm_2_f4, a3_display_hm_2_g1, a3_display_hm_2_g2,
       a3_display_hm_2_g3, a3_display_hm_2_g4, a3_display_hm_2_out_31, a3_display_hm_2_out_33,
       a3_display_hm_2_out_34, a3_display_hm_2_p1, a3_display_hm_3_a1, a3_display_hm_3_a2,
       a3_display_hm_3_a3, a3_display_hm_3_a4, a3_display_hm_3_b1, a3_display_hm_3_b2, a3_display_hm_3_b3,
       a3_display_hm_3_b4, a3_display_hm_3_c1, a3_display_hm_3_c2, a3_display_hm_3_c3, a3_display_hm_3_c4,
       a3_display_hm_3_d1, a3_display_hm_3_d2, a3_display_hm_3_d3, a3_display_hm_3_d4, a3_display_hm_3_e1,
       a3_display_hm_3_e2, a3_display_hm_3_e3, a3_display_hm_3_e4, a3_display_hm_3_f1, a3_display_hm_3_f2,
       a3_display_hm_3_f3, a3_display_hm_3_f4, a3_display_hm_3_g1, a3_display_hm_3_g2, a3_display_hm_3_g3,
       a3_display_hm_3_g4, a3_display_hm_3_out_31, a3_display_hm_3_out_33, a3_display_hm_3_out_34,
       a3_display_hm_3_p1, a3_display_hm_4_a1, a3_display_hm_4_a2, a3_display_hm_4_a3, a3_display_hm_4_a4,
       a3_display_hm_4_b1, a3_display_hm_4_b2, a3_display_hm_4_b3, a3_display_hm_4_b4, a3_display_hm_4_c1,
       a3_display_hm_4_c2, a3_display_hm_4_c3, a3_display_hm_4_c4, a3_display_hm_4_d1, a3_display_hm_4_d2,
       a3_display_hm_4_d3, a3_display_hm_4_d4, a3_display_hm_4_e1, a3_display_hm_4_e2, a3_display_hm_4_e3,
       a3_display_hm_4_e4, a3_display_hm_4_f1, a3_display_hm_4_f2, a3_display_hm_4_f3, a3_display_hm_4_f4,
       a3_display_hm_4_g1, a3_display_hm_4_g2, a3_display_hm_4_g3, a3_display_hm_4_g4,
       a3_display_hm_4_out_31, a3_display_hm_4_out_33, a3_display_hm_4_out_34, a3_display_hm_4_p1,
       a3_temp_hores_minuts_1_a1h, a3_temp_hores_minuts_1_a1m, a3_temp_hores_minuts_1_a2h,
       a3_temp_hores_minuts_1_a2m, a3_temp_hores_minuts_1_b1h, a3_temp_hores_minuts_1_b1m,
       a3_temp_hores_minuts_1_b2h, a3_temp_hores_minuts_1_b2m, a3_temp_hores_minuts_1_c1h,
       a3_temp_hores_minuts_1_c1m, a3_temp_hores_minuts_1_c2h, a3_temp_hores_minuts_1_c2m,
       a3_temp_hores_minuts_1_d1h, a3_temp_hores_minuts_1_d1m, a3_temp_hores_minuts_1_d2g,
       a3_temp_hores_minuts_1_d2m, a3_temp_hores_minuts_1_e1h, a3_temp_hores_minuts_1_e1m,
       a3_temp_hores_minuts_1_e2h, a3_temp_hores_minuts_1_e2m, a3_temp_hores_minuts_1_f1h,
       a3_temp_hores_minuts_1_f1m, a3_temp_hores_minuts_1_f2h, a3_temp_hores_minuts_1_f2m,
       a3_temp_hores_minuts_1_g1h, a3_temp_hores_minuts_1_g1m, a3_temp_hores_minuts_1_g2h,
       a3_temp_hores_minuts_1_g2m, a3_temp_hores_minuts_1_p1h, a3_temp_hores_minuts_1_p1m,
       a3_temp_hores_minuts_1_p2h, a3_temp_hores_minuts_1_p2m, a3_temp_hores_minuts_2_a1h,
       a3_temp_hores_minuts_2_a1m, a3_temp_hores_minuts_2_a2h, a3_temp_hores_minuts_2_a2m,
       a3_temp_hores_minuts_2_b1h, a3_temp_hores_minuts_2_b1m, a3_temp_hores_minuts_2_b2h,
       a3_temp_hores_minuts_2_b2m, a3_temp_hores_minuts_2_c1h, a3_temp_hores_minuts_2_c1m,
       a3_temp_hores_minuts_2_c2h, a3_temp_hores_minuts_2_c2m, a3_temp_hores_minuts_2_d1h,
       a3_temp_hores_minuts_2_d1m, a3_temp_hores_minuts_2_d2g, a3_temp_hores_minuts_2_d2m,
       a3_temp_hores_minuts_2_e1h, a3_temp_hores_minuts_2_e1m, a3_temp_hores_minuts_2_e2h,
       a3_temp_hores_minuts_2_e2m, a3_temp_hores_minuts_2_f1h, a3_temp_hores_minuts_2_f1m,
       a3_temp_hores_minuts_2_f2h, a3_temp_hores_minuts_2_f2m, a3_temp_hores_minuts_2_g1h,
       a3_temp_hores_minuts_2_g1m, a3_temp_hores_minuts_2_g2h, a3_temp_hores_minuts_2_g2m,
       a3_temp_hores_minuts_2_p1h, a3_temp_hores_minuts_2_p1m, a3_temp_hores_minuts_2_p2h,
       a3_temp_hores_minuts_2_p2m, a3_temp_hores_minuts_3_a1h, a3_temp_hores_minuts_3_a1m,
       a3_temp_hores_minuts_3_a2h, a3_temp_hores_minuts_3_a2m, a3_temp_hores_minuts_3_b1h,
       a3_temp_hores_minuts_3_b1m, a3_temp_hores_minuts_3_b2h, a3_temp_hores_minuts_3_b2m,
       a3_temp_hores_minuts_3_c1h, a3_temp_hores_minuts_3_c1m, a3_temp_hores_minuts_3_c2h,
       a3_temp_hores_minuts_3_c2m, a3_temp_hores_minuts_3_d1h, a3_temp_hores_minuts_3_d1m,
       a3_temp_hores_minuts_3_d2g, a3_temp_hores_minuts_3_d2m, a3_temp_hores_minuts_3_e1h,
       a3_temp_hores_minuts_3_e1m, a3_temp_hores_minuts_3_e2h, a3_temp_hores_minuts_3_e2m,
       a3_temp_hores_minuts_3_f1h, a3_temp_hores_minuts_3_f1m, a3_temp_hores_minuts_3_f2h,
       a3_temp_hores_minuts_3_f2m, a3_temp_hores_minuts_3_g1h, a3_temp_hores_minuts_3_g1m,
       a3_temp_hores_minuts_3_g2h, a3_temp_hores_minuts_3_g2m, a3_temp_hores_minuts_3_p1h,
       a3_temp_hores_minuts_3_p1m, a3_temp_hores_minuts_3_p2h, a3_temp_hores_minuts_3_p2m,
       a3_temp_hores_minuts_4_a1h, a3_temp_hores_minuts_4_a1m, a3_temp_hores_minuts_4_a2h,
       a3_temp_hores_minuts_4_a2m, a3_temp_hores_minuts_4_b1h, a3_temp_hores_minuts_4_b1m,
       a3_temp_hores_minuts_4_b2h, a3_temp_hores_minuts_4_b2m, a3_temp_hores_minuts_4_c1h,
       a3_temp_hores_minuts_4_c1m, a3_temp_hores_minuts_4_c2h, a3_temp_hores_minuts_4_c2m,
       a3_temp_hores_minuts_4_d1h, a3_temp_hores_minuts_4_d1m, a3_temp_hores_minuts_4_d2g,
       a3_temp_hores_minuts_4_d2m, a3_temp_hores_minuts_4_e1h, a3_temp_hores_minuts_4_e1m,
       a3_temp_hores_minuts_4_e2h, a3_temp_hores_minuts_4_e2m, a3_temp_hores_minuts_4_f1h,
       a3_temp_hores_minuts_4_f1m, a3_temp_hores_minuts_4_f2h, a3_temp_hores_minuts_4_f2m,
       a3_temp_hores_minuts_4_g1h, a3_temp_hores_minuts_4_g1m, a3_temp_hores_minuts_4_g2h,
       a3_temp_hores_minuts_4_g2m, a3_temp_hores_minuts_4_p1h, a3_temp_hores_minuts_4_p1m,
       a3_temp_hores_minuts_4_p2h, a3_temp_hores_minuts_4_p2m, a3_temp_hores_minuts_5_a1h,
       a3_temp_hores_minuts_5_a1m, a3_temp_hores_minuts_5_a2h, a3_temp_hores_minuts_5_a2m,
       a3_temp_hores_minuts_5_b1h, a3_temp_hores_minuts_5_b1m, a3_temp_hores_minuts_5_b2h,
       a3_temp_hores_minuts_5_b2m, a3_temp_hores_minuts_5_c1h, a3_temp_hores_minuts_5_c1m,
       a3_temp_hores_minuts_5_c2h, a3_temp_hores_minuts_5_c2m, a3_temp_hores_minuts_5_d1h,
       a3_temp_hores_minuts_5_d1m, a3_temp_hores_minuts_5_d2g, a3_temp_hores_minuts_5_d2m,
       a3_temp_hores_minuts_5_e1h, a3_temp_hores_minuts_5_e1m, a3_temp_hores_minuts_5_e2h,
       a3_temp_hores_minuts_5_e2m, a3_temp_hores_minuts_5_f1h, a3_temp_hores_minuts_5_f1m,
       a3_temp_hores_minuts_5_f2h, a3_temp_hores_minuts_5_f2m, a3_temp_hores_minuts_5_g1h,
       a3_temp_hores_minuts_5_g1m, a3_temp_hores_minuts_5_g2h, a3_temp_hores_minuts_5_g2m,
       a3_temp_hores_minuts_5_p1h, a3_temp_hores_minuts_5_p1m, a3_temp_hores_minuts_5_p2h,
       a3_temp_hores_minuts_5_p2m, a3_temp_hores_minuts_6_a1h, a3_temp_hores_minuts_6_a1m,
       a3_temp_hores_minuts_6_a2h, a3_temp_hores_minuts_6_a2m, a3_temp_hores_minuts_6_b1h,
       a3_temp_hores_minuts_6_b1m, a3_temp_hores_minuts_6_b2h, a3_temp_hores_minuts_6_b2m,
       a3_temp_hores_minuts_6_c1h, a3_temp_hores_minuts_6_c1m, a3_temp_hores_minuts_6_c2h,
       a3_temp_hores_minuts_6_c2m, a3_temp_hores_minuts_6_d1h, a3_temp_hores_minuts_6_d1m,
       a3_temp_hores_minuts_6_d2g, a3_temp_hores_minuts_6_d2m, a3_temp_hores_minuts_6_e1h,
       a3_temp_hores_minuts_6_e1m, a3_temp_hores_minuts_6_e2h, a3_temp_hores_minuts_6_e2m,
       a3_temp_hores_minuts_6_f1h, a3_temp_hores_minuts_6_f1m, a3_temp_hores_minuts_6_f2h,
       a3_temp_hores_minuts_6_f2m, a3_temp_hores_minuts_6_g1h, a3_temp_hores_minuts_6_g1m,
       a3_temp_hores_minuts_6_g2h, a3_temp_hores_minuts_6_g2m, a3_temp_hores_minuts_6_p1h,
       a3_temp_hores_minuts_6_p1m, a3_temp_hores_minuts_6_p2h, a3_temp_hores_minuts_6_p2m,
       a3_temp_hores_minuts_7_a1h, a3_temp_hores_minuts_7_a1m, a3_temp_hores_minuts_7_a2h,
       a3_temp_hores_minuts_7_a2m, a3_temp_hores_minuts_7_b1h, a3_temp_hores_minuts_7_b1m,
       a3_temp_hores_minuts_7_b2h, a3_temp_hores_minuts_7_b2m, a3_temp_hores_minuts_7_c1h,
       a3_temp_hores_minuts_7_c1m, a3_temp_hores_minuts_7_c2h, a3_temp_hores_minuts_7_c2m,
       a3_temp_hores_minuts_7_d1h, a3_temp_hores_minuts_7_d1m, a3_temp_hores_minuts_7_d2g,
       a3_temp_hores_minuts_7_d2m, a3_temp_hores_minuts_7_e1h, a3_temp_hores_minuts_7_e1m,
       a3_temp_hores_minuts_7_e2h, a3_temp_hores_minuts_7_e2m, a3_temp_hores_minuts_7_f1h,
       a3_temp_hores_minuts_7_f1m, a3_temp_hores_minuts_7_f2h, a3_temp_hores_minuts_7_f2m,
       a3_temp_hores_minuts_7_g1h, a3_temp_hores_minuts_7_g1m, a3_temp_hores_minuts_7_g2h,
       a3_temp_hores_minuts_7_g2m, a3_temp_hores_minuts_7_p1h, a3_temp_hores_minuts_7_p1m,
       a3_temp_hores_minuts_7_p2h, a3_temp_hores_minuts_7_p2m, a3_temp_hores_minuts_8_a1h,
       a3_temp_hores_minuts_8_a1m, a3_temp_hores_minuts_8_a2h, a3_temp_hores_minuts_8_a2m,
       a3_temp_hores_minuts_8_b1h, a3_temp_hores_minuts_8_b1m, a3_temp_hores_minuts_8_b2h,
       a3_temp_hores_minuts_8_b2m, a3_temp_hores_minuts_8_c1h, a3_temp_hores_minuts_8_c1m,
       a3_temp_hores_minuts_8_c2h, a3_temp_hores_minuts_8_c2m, a3_temp_hores_minuts_8_d1h,
       a3_temp_hores_minuts_8_d1m, a3_temp_hores_minuts_8_d2g, a3_temp_hores_minuts_8_d2m,
       a3_temp_hores_minuts_8_e1h, a3_temp_hores_minuts_8_e1m, a3_temp_hores_minuts_8_e2h,
       a3_temp_hores_minuts_8_e2m, a3_temp_hores_minuts_8_f1h, a3_temp_hores_minuts_8_f1m,
       a3_temp_hores_minuts_8_f2h, a3_temp_hores_minuts_8_f2m, a3_temp_hores_minuts_8_g1h,
       a3_temp_hores_minuts_8_g1m, a3_temp_hores_minuts_8_g2h, a3_temp_hores_minuts_8_g2m,
       a3_temp_hores_minuts_8_p1h, a3_temp_hores_minuts_8_p1m, a3_temp_hores_minuts_8_p2h,
       a3_temp_hores_minuts_8_p2m, a3_temp_hores_minuts_9_a1h, a3_temp_hores_minuts_9_a1m,
       a3_temp_hores_minuts_9_a2h, a3_temp_hores_minuts_9_a2m, a3_temp_hores_minuts_9_b1h,
       a3_temp_hores_minuts_9_b1m, a3_temp_hores_minuts_9_b2h, a3_temp_hores_minuts_9_b2m,
       a3_temp_hores_minuts_9_c1h, a3_temp_hores_minuts_9_c1m, a3_temp_hores_minuts_9_c2h,
       a3_temp_hores_minuts_9_c2m, a3_temp_hores_minuts_9_d1h, a3_temp_hores_minuts_9_d1m,
       a3_temp_hores_minuts_9_d2g, a3_temp_hores_minuts_9_d2m, a3_temp_hores_minuts_9_e1h,
       a3_temp_hores_minuts_9_e1m, a3_temp_hores_minuts_9_e2h, a3_temp_hores_minuts_9_e2m,
       a3_temp_hores_minuts_9_f1h, a3_temp_hores_minuts_9_f1m, a3_temp_hores_minuts_9_f2h,
       a3_temp_hores_minuts_9_f2m, a3_temp_hores_minuts_9_g1h, a3_temp_hores_minuts_9_g1m,
       a3_temp_hores_minuts_9_g2h, a3_temp_hores_minuts_9_g2m, a3_temp_hores_minuts_9_p1h,
       a3_temp_hores_minuts_9_p1m, a3_temp_hores_minuts_9_p2h, a3_temp_hores_minuts_9_p2m,
       a4_rellotge_intern_1_a1, a4_rellotge_intern_1_a2, a4_rellotge_intern_1_a3, a4_rellotge_intern_1_a4,
       a4_rellotge_intern_1_a5, a4_rellotge_intern_1_a6, a4_rellotge_intern_1_b1, a4_rellotge_intern_1_b2,
       a4_rellotge_intern_1_b3, a4_rellotge_intern_1_b4, a4_rellotge_intern_1_b5, a4_rellotge_intern_1_b6,
       a4_rellotge_intern_1_c1, a4_rellotge_intern_1_c2, a4_rellotge_intern_1_c3, a4_rellotge_intern_1_c4,
       a4_rellotge_intern_1_c5, a4_rellotge_intern_1_c6, a4_rellotge_intern_1_d1, a4_rellotge_intern_1_d2,
       a4_rellotge_intern_1_d3, a4_rellotge_intern_1_d4, a4_rellotge_intern_1_d5, a4_rellotge_intern_1_d6,
       a4_rellotge_intern_1_e1, a4_rellotge_intern_1_e2, a4_rellotge_intern_1_e3, a4_rellotge_intern_1_e4,
       a4_rellotge_intern_1_e5, a4_rellotge_intern_1_e6, a4_rellotge_intern_1_f1, a4_rellotge_intern_1_f2,
       a4_rellotge_intern_1_f3, a4_rellotge_intern_1_f4, a4_rellotge_intern_1_f5, a4_rellotge_intern_1_f6,
       a4_rellotge_intern_1_g1, a4_rellotge_intern_1_g2, a4_rellotge_intern_1_g3, a4_rellotge_intern_1_g4,
       a4_rellotge_intern_1_g5, a4_rellotge_intern_1_g6, a4_rellotge_intern_1_p1, a4_rellotge_intern_1_p2,
       a4_rellotge_intern_1_p3, a4_rellotge_intern_1_p4, a4_rellotge_intern_1_p5, a4_rellotge_intern_1_p6,
       ActA, ActP, AFR, AH1, AH2, AM1, AM2, ARC, b0_ctrl_temperatura_1_a1, b0_ctrl_temperatura_1_a2,
       b0_ctrl_temperatura_1_a3, b0_ctrl_temperatura_1_b1, b0_ctrl_temperatura_1_b2,
       b0_ctrl_temperatura_1_b3, b0_ctrl_temperatura_1_c1, b0_ctrl_temperatura_1_c2,
       b0_ctrl_temperatura_1_c3, b0_ctrl_temperatura_1_d1, b0_ctrl_temperatura_1_d2,
       b0_ctrl_temperatura_1_d3, b0_ctrl_temperatura_1_e1, b0_ctrl_temperatura_1_e2,
       b0_ctrl_temperatura_1_e3, b0_ctrl_temperatura_1_f1, b0_ctrl_temperatura_1_f2,
       b0_ctrl_temperatura_1_f3, b0_ctrl_temperatura_1_g1, b0_ctrl_temperatura_1_g2,
       b0_ctrl_temperatura_1_g3, b0_ctrl_temperatura_1_p1, b0_ctrl_temperatura_1_p2,
       b0_ctrl_temperatura_1_p3, b0_ctrl_temperatura_2_a1, b0_ctrl_temperatura_2_a2,
       b0_ctrl_temperatura_2_a3, b0_ctrl_temperatura_2_b1, b0_ctrl_temperatura_2_b2,
       b0_ctrl_temperatura_2_b3, b0_ctrl_temperatura_2_c1, b0_ctrl_temperatura_2_c2,
       b0_ctrl_temperatura_2_c3, b0_ctrl_temperatura_2_d1, b0_ctrl_temperatura_2_d2,
       b0_ctrl_temperatura_2_d3, b0_ctrl_temperatura_2_e1, b0_ctrl_temperatura_2_e2,
       b0_ctrl_temperatura_2_e3, b0_ctrl_temperatura_2_f1, b0_ctrl_temperatura_2_f2,
       b0_ctrl_temperatura_2_f3, b0_ctrl_temperatura_2_g1, b0_ctrl_temperatura_2_g2,
       b0_ctrl_temperatura_2_g3, b0_ctrl_temperatura_2_p1, b0_ctrl_temperatura_2_p2,
       b0_ctrl_temperatura_2_p3, b0_ctrl_temperatura_3_a1, b0_ctrl_temperatura_3_a2,
       b0_ctrl_temperatura_3_a3, b0_ctrl_temperatura_3_b1, b0_ctrl_temperatura_3_b2,
       b0_ctrl_temperatura_3_b3, b0_ctrl_temperatura_3_c1, b0_ctrl_temperatura_3_c2,
       b0_ctrl_temperatura_3_c3, b0_ctrl_temperatura_3_d1, b0_ctrl_temperatura_3_d2,
       b0_ctrl_temperatura_3_d3, b0_ctrl_temperatura_3_e1, b0_ctrl_temperatura_3_e2,
       b0_ctrl_temperatura_3_e3, b0_ctrl_temperatura_3_f1, b0_ctrl_temperatura_3_f2,
       b0_ctrl_temperatura_3_f3, b0_ctrl_temperatura_3_g1, b0_ctrl_temperatura_3_g2,
       b0_ctrl_temperatura_3_g3, b0_ctrl_temperatura_3_p1, b0_ctrl_temperatura_3_p2,
       b0_ctrl_temperatura_3_p3, b2_ctrl_humetatrelativa_1_a1, b2_ctrl_humetatrelativa_1_a2,
       b2_ctrl_humetatrelativa_1_a3, b2_ctrl_humetatrelativa_1_b1, b2_ctrl_humetatrelativa_1_b2,
       b2_ctrl_humetatrelativa_1_b3, b2_ctrl_humetatrelativa_1_c1, b2_ctrl_humetatrelativa_1_c2,
       b2_ctrl_humetatrelativa_1_c3, b2_ctrl_humetatrelativa_1_d1, b2_ctrl_humetatrelativa_1_d2,
       b2_ctrl_humetatrelativa_1_d3, b2_ctrl_humetatrelativa_1_e1, b2_ctrl_humetatrelativa_1_e2,
       b2_ctrl_humetatrelativa_1_e3, b2_ctrl_humetatrelativa_1_f1, b2_ctrl_humetatrelativa_1_f2,
       b2_ctrl_humetatrelativa_1_f3, b2_ctrl_humetatrelativa_1_g1, b2_ctrl_humetatrelativa_1_g2,
       b2_ctrl_humetatrelativa_1_g3, b2_ctrl_humetatrelativa_1_p1, b2_ctrl_humetatrelativa_1_p2,
       b2_ctrl_humetatrelativa_1_p3, b2_ctrl_humetatrelativa_2_a1, b2_ctrl_humetatrelativa_2_a2,
       b2_ctrl_humetatrelativa_2_a3, b2_ctrl_humetatrelativa_2_b1, b2_ctrl_humetatrelativa_2_b2,
       b2_ctrl_humetatrelativa_2_b3, b2_ctrl_humetatrelativa_2_c1, b2_ctrl_humetatrelativa_2_c2,
       b2_ctrl_humetatrelativa_2_c3, b2_ctrl_humetatrelativa_2_d1, b2_ctrl_humetatrelativa_2_d2,
       b2_ctrl_humetatrelativa_2_d3, b2_ctrl_humetatrelativa_2_e1, b2_ctrl_humetatrelativa_2_e2,
       b2_ctrl_humetatrelativa_2_e3, b2_ctrl_humetatrelativa_2_f1, b2_ctrl_humetatrelativa_2_f2,
       b2_ctrl_humetatrelativa_2_f3, b2_ctrl_humetatrelativa_2_g1, b2_ctrl_humetatrelativa_2_g2,
       b2_ctrl_humetatrelativa_2_g3, b2_ctrl_humetatrelativa_2_p1, b2_ctrl_humetatrelativa_2_p2,
       b2_ctrl_humetatrelativa_2_p3, b2_ctrl_humetatrelativa_3_a1, b2_ctrl_humetatrelativa_3_a2,
       b2_ctrl_humetatrelativa_3_a3, b2_ctrl_humetatrelativa_3_b1, b2_ctrl_humetatrelativa_3_b2,
       b2_ctrl_humetatrelativa_3_b3, b2_ctrl_humetatrelativa_3_c1, b2_ctrl_humetatrelativa_3_c2,
       b2_ctrl_humetatrelativa_3_c3, b2_ctrl_humetatrelativa_3_d1, b2_ctrl_humetatrelativa_3_d2,
       b2_ctrl_humetatrelativa_3_d3, b2_ctrl_humetatrelativa_3_e1, b2_ctrl_humetatrelativa_3_e2,
       b2_ctrl_humetatrelativa_3_e3, b2_ctrl_humetatrelativa_3_f1, b2_ctrl_humetatrelativa_3_f2,
       b2_ctrl_humetatrelativa_3_f3, b2_ctrl_humetatrelativa_3_g1, b2_ctrl_humetatrelativa_3_g2,
       b2_ctrl_humetatrelativa_3_g3, b2_ctrl_humetatrelativa_3_p1, b2_ctrl_humetatrelativa_3_p2,
       b2_ctrl_humetatrelativa_3_p3, DESHU, EMHMA, EMHR, EMMMA, EMMR, HH1, HH2, HM1, HM2, HUMI, JAR, JEH1,
       JEH2, JEM1, JEM2, JIH1, JIH2, JIM1, JIM2, K, L, L3S, LA, LAV1, LAV2, LH, LJA, LJCE, LJCI, LJE, LJH,
       LJI, LOOFT, M1, M2, MEH, MEHR, MEHS, MEQ, MET, METR, METS, MYH, MYHR, MYHS, MYT, MYTR, MYTS, o, OOFT,
       POL, PROP, S, SAE1, SAE2, VA, VE, VH, VI;
  wire [7:0] HIS, HPR, HRE, TIS, TPR, TRE;
  wire [15:0] CRA, CRH, CRJE, CRJI, HA, HH, HJE, HJI, TA, TACR, TC, TH, THCR, TJE, TJECR, TJI, TJICR, TR;

  _7_Segment_Display #(.active("false")) u_7_segment_display_1 (
    .g(a3_temp_hores_minuts_1_g2h), .f(a3_temp_hores_minuts_1_f2h), .a(a3_temp_hores_minuts_1_a2h),
    .b(a3_temp_hores_minuts_1_b2h), .e(a3_temp_hores_minuts_1_e2h), .d(a3_temp_hores_minuts_1_d2g),
    .c(a3_temp_hores_minuts_1_c2h), .dp(a3_temp_hores_minuts_1_p2h));
  A3_Temp_Hores_Minuts a3_temp_hores_minuts_1 (
    .Entrada_H(JIH2), .Entrada_M(JIM2), .G2H(a3_temp_hores_minuts_1_g2h), .E2H(a3_temp_hores_minuts_1_e2h),
    .F2H(a3_temp_hores_minuts_1_f2h), .D2G(a3_temp_hores_minuts_1_d2g), .A2H(a3_temp_hores_minuts_1_a2h),
    .C2H(a3_temp_hores_minuts_1_c2h), .B2H(a3_temp_hores_minuts_1_b2h), .P2H(a3_temp_hores_minuts_1_p2h),
    .G1H(a3_temp_hores_minuts_1_g1h), .E1H(a3_temp_hores_minuts_1_e1h), .F1H(a3_temp_hores_minuts_1_f1h),
    .D1H(a3_temp_hores_minuts_1_d1h), .A1H(a3_temp_hores_minuts_1_a1h), .C1H(a3_temp_hores_minuts_1_c1h),
    .B1H(a3_temp_hores_minuts_1_b1h), .P1H(a3_temp_hores_minuts_1_p1h), .G2M(a3_temp_hores_minuts_1_g2m),
    .E2M(a3_temp_hores_minuts_1_e2m), .F2M(a3_temp_hores_minuts_1_f2m), .D2M(a3_temp_hores_minuts_1_d2m),
    .A2M(a3_temp_hores_minuts_1_a2m), .C2M(a3_temp_hores_minuts_1_c2m), .B2M(a3_temp_hores_minuts_1_b2m),
    .P2M(a3_temp_hores_minuts_1_p2m), .G1M(a3_temp_hores_minuts_1_g1m), .E1M(a3_temp_hores_minuts_1_e1m),
    .F1M(a3_temp_hores_minuts_1_f1m), .D1M(a3_temp_hores_minuts_1_d1m), .A1M(a3_temp_hores_minuts_1_a1m),
    .C1M(a3_temp_hores_minuts_1_c1m), .TB_MA(HJI), .B1M(a3_temp_hores_minuts_1_b1m),
    .P1M(a3_temp_hores_minuts_1_p1m));
  _7_Segment_Display #(.active("false")) u_7_segment_display_2 (
    .g(a3_temp_hores_minuts_2_g2h), .f(a3_temp_hores_minuts_2_f2h), .a(a3_temp_hores_minuts_2_a2h),
    .b(a3_temp_hores_minuts_2_b2h), .e(a3_temp_hores_minuts_2_e2h), .d(a3_temp_hores_minuts_2_d2g),
    .c(a3_temp_hores_minuts_2_c2h), .dp(a3_temp_hores_minuts_2_p2h));
  A3_Temp_Hores_Minuts a3_temp_hores_minuts_2 (
    .Entrada_H(HH2), .Entrada_M(HM2), .G2H(a3_temp_hores_minuts_2_g2h), .E2H(a3_temp_hores_minuts_2_e2h),
    .F2H(a3_temp_hores_minuts_2_f2h), .D2G(a3_temp_hores_minuts_2_d2g), .A2H(a3_temp_hores_minuts_2_a2h),
    .C2H(a3_temp_hores_minuts_2_c2h), .B2H(a3_temp_hores_minuts_2_b2h), .P2H(a3_temp_hores_minuts_2_p2h),
    .G1H(a3_temp_hores_minuts_2_g1h), .E1H(a3_temp_hores_minuts_2_e1h), .F1H(a3_temp_hores_minuts_2_f1h),
    .D1H(a3_temp_hores_minuts_2_d1h), .A1H(a3_temp_hores_minuts_2_a1h), .C1H(a3_temp_hores_minuts_2_c1h),
    .B1H(a3_temp_hores_minuts_2_b1h), .P1H(a3_temp_hores_minuts_2_p1h), .G2M(a3_temp_hores_minuts_2_g2m),
    .E2M(a3_temp_hores_minuts_2_e2m), .F2M(a3_temp_hores_minuts_2_f2m), .D2M(a3_temp_hores_minuts_2_d2m),
    .A2M(a3_temp_hores_minuts_2_a2m), .C2M(a3_temp_hores_minuts_2_c2m), .B2M(a3_temp_hores_minuts_2_b2m),
    .P2M(a3_temp_hores_minuts_2_p2m), .G1M(a3_temp_hores_minuts_2_g1m), .E1M(a3_temp_hores_minuts_2_e1m),
    .F1M(a3_temp_hores_minuts_2_f1m), .D1M(a3_temp_hores_minuts_2_d1m), .A1M(a3_temp_hores_minuts_2_a1m),
    .C1M(a3_temp_hores_minuts_2_c1m), .TB_MA(HH), .B1M(a3_temp_hores_minuts_2_b1m),
    .P1M(a3_temp_hores_minuts_2_p1m));
  _7_Segment_Display #(.active("false")) u_7_segment_display_3 (
    .g(a4_rellotge_intern_1_g6), .f(a4_rellotge_intern_1_f6), .a(a4_rellotge_intern_1_a6),
    .b(a4_rellotge_intern_1_b6), .e(a4_rellotge_intern_1_e6), .d(a4_rellotge_intern_1_d6),
    .c(a4_rellotge_intern_1_c6), .dp(a4_rellotge_intern_1_p6));
  Button button_1 (.out(EMHR));
  _7_Segment_Display #(.active("false")) u_7_segment_display_4 (
    .g(a3_temp_hores_minuts_1_g1h), .f(a3_temp_hores_minuts_1_f1h), .a(a3_temp_hores_minuts_1_a1h),
    .b(a3_temp_hores_minuts_1_b1h), .e(a3_temp_hores_minuts_1_e1h), .d(a3_temp_hores_minuts_1_d1h),
    .c(a3_temp_hores_minuts_1_c1h), .dp(a3_temp_hores_minuts_1_p1h));
  Button button_2 (.out(JIH2));
  _7_Segment_Display #(.active("false")) u_7_segment_display_5 (
    .g(a3_temp_hores_minuts_2_g1h), .f(a3_temp_hores_minuts_2_f1h), .a(a3_temp_hores_minuts_2_a1h),
    .b(a3_temp_hores_minuts_2_b1h), .e(a3_temp_hores_minuts_2_e1h), .d(a3_temp_hores_minuts_2_d1h),
    .c(a3_temp_hores_minuts_2_c1h), .dp(a3_temp_hores_minuts_2_p1h));
  Button button_3 (.out(HH2));
  _7_Segment_Display #(.active("false")) u_7_segment_display_6 (
    .g(a4_rellotge_intern_1_g5), .f(a4_rellotge_intern_1_f5), .a(a4_rellotge_intern_1_a5),
    .b(a4_rellotge_intern_1_b5), .e(a4_rellotge_intern_1_e5), .d(a4_rellotge_intern_1_d5),
    .c(a4_rellotge_intern_1_c5), .dp(a4_rellotge_intern_1_p5));
  _7_Segment_Display #(.active("false")) u_7_segment_display_7 (
    .g(a3_temp_hores_minuts_1_g2m), .f(a3_temp_hores_minuts_1_f2m), .a(a3_temp_hores_minuts_1_a2m),
    .b(a3_temp_hores_minuts_1_b2m), .e(a3_temp_hores_minuts_1_e2m), .d(a3_temp_hores_minuts_1_d2m),
    .c(a3_temp_hores_minuts_1_c2m), .dp(a3_temp_hores_minuts_1_p2m));
  Button button_4 (.out(JIM2));
  _7_Segment_Display #(.active("false")) u_7_segment_display_8 (
    .g(a3_temp_hores_minuts_2_g2m), .f(a3_temp_hores_minuts_2_f2m), .a(a3_temp_hores_minuts_2_a2m),
    .b(a3_temp_hores_minuts_2_b2m), .e(a3_temp_hores_minuts_2_e2m), .d(a3_temp_hores_minuts_2_d2m),
    .c(a3_temp_hores_minuts_2_c2m), .dp(a3_temp_hores_minuts_2_p2m));
  Button button_5 (.out(HM2));
  _7_Segment_Display #(.active("false")) u_7_segment_display_9 (
    .g(a4_rellotge_intern_1_g4), .f(a4_rellotge_intern_1_f4), .a(a4_rellotge_intern_1_a4),
    .b(a4_rellotge_intern_1_b4), .e(a4_rellotge_intern_1_e4), .d(a4_rellotge_intern_1_d4),
    .c(a4_rellotge_intern_1_c4), .dp(a4_rellotge_intern_1_p4));
  _7_Segment_Display #(.active("false")) u_7_segment_display_10 (
    .g(a4_rellotge_intern_1_g3), .f(a4_rellotge_intern_1_f3), .a(a4_rellotge_intern_1_a3),
    .b(a4_rellotge_intern_1_b3), .e(a4_rellotge_intern_1_e3), .d(a4_rellotge_intern_1_d3),
    .c(a4_rellotge_intern_1_c3), .dp(a4_rellotge_intern_1_p3));
  Button button_6 (.out(EMMR));
  _7_Segment_Display #(.active("false")) u_7_segment_display_11 (
    .g(a3_temp_hores_minuts_1_g1m), .f(a3_temp_hores_minuts_1_f1m), .a(a3_temp_hores_minuts_1_a1m),
    .b(a3_temp_hores_minuts_1_b1m), .e(a3_temp_hores_minuts_1_e1m), .d(a3_temp_hores_minuts_1_d1m),
    .c(a3_temp_hores_minuts_1_c1m), .dp(a3_temp_hores_minuts_1_p1m));
  _7_Segment_Display #(.active("false")) u_7_segment_display_12 (
    .g(a3_temp_hores_minuts_2_g1m), .f(a3_temp_hores_minuts_2_f1m), .a(a3_temp_hores_minuts_2_a1m),
    .b(a3_temp_hores_minuts_2_b1m), .e(a3_temp_hores_minuts_2_e1m), .d(a3_temp_hores_minuts_2_d1m),
    .c(a3_temp_hores_minuts_2_c1m), .dp(a3_temp_hores_minuts_2_p1m));
  _7_Segment_Display #(.active("false")) u_7_segment_display_13 (
    .g(a4_rellotge_intern_1_g2), .f(a4_rellotge_intern_1_f2), .a(a4_rellotge_intern_1_a2),
    .b(a4_rellotge_intern_1_b2), .e(a4_rellotge_intern_1_e2), .d(a4_rellotge_intern_1_d2),
    .c(a4_rellotge_intern_1_c2), .dp(a4_rellotge_intern_1_p2));
  _7_Segment_Display #(.active("false")) u_7_segment_display_14 (
    .g(a3_temp_hores_minuts_3_g2h), .f(a3_temp_hores_minuts_3_f2h), .a(a3_temp_hores_minuts_3_a2h),
    .b(a3_temp_hores_minuts_3_b2h), .e(a3_temp_hores_minuts_3_e2h), .d(a3_temp_hores_minuts_3_d2g),
    .c(a3_temp_hores_minuts_3_c2h), .dp(a3_temp_hores_minuts_3_p2h));
  A3_Temp_Hores_Minuts a3_temp_hores_minuts_3 (
    .Entrada_H(JIH1), .Entrada_M(JIM1), .G2H(a3_temp_hores_minuts_3_g2h), .E2H(a3_temp_hores_minuts_3_e2h),
    .F2H(a3_temp_hores_minuts_3_f2h), .D2G(a3_temp_hores_minuts_3_d2g), .A2H(a3_temp_hores_minuts_3_a2h),
    .C2H(a3_temp_hores_minuts_3_c2h), .B2H(a3_temp_hores_minuts_3_b2h), .P2H(a3_temp_hores_minuts_3_p2h),
    .G1H(a3_temp_hores_minuts_3_g1h), .E1H(a3_temp_hores_minuts_3_e1h), .F1H(a3_temp_hores_minuts_3_f1h),
    .D1H(a3_temp_hores_minuts_3_d1h), .A1H(a3_temp_hores_minuts_3_a1h), .C1H(a3_temp_hores_minuts_3_c1h),
    .B1H(a3_temp_hores_minuts_3_b1h), .P1H(a3_temp_hores_minuts_3_p1h), .G2M(a3_temp_hores_minuts_3_g2m),
    .E2M(a3_temp_hores_minuts_3_e2m), .F2M(a3_temp_hores_minuts_3_f2m), .D2M(a3_temp_hores_minuts_3_d2m),
    .A2M(a3_temp_hores_minuts_3_a2m), .C2M(a3_temp_hores_minuts_3_c2m), .B2M(a3_temp_hores_minuts_3_b2m),
    .P2M(a3_temp_hores_minuts_3_p2m), .G1M(a3_temp_hores_minuts_3_g1m), .E1M(a3_temp_hores_minuts_3_e1m),
    .F1M(a3_temp_hores_minuts_3_f1m), .D1M(a3_temp_hores_minuts_3_d1m), .A1M(a3_temp_hores_minuts_3_a1m),
    .C1M(a3_temp_hores_minuts_3_c1m), .TB_MA(TJI), .B1M(a3_temp_hores_minuts_3_b1m),
    .P1M(a3_temp_hores_minuts_3_p1m));
  _7_Segment_Display #(.active("false")) u_7_segment_display_15 (
    .g(a3_temp_hores_minuts_4_g2h), .f(a3_temp_hores_minuts_4_f2h), .a(a3_temp_hores_minuts_4_a2h),
    .b(a3_temp_hores_minuts_4_b2h), .e(a3_temp_hores_minuts_4_e2h), .d(a3_temp_hores_minuts_4_d2g),
    .c(a3_temp_hores_minuts_4_c2h), .dp(a3_temp_hores_minuts_4_p2h));
  A3_Temp_Hores_Minuts a3_temp_hores_minuts_4 (
    .Entrada_H(HH1), .Entrada_M(HM1), .G2H(a3_temp_hores_minuts_4_g2h), .E2H(a3_temp_hores_minuts_4_e2h),
    .F2H(a3_temp_hores_minuts_4_f2h), .D2G(a3_temp_hores_minuts_4_d2g), .A2H(a3_temp_hores_minuts_4_a2h),
    .C2H(a3_temp_hores_minuts_4_c2h), .B2H(a3_temp_hores_minuts_4_b2h), .P2H(a3_temp_hores_minuts_4_p2h),
    .G1H(a3_temp_hores_minuts_4_g1h), .E1H(a3_temp_hores_minuts_4_e1h), .F1H(a3_temp_hores_minuts_4_f1h),
    .D1H(a3_temp_hores_minuts_4_d1h), .A1H(a3_temp_hores_minuts_4_a1h), .C1H(a3_temp_hores_minuts_4_c1h),
    .B1H(a3_temp_hores_minuts_4_b1h), .P1H(a3_temp_hores_minuts_4_p1h), .G2M(a3_temp_hores_minuts_4_g2m),
    .E2M(a3_temp_hores_minuts_4_e2m), .F2M(a3_temp_hores_minuts_4_f2m), .D2M(a3_temp_hores_minuts_4_d2m),
    .A2M(a3_temp_hores_minuts_4_a2m), .C2M(a3_temp_hores_minuts_4_c2m), .B2M(a3_temp_hores_minuts_4_b2m),
    .P2M(a3_temp_hores_minuts_4_p2m), .G1M(a3_temp_hores_minuts_4_g1m), .E1M(a3_temp_hores_minuts_4_e1m),
    .F1M(a3_temp_hores_minuts_4_f1m), .D1M(a3_temp_hores_minuts_4_d1m), .A1M(a3_temp_hores_minuts_4_a1m),
    .C1M(a3_temp_hores_minuts_4_c1m), .TB_MA(TH), .B1M(a3_temp_hores_minuts_4_b1m),
    .P1M(a3_temp_hores_minuts_4_p1m));
  _7_Segment_Display #(.active("false")) u_7_segment_display_16 (
    .g(a4_rellotge_intern_1_g1), .f(a4_rellotge_intern_1_f1), .a(a4_rellotge_intern_1_a1),
    .b(a4_rellotge_intern_1_b1), .e(a4_rellotge_intern_1_e1), .d(a4_rellotge_intern_1_d1),
    .c(a4_rellotge_intern_1_c1), .dp(a4_rellotge_intern_1_p1));
  A4_Rellotge_Intern a4_rellotge_intern_1 (
    .Entrada_Manual_M(EMMR), .Power(1'b1), .Entrada_manual_H(EMHR), .E4(a4_rellotge_intern_1_e4),
    .F4(a4_rellotge_intern_1_f4), .G4(a4_rellotge_intern_1_g4), .P4(a4_rellotge_intern_1_p4),
    .A3(a4_rellotge_intern_1_a3), .B3(a4_rellotge_intern_1_b3), .C3(a4_rellotge_intern_1_c3),
    .D3(a4_rellotge_intern_1_d3), .E3(a4_rellotge_intern_1_e3), .F3(a4_rellotge_intern_1_f3),
    .G3(a4_rellotge_intern_1_g3), .p3(a4_rellotge_intern_1_p3), .A2(a4_rellotge_intern_1_a2),
    .B2(a4_rellotge_intern_1_b2), .C2(a4_rellotge_intern_1_c2), .D2(a4_rellotge_intern_1_d2),
    .E2(a4_rellotge_intern_1_e2), .F2(a4_rellotge_intern_1_f2), .G2(a4_rellotge_intern_1_g2),
    .P2(a4_rellotge_intern_1_p2), .A1(a4_rellotge_intern_1_a1), .B1(a4_rellotge_intern_1_b1),
    .C1(a4_rellotge_intern_1_c1), .D1(a4_rellotge_intern_1_d1), .E1(a4_rellotge_intern_1_e1),
    .F1(a4_rellotge_intern_1_f1), .G1(a4_rellotge_intern_1_g1), .P1(a4_rellotge_intern_1_p1),
    .A6(a4_rellotge_intern_1_a6), .B6(a4_rellotge_intern_1_b6), .C6(a4_rellotge_intern_1_c6),
    .D6(a4_rellotge_intern_1_d6), .E6(a4_rellotge_intern_1_e6), .F6(a4_rellotge_intern_1_f6),
    .G6(a4_rellotge_intern_1_g6), .P6(a4_rellotge_intern_1_p6), .A5(a4_rellotge_intern_1_a5),
    .B5(a4_rellotge_intern_1_b5), .C5(a4_rellotge_intern_1_c5), .D5(a4_rellotge_intern_1_d5),
    .E5(a4_rellotge_intern_1_e5), .F5(a4_rellotge_intern_1_f5), .G5(a4_rellotge_intern_1_g5),
    .P5(a4_rellotge_intern_1_p5), .A4(a4_rellotge_intern_1_a4), .Hora_Act_Bin_16B(TR),
    .B4(a4_rellotge_intern_1_b4), .C4(a4_rellotge_intern_1_c4), .D4(a4_rellotge_intern_1_d4));  // open: RESET
  Button button_7 (.out(L));
  _7_Segment_Display #(.active("false")) u_7_segment_display_17 (
    .g(a3_temp_hores_minuts_3_g1h), .f(a3_temp_hores_minuts_3_f1h), .a(a3_temp_hores_minuts_3_a1h),
    .b(a3_temp_hores_minuts_3_b1h), .e(a3_temp_hores_minuts_3_e1h), .d(a3_temp_hores_minuts_3_d1h),
    .c(a3_temp_hores_minuts_3_c1h), .dp(a3_temp_hores_minuts_3_p1h));
  Button button_8 (.out(JIH1));
  _7_Segment_Display #(.active("false")) u_7_segment_display_18 (
    .g(a3_temp_hores_minuts_4_g1h), .f(a3_temp_hores_minuts_4_f1h), .a(a3_temp_hores_minuts_4_a1h),
    .b(a3_temp_hores_minuts_4_b1h), .e(a3_temp_hores_minuts_4_e1h), .d(a3_temp_hores_minuts_4_d1h),
    .c(a3_temp_hores_minuts_4_c1h), .dp(a3_temp_hores_minuts_4_p1h));
  Button button_9 (.out(HH1));
  _7_Segment_Display #(.active("false")) u_7_segment_display_19 (
    .g(a3_temp_hores_minuts_3_g2m), .f(a3_temp_hores_minuts_3_f2m), .a(a3_temp_hores_minuts_3_a2m),
    .b(a3_temp_hores_minuts_3_b2m), .e(a3_temp_hores_minuts_3_e2m), .d(a3_temp_hores_minuts_3_d2m),
    .c(a3_temp_hores_minuts_3_c2m), .dp(a3_temp_hores_minuts_3_p2m));
  _7_Segment_Display #(.active("false")) u_7_segment_display_20 (
    .g(a3_temp_hores_minuts_3_g1m), .f(a3_temp_hores_minuts_3_f1m), .a(a3_temp_hores_minuts_3_a1m),
    .b(a3_temp_hores_minuts_3_b1m), .e(a3_temp_hores_minuts_3_e1m), .d(a3_temp_hores_minuts_3_d1m),
    .c(a3_temp_hores_minuts_3_c1m), .dp(a3_temp_hores_minuts_3_p1m));
  Button button_10 (.out(JIM1));
  _7_Segment_Display #(.active("false")) u_7_segment_display_21 (
    .g(a3_temp_hores_minuts_4_g2m), .f(a3_temp_hores_minuts_4_f2m), .a(a3_temp_hores_minuts_4_a2m),
    .b(a3_temp_hores_minuts_4_b2m), .e(a3_temp_hores_minuts_4_e2m), .d(a3_temp_hores_minuts_4_d2m),
    .c(a3_temp_hores_minuts_4_c2m), .dp(a3_temp_hores_minuts_4_p2m));
  _7_Segment_Display #(.active("false")) u_7_segment_display_22 (
    .g(a3_temp_hores_minuts_4_g1m), .f(a3_temp_hores_minuts_4_f1m), .a(a3_temp_hores_minuts_4_a1m),
    .b(a3_temp_hores_minuts_4_b1m), .e(a3_temp_hores_minuts_4_e1m), .d(a3_temp_hores_minuts_4_d1m),
    .c(a3_temp_hores_minuts_4_c1m), .dp(a3_temp_hores_minuts_4_p1m));
  Button button_11 (.out(HM1));
  _7_Segment_Display #(.active("false")) u_7_segment_display_23 (
    .g(a3_temp_hores_minuts_5_g2h), .f(a3_temp_hores_minuts_5_f2h), .a(a3_temp_hores_minuts_5_a2h),
    .b(a3_temp_hores_minuts_5_b2h), .e(a3_temp_hores_minuts_5_e2h), .d(a3_temp_hores_minuts_5_d2g),
    .c(a3_temp_hores_minuts_5_c2h), .dp(a3_temp_hores_minuts_5_p2h));
  A3_Temp_Hores_Minuts a3_temp_hores_minuts_5 (
    .Entrada_H(EMHMA), .Entrada_M(EMMMA), .G2H(a3_temp_hores_minuts_5_g2h), .E2H(a3_temp_hores_minuts_5_e2h),
    .F2H(a3_temp_hores_minuts_5_f2h), .D2G(a3_temp_hores_minuts_5_d2g), .A2H(a3_temp_hores_minuts_5_a2h),
    .C2H(a3_temp_hores_minuts_5_c2h), .B2H(a3_temp_hores_minuts_5_b2h), .P2H(a3_temp_hores_minuts_5_p2h),
    .G1H(a3_temp_hores_minuts_5_g1h), .E1H(a3_temp_hores_minuts_5_e1h), .F1H(a3_temp_hores_minuts_5_f1h),
    .D1H(a3_temp_hores_minuts_5_d1h), .A1H(a3_temp_hores_minuts_5_a1h), .C1H(a3_temp_hores_minuts_5_c1h),
    .B1H(a3_temp_hores_minuts_5_b1h), .P1H(a3_temp_hores_minuts_5_p1h), .G2M(a3_temp_hores_minuts_5_g2m),
    .E2M(a3_temp_hores_minuts_5_e2m), .F2M(a3_temp_hores_minuts_5_f2m), .D2M(a3_temp_hores_minuts_5_d2m),
    .A2M(a3_temp_hores_minuts_5_a2m), .C2M(a3_temp_hores_minuts_5_c2m), .B2M(a3_temp_hores_minuts_5_b2m),
    .P2M(a3_temp_hores_minuts_5_p2m), .G1M(a3_temp_hores_minuts_5_g1m), .E1M(a3_temp_hores_minuts_5_e1m),
    .F1M(a3_temp_hores_minuts_5_f1m), .D1M(a3_temp_hores_minuts_5_d1m), .A1M(a3_temp_hores_minuts_5_a1m),
    .C1M(a3_temp_hores_minuts_5_c1m), .TB_MA(TC), .B1M(a3_temp_hores_minuts_5_b1m),
    .P1M(a3_temp_hores_minuts_5_p1m));
  Button button_12 (.out(EMHMA));
  _7_Segment_Display #(.active("false")) u_7_segment_display_24 (
    .g(a3_display_hm_1_g4), .f(a3_display_hm_1_f4), .a(a3_display_hm_1_a4), .b(a3_display_hm_1_b4),
    .e(a3_display_hm_1_e4), .d(a3_display_hm_1_d4), .c(a3_display_hm_1_c4), .dp(a3_display_hm_1_p1));
  _7_Segment_Display #(.active("false")) u_7_segment_display_25 (
    .g(a3_display_hm_1_g3), .f(a3_display_hm_1_f3), .a(a3_display_hm_1_a3), .b(a3_display_hm_1_b3),
    .e(a3_display_hm_1_e3), .d(a3_display_hm_1_d3), .c(a3_display_hm_1_c3), .dp(a3_display_hm_1_out_31));
  _7_Segment_Display #(.active("false")) u_7_segment_display_26 (
    .g(a3_display_hm_2_g4), .f(a3_display_hm_2_f4), .a(a3_display_hm_2_a4), .b(a3_display_hm_2_b4),
    .e(a3_display_hm_2_e4), .d(a3_display_hm_2_d4), .c(a3_display_hm_2_c4), .dp(a3_display_hm_2_p1));
  _7_Segment_Display #(.active("false")) u_7_segment_display_27 (
    .g(a3_display_hm_2_g3), .f(a3_display_hm_2_f3), .a(a3_display_hm_2_a3), .b(a3_display_hm_2_b3),
    .e(a3_display_hm_2_e3), .d(a3_display_hm_2_d3), .c(a3_display_hm_2_c3), .dp(a3_display_hm_2_out_31));
  _7_Segment_Display #(.active("false")) u_7_segment_display_28 (
    .g(a3_temp_hores_minuts_5_g1h), .f(a3_temp_hores_minuts_5_f1h), .a(a3_temp_hores_minuts_5_a1h),
    .b(a3_temp_hores_minuts_5_b1h), .e(a3_temp_hores_minuts_5_e1h), .d(a3_temp_hores_minuts_5_d1h),
    .c(a3_temp_hores_minuts_5_c1h), .dp(a3_temp_hores_minuts_5_p1h));
  Button button_13 (.out(EMMMA));
  _7_Segment_Display #(.active("false")) u_7_segment_display_29 (
    .g(a3_display_hm_1_g2), .f(a3_display_hm_1_f2), .a(a3_display_hm_1_a2), .b(a3_display_hm_1_b2),
    .e(a3_display_hm_1_e2), .d(a3_display_hm_1_d2), .c(a3_display_hm_1_c2), .dp(a3_display_hm_1_out_33));
  _7_Segment_Display #(.active("false")) u_7_segment_display_30 (
    .g(a3_display_hm_2_g2), .f(a3_display_hm_2_f2), .a(a3_display_hm_2_a2), .b(a3_display_hm_2_b2),
    .e(a3_display_hm_2_e2), .d(a3_display_hm_2_d2), .c(a3_display_hm_2_c2), .dp(a3_display_hm_2_out_33));
  _7_Segment_Display #(.active("false")) u_7_segment_display_31 (
    .g(a3_temp_hores_minuts_5_g2m), .f(a3_temp_hores_minuts_5_f2m), .a(a3_temp_hores_minuts_5_a2m),
    .b(a3_temp_hores_minuts_5_b2m), .e(a3_temp_hores_minuts_5_e2m), .d(a3_temp_hores_minuts_5_d2m),
    .c(a3_temp_hores_minuts_5_c2m), .dp(a3_temp_hores_minuts_5_p2m));
  _7_Segment_Display #(.active("false")) u_7_segment_display_32 (
    .g(a3_temp_hores_minuts_5_g1m), .f(a3_temp_hores_minuts_5_f1m), .a(a3_temp_hores_minuts_5_a1m),
    .b(a3_temp_hores_minuts_5_b1m), .e(a3_temp_hores_minuts_5_e1m), .d(a3_temp_hores_minuts_5_d1m),
    .c(a3_temp_hores_minuts_5_c1m), .dp(a3_temp_hores_minuts_5_p1m));
  _7_Segment_Display #(.active("false")) u_7_segment_display_33 (
    .g(a3_display_hm_1_g1), .f(a3_display_hm_1_f1), .a(a3_display_hm_1_a1), .b(a3_display_hm_1_b1),
    .e(a3_display_hm_1_e1), .d(a3_display_hm_1_d1), .c(a3_display_hm_1_c1), .dp(a3_display_hm_1_out_34));
  A3_Display_HM a3_display_hm_1 (
    .Power(LJI), .Countador(CRJI), .A2(a3_display_hm_1_a2), .B2(a3_display_hm_1_b2), .C2(a3_display_hm_1_c2),
    .D2(a3_display_hm_1_d2), .E2(a3_display_hm_1_e2), .F2(a3_display_hm_1_f2), .G2(a3_display_hm_1_g2),
    .out_33(a3_display_hm_1_out_33), .A1(a3_display_hm_1_a1), .B1(a3_display_hm_1_b1),
    .C1(a3_display_hm_1_c1), .D1(a3_display_hm_1_d1), .E1(a3_display_hm_1_e1), .F1(a3_display_hm_1_f1),
    .G1(a3_display_hm_1_g1), .out_34(a3_display_hm_1_out_34), .A4(a3_display_hm_1_a4),
    .B4(a3_display_hm_1_b4), .C4(a3_display_hm_1_c4), .D4(a3_display_hm_1_d4), .E4(a3_display_hm_1_e4),
    .F4(a3_display_hm_1_f4), .G4(a3_display_hm_1_g4), .out_31(a3_display_hm_1_out_31),
    .A3(a3_display_hm_1_a3), .B3(a3_display_hm_1_b3), .C3(a3_display_hm_1_c3), .D3(a3_display_hm_1_d3),
    .E3(a3_display_hm_1_e3), .F3(a3_display_hm_1_f3), .G3(a3_display_hm_1_g3), .P1(a3_display_hm_1_p1));
  _7_Segment_Display #(.active("false")) u_7_segment_display_34 (
    .g(a3_display_hm_2_g1), .f(a3_display_hm_2_f1), .a(a3_display_hm_2_a1), .b(a3_display_hm_2_b1),
    .e(a3_display_hm_2_e1), .d(a3_display_hm_2_d1), .c(a3_display_hm_2_c1), .dp(a3_display_hm_2_out_34));
  A3_Display_HM a3_display_hm_2 (
    .Power(LH), .Countador(CRH), .A2(a3_display_hm_2_a2), .B2(a3_display_hm_2_b2), .C2(a3_display_hm_2_c2),
    .D2(a3_display_hm_2_d2), .E2(a3_display_hm_2_e2), .F2(a3_display_hm_2_f2), .G2(a3_display_hm_2_g2),
    .out_33(a3_display_hm_2_out_33), .A1(a3_display_hm_2_a1), .B1(a3_display_hm_2_b1),
    .C1(a3_display_hm_2_c1), .D1(a3_display_hm_2_d1), .E1(a3_display_hm_2_e1), .F1(a3_display_hm_2_f1),
    .G1(a3_display_hm_2_g1), .out_34(a3_display_hm_2_out_34), .A4(a3_display_hm_2_a4),
    .B4(a3_display_hm_2_b4), .C4(a3_display_hm_2_c4), .D4(a3_display_hm_2_d4), .E4(a3_display_hm_2_e4),
    .F4(a3_display_hm_2_f4), .G4(a3_display_hm_2_g4), .out_31(a3_display_hm_2_out_31),
    .A3(a3_display_hm_2_a3), .B3(a3_display_hm_2_b3), .C3(a3_display_hm_2_c3), .D3(a3_display_hm_2_d3),
    .E3(a3_display_hm_2_e3), .F3(a3_display_hm_2_f3), .G3(a3_display_hm_2_g3), .P1(a3_display_hm_2_p1));
  LED led_1 (.in(S));
  Button button_14 (.out(K));
  A3_Temp_Hores_Minuts a3_temp_hores_minuts_6 (
    .Entrada_H(JEH2), .Entrada_M(JEM2), .G2H(a3_temp_hores_minuts_6_g2h), .E2H(a3_temp_hores_minuts_6_e2h),
    .F2H(a3_temp_hores_minuts_6_f2h), .D2G(a3_temp_hores_minuts_6_d2g), .A2H(a3_temp_hores_minuts_6_a2h),
    .C2H(a3_temp_hores_minuts_6_c2h), .B2H(a3_temp_hores_minuts_6_b2h), .P2H(a3_temp_hores_minuts_6_p2h),
    .G1H(a3_temp_hores_minuts_6_g1h), .E1H(a3_temp_hores_minuts_6_e1h), .F1H(a3_temp_hores_minuts_6_f1h),
    .D1H(a3_temp_hores_minuts_6_d1h), .A1H(a3_temp_hores_minuts_6_a1h), .C1H(a3_temp_hores_minuts_6_c1h),
    .B1H(a3_temp_hores_minuts_6_b1h), .P1H(a3_temp_hores_minuts_6_p1h), .G2M(a3_temp_hores_minuts_6_g2m),
    .E2M(a3_temp_hores_minuts_6_e2m), .F2M(a3_temp_hores_minuts_6_f2m), .D2M(a3_temp_hores_minuts_6_d2m),
    .A2M(a3_temp_hores_minuts_6_a2m), .C2M(a3_temp_hores_minuts_6_c2m), .B2M(a3_temp_hores_minuts_6_b2m),
    .P2M(a3_temp_hores_minuts_6_p2m), .G1M(a3_temp_hores_minuts_6_g1m), .E1M(a3_temp_hores_minuts_6_e1m),
    .F1M(a3_temp_hores_minuts_6_f1m), .D1M(a3_temp_hores_minuts_6_d1m), .A1M(a3_temp_hores_minuts_6_a1m),
    .C1M(a3_temp_hores_minuts_6_c1m), .TB_MA(HJE), .B1M(a3_temp_hores_minuts_6_b1m),
    .P1M(a3_temp_hores_minuts_6_p1m));
  A3_Temp_Hores_Minuts a3_temp_hores_minuts_7 (
    .Entrada_H(AH2), .Entrada_M(AM2), .G2H(a3_temp_hores_minuts_7_g2h), .E2H(a3_temp_hores_minuts_7_e2h),
    .F2H(a3_temp_hores_minuts_7_f2h), .D2G(a3_temp_hores_minuts_7_d2g), .A2H(a3_temp_hores_minuts_7_a2h),
    .C2H(a3_temp_hores_minuts_7_c2h), .B2H(a3_temp_hores_minuts_7_b2h), .P2H(a3_temp_hores_minuts_7_p2h),
    .G1H(a3_temp_hores_minuts_7_g1h), .E1H(a3_temp_hores_minuts_7_e1h), .F1H(a3_temp_hores_minuts_7_f1h),
    .D1H(a3_temp_hores_minuts_7_d1h), .A1H(a3_temp_hores_minuts_7_a1h), .C1H(a3_temp_hores_minuts_7_c1h),
    .B1H(a3_temp_hores_minuts_7_b1h), .P1H(a3_temp_hores_minuts_7_p1h), .G2M(a3_temp_hores_minuts_7_g2m),
    .E2M(a3_temp_hores_minuts_7_e2m), .F2M(a3_temp_hores_minuts_7_f2m), .D2M(a3_temp_hores_minuts_7_d2m),
    .A2M(a3_temp_hores_minuts_7_a2m), .C2M(a3_temp_hores_minuts_7_c2m), .B2M(a3_temp_hores_minuts_7_b2m),
    .P2M(a3_temp_hores_minuts_7_p2m), .G1M(a3_temp_hores_minuts_7_g1m), .E1M(a3_temp_hores_minuts_7_e1m),
    .F1M(a3_temp_hores_minuts_7_f1m), .D1M(a3_temp_hores_minuts_7_d1m), .A1M(a3_temp_hores_minuts_7_a1m),
    .C1M(a3_temp_hores_minuts_7_c1m), .TB_MA(HA), .B1M(a3_temp_hores_minuts_7_b1m),
    .P1M(a3_temp_hores_minuts_7_p1m));
  LED led_2 (.in(o));
  _7_Segment_Display #(.active("false")) u_7_segment_display_35 (
    .g(a3_temp_hores_minuts_6_g2h), .f(a3_temp_hores_minuts_6_f2h), .a(a3_temp_hores_minuts_6_a2h),
    .b(a3_temp_hores_minuts_6_b2h), .e(a3_temp_hores_minuts_6_e2h), .d(a3_temp_hores_minuts_6_d2g),
    .c(a3_temp_hores_minuts_6_c2h), .dp(a3_temp_hores_minuts_6_p2h));
  _7_Segment_Display #(.active("false")) u_7_segment_display_36 (
    .g(a3_temp_hores_minuts_6_g1h), .f(a3_temp_hores_minuts_6_f1h), .a(a3_temp_hores_minuts_6_a1h),
    .b(a3_temp_hores_minuts_6_b1h), .e(a3_temp_hores_minuts_6_e1h), .d(a3_temp_hores_minuts_6_d1h),
    .c(a3_temp_hores_minuts_6_c1h), .dp(a3_temp_hores_minuts_6_p1h));
  Button button_15 (.out(JEH2));
  _7_Segment_Display #(.active("false")) u_7_segment_display_37 (
    .g(a3_temp_hores_minuts_7_g2h), .f(a3_temp_hores_minuts_7_f2h), .a(a3_temp_hores_minuts_7_a2h),
    .b(a3_temp_hores_minuts_7_b2h), .e(a3_temp_hores_minuts_7_e2h), .d(a3_temp_hores_minuts_7_d2g),
    .c(a3_temp_hores_minuts_7_c2h), .dp(a3_temp_hores_minuts_7_p2h));
  _7_Segment_Display #(.active("false")) u_7_segment_display_38 (
    .g(a3_temp_hores_minuts_7_g1h), .f(a3_temp_hores_minuts_7_f1h), .a(a3_temp_hores_minuts_7_a1h),
    .b(a3_temp_hores_minuts_7_b1h), .e(a3_temp_hores_minuts_7_e1h), .d(a3_temp_hores_minuts_7_d1h),
    .c(a3_temp_hores_minuts_7_c1h), .dp(a3_temp_hores_minuts_7_p1h));
  Button button_16 (.out(AH2));
  LED led_3 (.in(VI));
  LED led_4 (.in(LJI));
  LED led_5 (.in(LJCI));
  _7_Segment_Display #(.active("false")) u_7_segment_display_39 (
    .g(a3_temp_hores_minuts_6_g2m), .f(a3_temp_hores_minuts_6_f2m), .a(a3_temp_hores_minuts_6_a2m),
    .b(a3_temp_hores_minuts_6_b2m), .e(a3_temp_hores_minuts_6_e2m), .d(a3_temp_hores_minuts_6_d2m),
    .c(a3_temp_hores_minuts_6_c2m), .dp(a3_temp_hores_minuts_6_p2m));
  _7_Segment_Display #(.active("false")) u_7_segment_display_40 (
    .g(a3_temp_hores_minuts_7_g2m), .f(a3_temp_hores_minuts_7_f2m), .a(a3_temp_hores_minuts_7_a2m),
    .b(a3_temp_hores_minuts_7_b2m), .e(a3_temp_hores_minuts_7_e2m), .d(a3_temp_hores_minuts_7_d2m),
    .c(a3_temp_hores_minuts_7_c2m), .dp(a3_temp_hores_minuts_7_p2m));
  LED led_6 (.in(M1));
  LED led_7 (.in(VE));
  LED led_8 (.in(LJE));
  LED led_9 (.in(LJCE));
  _7_Segment_Display #(.active("false")) u_7_segment_display_41 (
    .g(a3_temp_hores_minuts_6_g1m), .f(a3_temp_hores_minuts_6_f1m), .a(a3_temp_hores_minuts_6_a1m),
    .b(a3_temp_hores_minuts_6_b1m), .e(a3_temp_hores_minuts_6_e1m), .d(a3_temp_hores_minuts_6_d1m),
    .c(a3_temp_hores_minuts_6_c1m), .dp(a3_temp_hores_minuts_6_p1m));
  Button button_17 (.out(JEM2));
  _7_Segment_Display #(.active("false")) u_7_segment_display_42 (
    .g(a3_temp_hores_minuts_7_g1m), .f(a3_temp_hores_minuts_7_f1m), .a(a3_temp_hores_minuts_7_a1m),
    .b(a3_temp_hores_minuts_7_b1m), .e(a3_temp_hores_minuts_7_e1m), .d(a3_temp_hores_minuts_7_d1m),
    .c(a3_temp_hores_minuts_7_c1m), .dp(a3_temp_hores_minuts_7_p1m));
  Button button_18 (.out(AM2));
  _7_Segment_Display #(.active("false")) u_7_segment_display_43 (
    .g(a3_temp_hores_minuts_8_g2h), .f(a3_temp_hores_minuts_8_f2h), .a(a3_temp_hores_minuts_8_a2h),
    .b(a3_temp_hores_minuts_8_b2h), .e(a3_temp_hores_minuts_8_e2h), .d(a3_temp_hores_minuts_8_d2g),
    .c(a3_temp_hores_minuts_8_c2h), .dp(a3_temp_hores_minuts_8_p2h));
  A3_Temp_Hores_Minuts a3_temp_hores_minuts_8 (
    .Entrada_H(JEH1), .Entrada_M(JEM1), .G2H(a3_temp_hores_minuts_8_g2h), .E2H(a3_temp_hores_minuts_8_e2h),
    .F2H(a3_temp_hores_minuts_8_f2h), .D2G(a3_temp_hores_minuts_8_d2g), .A2H(a3_temp_hores_minuts_8_a2h),
    .C2H(a3_temp_hores_minuts_8_c2h), .B2H(a3_temp_hores_minuts_8_b2h), .P2H(a3_temp_hores_minuts_8_p2h),
    .G1H(a3_temp_hores_minuts_8_g1h), .E1H(a3_temp_hores_minuts_8_e1h), .F1H(a3_temp_hores_minuts_8_f1h),
    .D1H(a3_temp_hores_minuts_8_d1h), .A1H(a3_temp_hores_minuts_8_a1h), .C1H(a3_temp_hores_minuts_8_c1h),
    .B1H(a3_temp_hores_minuts_8_b1h), .P1H(a3_temp_hores_minuts_8_p1h), .G2M(a3_temp_hores_minuts_8_g2m),
    .E2M(a3_temp_hores_minuts_8_e2m), .F2M(a3_temp_hores_minuts_8_f2m), .D2M(a3_temp_hores_minuts_8_d2m),
    .A2M(a3_temp_hores_minuts_8_a2m), .C2M(a3_temp_hores_minuts_8_c2m), .B2M(a3_temp_hores_minuts_8_b2m),
    .P2M(a3_temp_hores_minuts_8_p2m), .G1M(a3_temp_hores_minuts_8_g1m), .E1M(a3_temp_hores_minuts_8_e1m),
    .F1M(a3_temp_hores_minuts_8_f1m), .D1M(a3_temp_hores_minuts_8_d1m), .A1M(a3_temp_hores_minuts_8_a1m),
    .C1M(a3_temp_hores_minuts_8_c1m), .TB_MA(TJE), .B1M(a3_temp_hores_minuts_8_b1m),
    .P1M(a3_temp_hores_minuts_8_p1m));
  _7_Segment_Display #(.active("false")) u_7_segment_display_44 (
    .g(a3_temp_hores_minuts_9_g2h), .f(a3_temp_hores_minuts_9_f2h), .a(a3_temp_hores_minuts_9_a2h),
    .b(a3_temp_hores_minuts_9_b2h), .e(a3_temp_hores_minuts_9_e2h), .d(a3_temp_hores_minuts_9_d2g),
    .c(a3_temp_hores_minuts_9_c2h), .dp(a3_temp_hores_minuts_9_p2h));
  A3_Temp_Hores_Minuts a3_temp_hores_minuts_9 (
    .Entrada_H(AH1), .Entrada_M(AM1), .G2H(a3_temp_hores_minuts_9_g2h), .E2H(a3_temp_hores_minuts_9_e2h),
    .F2H(a3_temp_hores_minuts_9_f2h), .D2G(a3_temp_hores_minuts_9_d2g), .A2H(a3_temp_hores_minuts_9_a2h),
    .C2H(a3_temp_hores_minuts_9_c2h), .B2H(a3_temp_hores_minuts_9_b2h), .P2H(a3_temp_hores_minuts_9_p2h),
    .G1H(a3_temp_hores_minuts_9_g1h), .E1H(a3_temp_hores_minuts_9_e1h), .F1H(a3_temp_hores_minuts_9_f1h),
    .D1H(a3_temp_hores_minuts_9_d1h), .A1H(a3_temp_hores_minuts_9_a1h), .C1H(a3_temp_hores_minuts_9_c1h),
    .B1H(a3_temp_hores_minuts_9_b1h), .P1H(a3_temp_hores_minuts_9_p1h), .G2M(a3_temp_hores_minuts_9_g2m),
    .E2M(a3_temp_hores_minuts_9_e2m), .F2M(a3_temp_hores_minuts_9_f2m), .D2M(a3_temp_hores_minuts_9_d2m),
    .A2M(a3_temp_hores_minuts_9_a2m), .C2M(a3_temp_hores_minuts_9_c2m), .B2M(a3_temp_hores_minuts_9_b2m),
    .P2M(a3_temp_hores_minuts_9_p2m), .G1M(a3_temp_hores_minuts_9_g1m), .E1M(a3_temp_hores_minuts_9_e1m),
    .F1M(a3_temp_hores_minuts_9_f1m), .D1M(a3_temp_hores_minuts_9_d1m), .A1M(a3_temp_hores_minuts_9_a1m),
    .C1M(a3_temp_hores_minuts_9_c1m), .TB_MA(TA), .B1M(a3_temp_hores_minuts_9_b1m),
    .P1M(a3_temp_hores_minuts_9_p1m));
  LED led_10 (.in(VH));
  LED led_11 (.in(LH));
  LED led_12 (.in(LJH));
  _7_Segment_Display #(.active("false")) u_7_segment_display_45 (
    .g(a3_temp_hores_minuts_8_g1h), .f(a3_temp_hores_minuts_8_f1h), .a(a3_temp_hores_minuts_8_a1h),
    .b(a3_temp_hores_minuts_8_b1h), .e(a3_temp_hores_minuts_8_e1h), .d(a3_temp_hores_minuts_8_d1h),
    .c(a3_temp_hores_minuts_8_c1h), .dp(a3_temp_hores_minuts_8_p1h));
  Button button_19 (.out(JEH1));
  _7_Segment_Display #(.active("false")) u_7_segment_display_46 (
    .g(a3_temp_hores_minuts_9_g1h), .f(a3_temp_hores_minuts_9_f1h), .a(a3_temp_hores_minuts_9_a1h),
    .b(a3_temp_hores_minuts_9_b1h), .e(a3_temp_hores_minuts_9_e1h), .d(a3_temp_hores_minuts_9_d1h),
    .c(a3_temp_hores_minuts_9_c1h), .dp(a3_temp_hores_minuts_9_p1h));
  Button button_20 (.out(AH1));
  LED led_13 (.in(M2));
  LED led_14 (.in(VA));
  LED led_15 (.in(LA));
  LED led_16 (.in(LJA));
  _7_Segment_Display #(.active("false")) u_7_segment_display_47 (
    .g(a3_temp_hores_minuts_8_g2m), .f(a3_temp_hores_minuts_8_f2m), .a(a3_temp_hores_minuts_8_a2m),
    .b(a3_temp_hores_minuts_8_b2m), .e(a3_temp_hores_minuts_8_e2m), .d(a3_temp_hores_minuts_8_d2m),
    .c(a3_temp_hores_minuts_8_c2m), .dp(a3_temp_hores_minuts_8_p2m));
  Button button_21 (.out(JEM1));
  _7_Segment_Display #(.active("false")) u_7_segment_display_48 (
    .g(a3_temp_hores_minuts_9_g2m), .f(a3_temp_hores_minuts_9_f2m), .a(a3_temp_hores_minuts_9_a2m),
    .b(a3_temp_hores_minuts_9_b2m), .e(a3_temp_hores_minuts_9_e2m), .d(a3_temp_hores_minuts_9_d2m),
    .c(a3_temp_hores_minuts_9_c2m), .dp(a3_temp_hores_minuts_9_p2m));
  Button button_22 (.out(AM1));
  _7_Segment_Display #(.active("false")) u_7_segment_display_49 (
    .g(a3_temp_hores_minuts_8_g1m), .f(a3_temp_hores_minuts_8_f1m), .a(a3_temp_hores_minuts_8_a1m),
    .b(a3_temp_hores_minuts_8_b1m), .e(a3_temp_hores_minuts_8_e1m), .d(a3_temp_hores_minuts_8_d1m),
    .c(a3_temp_hores_minuts_8_c1m), .dp(a3_temp_hores_minuts_8_p1m));
  _7_Segment_Display #(.active("false")) u_7_segment_display_50 (
    .g(a3_temp_hores_minuts_9_g1m), .f(a3_temp_hores_minuts_9_f1m), .a(a3_temp_hores_minuts_9_a1m),
    .b(a3_temp_hores_minuts_9_b1m), .e(a3_temp_hores_minuts_9_e1m), .d(a3_temp_hores_minuts_9_d1m),
    .c(a3_temp_hores_minuts_9_c1m), .dp(a3_temp_hores_minuts_9_p1m));
  _7_Segment_Display #(.active("false")) u_7_segment_display_51 (
    .g(a3_display_hm_3_g4), .f(a3_display_hm_3_f4), .a(a3_display_hm_3_a4), .b(a3_display_hm_3_b4),
    .e(a3_display_hm_3_e4), .d(a3_display_hm_3_d4), .c(a3_display_hm_3_c4), .dp(a3_display_hm_3_p1));
  _7_Segment_Display #(.active("false")) u_7_segment_display_52 (
    .g(a3_display_hm_4_g4), .f(a3_display_hm_4_f4), .a(a3_display_hm_4_a4), .b(a3_display_hm_4_b4),
    .e(a3_display_hm_4_e4), .d(a3_display_hm_4_d4), .c(a3_display_hm_4_c4), .dp(a3_display_hm_4_p1));
  Button button_23 (.out(SAE1));
  Button button_24 (.out(SAE2));
  _7_Segment_Display #(.active("false")) u_7_segment_display_53 (
    .g(a3_display_hm_3_g3), .f(a3_display_hm_3_f3), .a(a3_display_hm_3_a3), .b(a3_display_hm_3_b3),
    .e(a3_display_hm_3_e3), .d(a3_display_hm_3_d3), .c(a3_display_hm_3_c3), .dp(a3_display_hm_3_out_31));
  _7_Segment_Display #(.active("false")) u_7_segment_display_54 (
    .g(a3_display_hm_3_g2), .f(a3_display_hm_3_f2), .a(a3_display_hm_3_a2), .b(a3_display_hm_3_b2),
    .e(a3_display_hm_3_e2), .d(a3_display_hm_3_d2), .c(a3_display_hm_3_c2), .dp(a3_display_hm_3_out_33));
  _7_Segment_Display #(.active("false")) u_7_segment_display_55 (
    .g(a3_display_hm_4_g3), .f(a3_display_hm_4_f3), .a(a3_display_hm_4_a3), .b(a3_display_hm_4_b3),
    .e(a3_display_hm_4_e3), .d(a3_display_hm_4_d3), .c(a3_display_hm_4_c3), .dp(a3_display_hm_4_out_31));
  _7_Segment_Display #(.active("false")) u_7_segment_display_56 (
    .g(a3_display_hm_4_g2), .f(a3_display_hm_4_f2), .a(a3_display_hm_4_a2), .b(a3_display_hm_4_b2),
    .e(a3_display_hm_4_e2), .d(a3_display_hm_4_d2), .c(a3_display_hm_4_c2), .dp(a3_display_hm_4_out_33));
  LED led_17 (.in(LAV1));
  LED led_18 (.in(LAV2));
  _7_Segment_Display #(.active("false")) u_7_segment_display_57 (
    .g(a3_display_hm_3_g1), .f(a3_display_hm_3_f1), .a(a3_display_hm_3_a1), .b(a3_display_hm_3_b1),
    .e(a3_display_hm_3_e1), .d(a3_display_hm_3_d1), .c(a3_display_hm_3_c1), .dp(a3_display_hm_3_out_34));
  A3_Display_HM a3_display_hm_3 (
    .Power(LJE), .Countador(CRJE), .A2(a3_display_hm_3_a2), .B2(a3_display_hm_3_b2), .C2(a3_display_hm_3_c2),
    .D2(a3_display_hm_3_d2), .E2(a3_display_hm_3_e2), .F2(a3_display_hm_3_f2), .G2(a3_display_hm_3_g2),
    .out_33(a3_display_hm_3_out_33), .A1(a3_display_hm_3_a1), .B1(a3_display_hm_3_b1),
    .C1(a3_display_hm_3_c1), .D1(a3_display_hm_3_d1), .E1(a3_display_hm_3_e1), .F1(a3_display_hm_3_f1),
    .G1(a3_display_hm_3_g1), .out_34(a3_display_hm_3_out_34), .A4(a3_display_hm_3_a4),
    .B4(a3_display_hm_3_b4), .C4(a3_display_hm_3_c4), .D4(a3_display_hm_3_d4), .E4(a3_display_hm_3_e4),
    .F4(a3_display_hm_3_f4), .G4(a3_display_hm_3_g4), .out_31(a3_display_hm_3_out_31),
    .A3(a3_display_hm_3_a3), .B3(a3_display_hm_3_b3), .C3(a3_display_hm_3_c3), .D3(a3_display_hm_3_d3),
    .E3(a3_display_hm_3_e3), .F3(a3_display_hm_3_f3), .G3(a3_display_hm_3_g3), .P1(a3_display_hm_3_p1));
  _7_Segment_Display #(.active("false")) u_7_segment_display_58 (
    .g(a3_display_hm_4_g1), .f(a3_display_hm_4_f1), .a(a3_display_hm_4_a1), .b(a3_display_hm_4_b1),
    .e(a3_display_hm_4_e1), .d(a3_display_hm_4_d1), .c(a3_display_hm_4_c1), .dp(a3_display_hm_4_out_34));
  A3_Display_HM a3_display_hm_4 (
    .Power(LA), .Countador(CRA), .A2(a3_display_hm_4_a2), .B2(a3_display_hm_4_b2), .C2(a3_display_hm_4_c2),
    .D2(a3_display_hm_4_d2), .E2(a3_display_hm_4_e2), .F2(a3_display_hm_4_f2), .G2(a3_display_hm_4_g2),
    .out_33(a3_display_hm_4_out_33), .A1(a3_display_hm_4_a1), .B1(a3_display_hm_4_b1),
    .C1(a3_display_hm_4_c1), .D1(a3_display_hm_4_d1), .E1(a3_display_hm_4_e1), .F1(a3_display_hm_4_f1),
    .G1(a3_display_hm_4_g1), .out_34(a3_display_hm_4_out_34), .A4(a3_display_hm_4_a4),
    .B4(a3_display_hm_4_b4), .C4(a3_display_hm_4_c4), .D4(a3_display_hm_4_d4), .E4(a3_display_hm_4_e4),
    .F4(a3_display_hm_4_f4), .G4(a3_display_hm_4_g4), .out_31(a3_display_hm_4_out_31),
    .A3(a3_display_hm_4_a3), .B3(a3_display_hm_4_b3), .C3(a3_display_hm_4_c3), .D3(a3_display_hm_4_d3),
    .E3(a3_display_hm_4_e3), .F3(a3_display_hm_4_f3), .G3(a3_display_hm_4_g3), .P1(a3_display_hm_4_p1));
  _7_Segment_Display #(.active("false")) u_7_segment_display_59 (
    .g(b0_ctrl_temperatura_1_g3), .f(b0_ctrl_temperatura_1_f3), .a(b0_ctrl_temperatura_1_a3),
    .b(b0_ctrl_temperatura_1_b3), .e(b0_ctrl_temperatura_1_e3), .d(b0_ctrl_temperatura_1_d3),
    .c(b0_ctrl_temperatura_1_c3), .dp(b0_ctrl_temperatura_1_p3));
  _7_Segment_Display #(.active("false")) u_7_segment_display_60 (
    .g(b0_ctrl_temperatura_1_g2), .f(b0_ctrl_temperatura_1_f2), .a(b0_ctrl_temperatura_1_a2),
    .b(b0_ctrl_temperatura_1_b2), .e(b0_ctrl_temperatura_1_e2), .d(b0_ctrl_temperatura_1_d2),
    .c(b0_ctrl_temperatura_1_c2), .dp(b0_ctrl_temperatura_1_p2));
  Button button_25 (.out(METS));
  _7_Segment_Display #(.active("false")) u_7_segment_display_61 (
    .g(b2_ctrl_humetatrelativa_1_g3), .f(b2_ctrl_humetatrelativa_1_f3), .a(b2_ctrl_humetatrelativa_1_a3),
    .b(b2_ctrl_humetatrelativa_1_b3), .e(b2_ctrl_humetatrelativa_1_e3), .d(b2_ctrl_humetatrelativa_1_d3),
    .c(b2_ctrl_humetatrelativa_1_c3), .dp(b2_ctrl_humetatrelativa_1_p3));
  _7_Segment_Display #(.active("false")) u_7_segment_display_62 (
    .g(b2_ctrl_humetatrelativa_1_g2), .f(b2_ctrl_humetatrelativa_1_f2), .a(b2_ctrl_humetatrelativa_1_a2),
    .b(b2_ctrl_humetatrelativa_1_b2), .e(b2_ctrl_humetatrelativa_1_e2), .d(b2_ctrl_humetatrelativa_1_d2),
    .c(b2_ctrl_humetatrelativa_1_c2), .dp(b2_ctrl_humetatrelativa_1_p1));
  Button button_26 (.out(MEHS));
  _7_Segment_Display #(.active("false")) u_7_segment_display_63 (
    .g(b0_ctrl_temperatura_1_g1), .f(b0_ctrl_temperatura_1_f1), .a(b0_ctrl_temperatura_1_a1),
    .b(b0_ctrl_temperatura_1_b1), .e(b0_ctrl_temperatura_1_e1), .d(b0_ctrl_temperatura_1_d1),
    .c(b0_ctrl_temperatura_1_c1), .dp(b0_ctrl_temperatura_1_p1));
  B0_CTRL_Temperatura b0_ctrl_temperatura_1 (
    .Mes(METS), .Menys(MYTS), .Mode(1'b0), .A3(b0_ctrl_temperatura_1_a3), .B3(b0_ctrl_temperatura_1_b3),
    .C3(b0_ctrl_temperatura_1_c3), .D3(b0_ctrl_temperatura_1_d3), .E3(b0_ctrl_temperatura_1_e3),
    .F3(b0_ctrl_temperatura_1_f3), .G3(b0_ctrl_temperatura_1_g3), .P3(b0_ctrl_temperatura_1_p3),
    .A2(b0_ctrl_temperatura_1_a2), .B2(b0_ctrl_temperatura_1_b2), .C2(b0_ctrl_temperatura_1_c2),
    .D2(b0_ctrl_temperatura_1_d2), .E2(b0_ctrl_temperatura_1_e2), .F2(b0_ctrl_temperatura_1_f2),
    .G2(b0_ctrl_temperatura_1_g2), .P2(b0_ctrl_temperatura_1_p2), .A1(b0_ctrl_temperatura_1_a1),
    .B1(b0_ctrl_temperatura_1_b1), .C1(b0_ctrl_temperatura_1_c1), .D1(b0_ctrl_temperatura_1_d1),
    .E1(b0_ctrl_temperatura_1_e1), .F1(b0_ctrl_temperatura_1_f1), .G1(b0_ctrl_temperatura_1_g1),
    .P1(b0_ctrl_temperatura_1_p1), .Sort_Temp(TIS));  // open: ON_OFF_SIS, Display_Bits
  Button button_27 (.out(MYTS));
  _7_Segment_Display #(.active("false")) u_7_segment_display_64 (
    .g(b2_ctrl_humetatrelativa_1_g1), .f(b2_ctrl_humetatrelativa_1_f1), .a(b2_ctrl_humetatrelativa_1_a1),
    .b(b2_ctrl_humetatrelativa_1_b1), .e(b2_ctrl_humetatrelativa_1_e1), .d(b2_ctrl_humetatrelativa_1_d1),
    .c(b2_ctrl_humetatrelativa_1_c1), .dp(b2_ctrl_humetatrelativa_1_p2));
  B2_CTRL_HumetatRelativa b2_ctrl_humetatrelativa_1 (
    .Mes(MEHS), .Menys(MYHS), .Mode(1'b0), .A3(b2_ctrl_humetatrelativa_1_a3),
    .B3(b2_ctrl_humetatrelativa_1_b3), .C3(b2_ctrl_humetatrelativa_1_c3), .D3(b2_ctrl_humetatrelativa_1_d3),
    .E3(b2_ctrl_humetatrelativa_1_e3), .F3(b2_ctrl_humetatrelativa_1_f3), .G3(b2_ctrl_humetatrelativa_1_g3),
    .P3(b2_ctrl_humetatrelativa_1_p3), .A2(b2_ctrl_humetatrelativa_1_a2), .B2(b2_ctrl_humetatrelativa_1_b2),
    .C2(b2_ctrl_humetatrelativa_1_c2), .D2(b2_ctrl_humetatrelativa_1_d2), .E2(b2_ctrl_humetatrelativa_1_e2),
    .F2(b2_ctrl_humetatrelativa_1_f2), .G2(b2_ctrl_humetatrelativa_1_g2), .P2(b2_ctrl_humetatrelativa_1_p2),
    .A1(b2_ctrl_humetatrelativa_1_a1), .B1(b2_ctrl_humetatrelativa_1_b1), .C1(b2_ctrl_humetatrelativa_1_c1),
    .D1(b2_ctrl_humetatrelativa_1_d1), .E1(b2_ctrl_humetatrelativa_1_e1), .F1(b2_ctrl_humetatrelativa_1_f1),
    .G1(b2_ctrl_humetatrelativa_1_g1), .P1(b2_ctrl_humetatrelativa_1_p1), .Sort_Temp(HIS));  // open: ON_OFF_SIS, Display_Bits
  Button button_28 (.out(MYHS));
  LED led_19 (.in(POL));
  LED led_20 (.in(JAR));
  LED led_21 (.in(MEQ));
  LED led_22 (.in(PROP));
  _7_Segment_Display #(.active("false")) u_7_segment_display_65 (
    .g(b0_ctrl_temperatura_2_g3), .f(b0_ctrl_temperatura_2_f3), .a(b0_ctrl_temperatura_2_a3),
    .b(b0_ctrl_temperatura_2_b3), .e(b0_ctrl_temperatura_2_e3), .d(b0_ctrl_temperatura_2_d3),
    .c(b0_ctrl_temperatura_2_c3), .dp(b0_ctrl_temperatura_2_p3));
  _7_Segment_Display #(.active("false")) u_7_segment_display_66 (
    .g(b0_ctrl_temperatura_2_g2), .f(b0_ctrl_temperatura_2_f2), .a(b0_ctrl_temperatura_2_a2),
    .b(b0_ctrl_temperatura_2_b2), .e(b0_ctrl_temperatura_2_e2), .d(b0_ctrl_temperatura_2_d2),
    .c(b0_ctrl_temperatura_2_c2), .dp(b0_ctrl_temperatura_2_p2));
  Button button_29 (.out(MET));
  _7_Segment_Display #(.active("false")) u_7_segment_display_67 (
    .g(b2_ctrl_humetatrelativa_2_g3), .f(b2_ctrl_humetatrelativa_2_f3), .a(b2_ctrl_humetatrelativa_2_a3),
    .b(b2_ctrl_humetatrelativa_2_b3), .e(b2_ctrl_humetatrelativa_2_e3), .d(b2_ctrl_humetatrelativa_2_d3),
    .c(b2_ctrl_humetatrelativa_2_c3), .dp(b2_ctrl_humetatrelativa_2_p3));
  _7_Segment_Display #(.active("false")) u_7_segment_display_68 (
    .g(b2_ctrl_humetatrelativa_2_g2), .f(b2_ctrl_humetatrelativa_2_f2), .a(b2_ctrl_humetatrelativa_2_a2),
    .b(b2_ctrl_humetatrelativa_2_b2), .e(b2_ctrl_humetatrelativa_2_e2), .d(b2_ctrl_humetatrelativa_2_d2),
    .c(b2_ctrl_humetatrelativa_2_c2), .dp(b2_ctrl_humetatrelativa_2_p1));
  Button button_30 (.out(MEH));
  _7_Segment_Display #(.active("false")) u_7_segment_display_69 (
    .g(b0_ctrl_temperatura_2_g1), .f(b0_ctrl_temperatura_2_f1), .a(b0_ctrl_temperatura_2_a1),
    .b(b0_ctrl_temperatura_2_b1), .e(b0_ctrl_temperatura_2_e1), .d(b0_ctrl_temperatura_2_d1),
    .c(b0_ctrl_temperatura_2_c1), .dp(b0_ctrl_temperatura_2_p1));
  Button button_31 (.out(MYT));
  _7_Segment_Display #(.active("false")) u_7_segment_display_70 (
    .g(b2_ctrl_humetatrelativa_2_g1), .f(b2_ctrl_humetatrelativa_2_f1), .a(b2_ctrl_humetatrelativa_2_a1),
    .b(b2_ctrl_humetatrelativa_2_b1), .e(b2_ctrl_humetatrelativa_2_e1), .d(b2_ctrl_humetatrelativa_2_d1),
    .c(b2_ctrl_humetatrelativa_2_c1), .dp(b2_ctrl_humetatrelativa_2_p2));
  Button button_32 (.out(MYH));
  B0_CTRL_Temperatura b0_ctrl_temperatura_2 (
    .Mes(MET), .Menys(MYT), .Mode(1'b0), .A3(b0_ctrl_temperatura_2_a3), .B3(b0_ctrl_temperatura_2_b3),
    .C3(b0_ctrl_temperatura_2_c3), .D3(b0_ctrl_temperatura_2_d3), .E3(b0_ctrl_temperatura_2_e3),
    .F3(b0_ctrl_temperatura_2_f3), .G3(b0_ctrl_temperatura_2_g3), .P3(b0_ctrl_temperatura_2_p3),
    .A2(b0_ctrl_temperatura_2_a2), .B2(b0_ctrl_temperatura_2_b2), .C2(b0_ctrl_temperatura_2_c2),
    .D2(b0_ctrl_temperatura_2_d2), .E2(b0_ctrl_temperatura_2_e2), .F2(b0_ctrl_temperatura_2_f2),
    .G2(b0_ctrl_temperatura_2_g2), .P2(b0_ctrl_temperatura_2_p2), .A1(b0_ctrl_temperatura_2_a1),
    .B1(b0_ctrl_temperatura_2_b1), .C1(b0_ctrl_temperatura_2_c1), .D1(b0_ctrl_temperatura_2_d1),
    .E1(b0_ctrl_temperatura_2_e1), .F1(b0_ctrl_temperatura_2_f1), .G1(b0_ctrl_temperatura_2_g1),
    .P1(b0_ctrl_temperatura_2_p1), .Sort_Temp(TPR));  // open: ON_OFF_SIS, Display_Bits
  B2_CTRL_HumetatRelativa b2_ctrl_humetatrelativa_2 (
    .Mes(MEH), .Menys(MYH), .Mode(1'b0), .A3(b2_ctrl_humetatrelativa_2_a3),
    .B3(b2_ctrl_humetatrelativa_2_b3), .C3(b2_ctrl_humetatrelativa_2_c3), .D3(b2_ctrl_humetatrelativa_2_d3),
    .E3(b2_ctrl_humetatrelativa_2_e3), .F3(b2_ctrl_humetatrelativa_2_f3), .G3(b2_ctrl_humetatrelativa_2_g3),
    .P3(b2_ctrl_humetatrelativa_2_p3), .A2(b2_ctrl_humetatrelativa_2_a2), .B2(b2_ctrl_humetatrelativa_2_b2),
    .C2(b2_ctrl_humetatrelativa_2_c2), .D2(b2_ctrl_humetatrelativa_2_d2), .E2(b2_ctrl_humetatrelativa_2_e2),
    .F2(b2_ctrl_humetatrelativa_2_f2), .G2(b2_ctrl_humetatrelativa_2_g2), .P2(b2_ctrl_humetatrelativa_2_p2),
    .A1(b2_ctrl_humetatrelativa_2_a1), .B1(b2_ctrl_humetatrelativa_2_b1), .C1(b2_ctrl_humetatrelativa_2_c1),
    .D1(b2_ctrl_humetatrelativa_2_d1), .E1(b2_ctrl_humetatrelativa_2_e1), .F1(b2_ctrl_humetatrelativa_2_f1),
    .G1(b2_ctrl_humetatrelativa_2_g1), .P1(b2_ctrl_humetatrelativa_2_p1), .Sort_Temp(HPR));  // open: ON_OFF_SIS, Display_Bits
  LED led_23 (.in(LOOFT));
  LED led_24 (.in(L3S));
  _7_Segment_Display #(.active("false")) u_7_segment_display_71 (
    .g(b0_ctrl_temperatura_3_g3), .f(b0_ctrl_temperatura_3_f3), .a(b0_ctrl_temperatura_3_a3),
    .b(b0_ctrl_temperatura_3_b3), .e(b0_ctrl_temperatura_3_e3), .d(b0_ctrl_temperatura_3_d3),
    .c(b0_ctrl_temperatura_3_c3), .dp(b0_ctrl_temperatura_3_p3));
  _7_Segment_Display #(.active("false")) u_7_segment_display_72 (
    .g(b2_ctrl_humetatrelativa_3_g3), .f(b2_ctrl_humetatrelativa_3_f3), .a(b2_ctrl_humetatrelativa_3_a3),
    .b(b2_ctrl_humetatrelativa_3_b3), .e(b2_ctrl_humetatrelativa_3_e3), .d(b2_ctrl_humetatrelativa_3_d3),
    .c(b2_ctrl_humetatrelativa_3_c3), .dp(b2_ctrl_humetatrelativa_3_p3));
  LED led_25 (.in(in_1));
  LED led_26 (.in(in_2));
  LED led_27 (.in(in_3));
  LED led_28 (.in(in_4));
  LED led_29 (.in(in_5));
  _7_Segment_Display #(.active("false")) u_7_segment_display_73 (
    .g(b0_ctrl_temperatura_3_g2), .f(b0_ctrl_temperatura_3_f2), .a(b0_ctrl_temperatura_3_a2),
    .b(b0_ctrl_temperatura_3_b2), .e(b0_ctrl_temperatura_3_e2), .d(b0_ctrl_temperatura_3_d2),
    .c(b0_ctrl_temperatura_3_c2), .dp(b0_ctrl_temperatura_3_p2));
  _7_Segment_Display #(.active("false")) u_7_segment_display_74 (
    .g(b0_ctrl_temperatura_3_g1), .f(b0_ctrl_temperatura_3_f1), .a(b0_ctrl_temperatura_3_a1),
    .b(b0_ctrl_temperatura_3_b1), .e(b0_ctrl_temperatura_3_e1), .d(b0_ctrl_temperatura_3_d1),
    .c(b0_ctrl_temperatura_3_c1), .dp(b0_ctrl_temperatura_3_p1));
  _7_Segment_Display #(.active("false")) u_7_segment_display_75 (
    .g(b2_ctrl_humetatrelativa_3_g2), .f(b2_ctrl_humetatrelativa_3_f2), .a(b2_ctrl_humetatrelativa_3_a2),
    .b(b2_ctrl_humetatrelativa_3_b2), .e(b2_ctrl_humetatrelativa_3_e2), .d(b2_ctrl_humetatrelativa_3_d2),
    .c(b2_ctrl_humetatrelativa_3_c2), .dp(b2_ctrl_humetatrelativa_3_p1));
  _7_Segment_Display #(.active("false")) u_7_segment_display_76 (
    .g(b2_ctrl_humetatrelativa_3_g1), .f(b2_ctrl_humetatrelativa_3_f1), .a(b2_ctrl_humetatrelativa_3_a1),
    .b(b2_ctrl_humetatrelativa_3_b1), .e(b2_ctrl_humetatrelativa_3_e1), .d(b2_ctrl_humetatrelativa_3_d1),
    .c(b2_ctrl_humetatrelativa_3_c1), .dp(b2_ctrl_humetatrelativa_3_p2));
  Button button_33 (.out(OOFT));
  B0_CTRL_Temperatura b0_ctrl_temperatura_3 (
    .ON_OFF_SIS(LOOFT), .Mes(METR), .Menys(MYTR), .Mode(1'b1), .Display_Bits(TIS),
    .A3(b0_ctrl_temperatura_3_a3), .B3(b0_ctrl_temperatura_3_b3), .C3(b0_ctrl_temperatura_3_c3),
    .D3(b0_ctrl_temperatura_3_d3), .E3(b0_ctrl_temperatura_3_e3), .F3(b0_ctrl_temperatura_3_f3),
    .G3(b0_ctrl_temperatura_3_g3), .P3(b0_ctrl_temperatura_3_p3), .A2(b0_ctrl_temperatura_3_a2),
    .B2(b0_ctrl_temperatura_3_b2), .C2(b0_ctrl_temperatura_3_c2), .D2(b0_ctrl_temperatura_3_d2),
    .E2(b0_ctrl_temperatura_3_e2), .F2(b0_ctrl_temperatura_3_f2), .G2(b0_ctrl_temperatura_3_g2),
    .P2(b0_ctrl_temperatura_3_p2), .A1(b0_ctrl_temperatura_3_a1), .B1(b0_ctrl_temperatura_3_b1),
    .C1(b0_ctrl_temperatura_3_c1), .D1(b0_ctrl_temperatura_3_d1), .E1(b0_ctrl_temperatura_3_e1),
    .F1(b0_ctrl_temperatura_3_f1), .G1(b0_ctrl_temperatura_3_g1), .P1(b0_ctrl_temperatura_3_p1),
    .Sort_Temp(TRE));
  B2_CTRL_HumetatRelativa b2_ctrl_humetatrelativa_3 (
    .ON_OFF_SIS(LOOFT), .Mes(MEHR), .Menys(MYHR), .Mode(1'b1), .Display_Bits(HIS),
    .A3(b2_ctrl_humetatrelativa_3_a3), .B3(b2_ctrl_humetatrelativa_3_b3), .C3(b2_ctrl_humetatrelativa_3_c3),
    .D3(b2_ctrl_humetatrelativa_3_d3), .E3(b2_ctrl_humetatrelativa_3_e3), .F3(b2_ctrl_humetatrelativa_3_f3),
    .G3(b2_ctrl_humetatrelativa_3_g3), .P3(b2_ctrl_humetatrelativa_3_p3), .A2(b2_ctrl_humetatrelativa_3_a2),
    .B2(b2_ctrl_humetatrelativa_3_b2), .C2(b2_ctrl_humetatrelativa_3_c2), .D2(b2_ctrl_humetatrelativa_3_d2),
    .E2(b2_ctrl_humetatrelativa_3_e2), .F2(b2_ctrl_humetatrelativa_3_f2), .G2(b2_ctrl_humetatrelativa_3_g2),
    .P2(b2_ctrl_humetatrelativa_3_p2), .A1(b2_ctrl_humetatrelativa_3_a1), .B1(b2_ctrl_humetatrelativa_3_b1),
    .C1(b2_ctrl_humetatrelativa_3_c1), .D1(b2_ctrl_humetatrelativa_3_d1), .E1(b2_ctrl_humetatrelativa_3_e1),
    .F1(b2_ctrl_humetatrelativa_3_f1), .G1(b2_ctrl_humetatrelativa_3_g1), .P1(b2_ctrl_humetatrelativa_3_p1),
    .Sort_Temp(HRE));
  LED led_30 (.in(AFR));
  LED led_31 (.in(ARC));
  LED led_32 (.in(DESHU));
  LED led_33 (.in(HUMI));
  A5_Control_Botons_Leds a5_control_botons_leds_1 (
    .Boto_Prog(L), .Avaria_Motor1(SAE1), .Boto_Auto(K), .Avaria_Motor2(SAE2), .LJI(VI), .LJE(VE), .LH(VH),
    .LA(VA), .LEDAVM1(LAV1), .LEDAVM2(LAV2), .L1_Prog(o), .L0_Auto(S), .Activador_SR_A(ActA),
    .Activador_SR_P(ActP), .LCJI(LJCI), .LCJE(LJCE), .LCH(LJH), .LJA(LJA));
  LED led_34 (.in(in_6));
  LED led_35 (.in(in_7));
  LED led_36 (.in(in_8));
  LED led_37 (.in(in_9));
  A6_Logica_Control a6_logica_control_1 (
    .Boto_Prog(L), .Avaria_Motor1(SAE1), .Boto_Auto(K), .Avaria_Motor2(SAE2), .Temps_JI(TJI),
    .Hora_Actual(TR), .Hora_JI(HJI), .Temps_JE(TJE), .Hora_JE(HJE), .Hora_Hort(HH), .Temps_H(TH),
    .Hora_Arbres(HA), .Temps_Comu(TC), .Temps_A(TA), .TJICR(TJICR), .CRJI(CRJI), .TJECR(TJECR), .CRJE(CRJE),
    .THCR(THCR), .CRH(CRH), .TACR(TACR), .CRA(CRA), .LED_JI(LJI), .LED_JE(LJE), .LED_H(LH), .LED_A(LA),
    .Motor1(M1), .Motor2(M2), .V1(VI), .V2(VE), .V3(VH), .V4(VA));
  B4_Logica_Control b4_logica_control_1 (
    .ON_OFF_ENT(OOFT), .Avaria_MQ_Temp(in_6), .Avaria_SEN_Temp(in_7), .Temperatura_Prog(TPR),
    .Temperatura_Real(TRE), .Avaria_MQ_Hum(in_8), .Avaria_SENS_Hum(in_9), .Humetat_Programada(HPR),
    .Humetat_Real(HRE), .ON_OFF_SORT(LOOFT), .LED_3S(L3S), .Mes_Temp(METR), .Aire_Calent(ARC),
    .Aire_Fred(AFR), .Menys_Temp(MYTR), .Mes_Hum(MEHR), .Humidificador(HUMI), .Deshumi(DESHU),
    .Menys_Hum(MYHR));
  C0_SIS_ALERTAS c0_sis_alertas_1 (
    .Al0(in_2), .Al1(in_3), .Al2(in_4), .AL4(in_5), .AL5(in_1), .M1(LAV1), .M2(LAV2), .ST(in_7), .SH(in_9),
    .MQT(in_6), .MQH(in_8), .Police(POL), .Jardiner(JAR), .Mecanic(MEQ), .Propietari(PROP));

  // Other names for the same wires on the sheet: ASCH_M = in_8; ASCH_S = in_9; ASCT_M = in_6; ASCT_S = in_7;
  //   SM0 = in_1; SM1 = in_2; SM2 = in_3; SM3 = in_4; SM4 = in_5

  // Notes on the sheet:
  //   AFEGIR HORES
  //   HORES
  //   AFEGIR HORES
  //   HORA INCI
  //   HORES
  //   AFEGIR HORES
  //   HORES
  //   HORA D'INCI
  //   MINUTS
  //   AFEGIR MINUTS
  //   MINUTS
  //   AFEGIR MINUTS
  //   HORA ACTUAL
  //   MINUTS
  //   AFEGIR MINUTS
  //   JARDÍ INTERIOR
  //   SEGONS
  //   ON/OFF_PROGRAMA
  //   TEMPS
  //   HORES
  //   AFEGIR HORES
  //   HORT
  //   TEMPS
  //   HORES
  //   AFEGIR HORES
  //   MINUTS
  //   AFEGIR MINUTS
  //   MINUTS
  //   AFEGIR MINUTS
  //   HORES
  //   AFEGIR HORES
  //   HORES
  //   HORES
  //   MODE AUTOMÀTIC
  //   DURACIÓ
  //   AFEGIR MINUTS
  //   CRONO
  //   CRONO
  //   MINUTS
  //   MINUTS
  //   MINUTS
  //   ON/OFF
  //   MODE PROGRAMAT
  //   HORES
  //   AFEGIR HORES
  //   HORES
  //   AFEGIR HORES
  //   MOTOR 1
  //   Jardí Interior
  //   V1
  //   Jardí Interior
  //   HORA INCI
  //   HORA INCI
  //   Jardí Exterior
  //   V2
  //   Jardí Exterior
  //   MINUTS
  //   AFEGIR MINUTS
  //   MINUTS
  //   AFEGIR MINUTS
  //   NOTIFICACIONS
  //   Hort
  //   V3
  //   REG EN CURS / ACA
  //   Hort
  //   MOTOR 2
  //   JARDÍ EXTERIOR
  //   HORES
  //   AFEGIR HORES
  //   HORES
  //   AFEGIR HORES
  //   Arbres
  //   V4
  //   Arbres
  //   TEMPS
  //   MINUTS
  //   AFEGIR MINUTS
  //   ZONA ARBRES FRUITERS
  //   TEMPS
  //   MINUTS
  //   AFEGIR MINUTS
  //   AVARIA MOTOR 1
  //   Avaria injector M1
  //   Avaria injector M2
  //   HORES
  //   HORES
  //   SIM AVARIA
  //   AVARIA MOTOR 2
  //   CRONO
  //   DURACIÓ
  //   MINUTS
  //   MINUTS
  //   SISTEMA D'AVISOS
  //   AVÍS POLICÍA
  //   AVÍS JARDINER
  //   AVÍS MECÀNIC
  //   AVÍS PROPIETÀRI
  //   TEMPERATURA DE
  //   INICI DE LA SIMULACIÓ
  //   (+)
  //   HR DE
  //   INICI DE LA SIMULACIÓ
  //   (+)
  //   (-)
  //   (-)
  //   SISTEMA DE CONTROL DE TEMPERATURA I HUMITAT
  //   (+)
  //   (+)
  //   SENSOR
  //   MOVIMENT C
  //   SENSOR
  //   MOVIMENT JI
  //   SENSOR
  //   MOVIMENT JE
  //   SENSOR
  //   MOVIMENT H
  //   SENSOR
  //   MOVIMENT ZA
  //   TERMOESTAT
  //   (-)
  //   REGULADOR
  //   (-)
  //   SISTEMA DE SEGURETAT
  //   SIM TEMPERATURA REAL
  //   SIM HR REAL
  //   ON/OFF SISTEMA 
  //   LEDS
  //   VENTILADOR
  //   CALEFACTOR
  //   DESHUMIDIFICADOR
  //   HUMIDIFICADOR
  //   SIM AVARÍA
  //   AVARIA MAQUINÀRIA CTRL TEMP
  //   AVARIA SENSOR CTRL TEMP
  //   AVARIA MAQUINÀRIA CTRL HR
  //   AVARIA SENSOR CTRL HR
  //   CHIPS
endmodule

module A1_Tempo_minuts (
  input  Min,
  output A2,
  output B2,
  output C2,
  output D2,
  output E2,
  output F2,
  output G2,
  output A1,
  output B1,
  output C1,
  output D1,
  output E1,
  output F1,
  output G1,
  output P2,
  output P1,
  output DEC0,
  output U0,
  output DEC1,
  output U1,
  output DEC2,
  output U2,
  output DEC3,
  output U4
);

  wire and_1_out, and_2_out;

  and and_1 (and_1_out, DEC2, DEC1);
  _7447 #(.ShowInternalStructure("true")) u_7447_1 (
    .pin1(DEC1), .pin2(DEC2), .pin3(P2), .pin4(P2), .pin5(P2), .pin6(DEC3), .pin7(DEC0), .pin15(F2),
    .pin14(G2), .pin13(A2), .pin12(B2), .pin11(C2), .pin10(D2), .pin9(E2));
  A7_CL74LS90 a7_cl74ls90_1 (
    .Input_A(and_2_out), .Input_B(DEC0), .R9_1(1'b0), .R9_2(1'b0), .R01(and_1_out), .R02(and_1_out),
    .QD(DEC3), .QA(DEC0), .QB(DEC1), .QC(DEC2));
  _7_Segment_Display #(.active("false")) u_7_segment_display_1 (
    .g(G2), .f(F2), .a(A2), .b(B2), .e(E2), .d(D2), .c(C2), .dp(P2));
  and and_2 (and_2_out, U0, U4);
  _7447 #(.ShowInternalStructure("true")) u_7447_2 (
    .pin1(U1), .pin2(U2), .pin3(P1), .pin4(P1), .pin5(P1), .pin6(U4), .pin7(U0), .pin15(F1), .pin14(G1),
    .pin13(A1), .pin12(B1), .pin11(C1), .pin10(D1), .pin9(E1));
  A7_CL74LS90 a7_cl74ls90_2 (
    .Input_A(Min), .Input_B(U0), .R9_1(1'b0), .R9_2(1'b0), .R01(and_2_out), .QD(U4), .QA(U0), .QB(U1), .QC(U2));  // open: R02
  _7_Segment_Display #(.active("false")) u_7_segment_display_2 (
    .g(G1), .f(F1), .a(A1), .b(B1), .e(E1), .d(D1), .c(C1), .dp(P1));
  // also tied to VCC on the sheet: {P1, P2}

  // Notes on the sheet:
  //   BINARIO DECENAS (0 a 6)
  //   MOD 5
  //   DE 00 A 59
  //   MOD 10
  //   BINARIO UNIDADES (0 a 9)
  //   7 SEGMENTOS ACTIVOS A BAJA
endmodule

module A2_Tempo_hores (
  input  in_1,
  output A2,
  output B2,
  output C2,
  output D2,
  output E2,
  output F2,
  output G2,
  output A1,
  output B1,
  output C1,
  output D1,
  output E1,
  output F1,
  output G1,
  output P2,
  output P1,
  output DEC0,
  output DEC1,
  output U0,
  output DEC2,
  output U1,
  output DEC3,
  output U2,
  output U4
);

  wire and_1_out, and_2_out;

  _7447 #(.ShowInternalStructure("true")) u_7447_1 (
    .pin1(DEC1), .pin2(DEC2), .pin3(P2), .pin4(P2), .pin5(P2), .pin6(DEC3), .pin7(DEC0), .pin15(F2),
    .pin14(G2), .pin13(A2), .pin12(B2), .pin11(C2), .pin10(D2), .pin9(E2));
  A7_CL74LS90 a7_cl74ls90_1 (
    .Input_A(and_1_out), .Input_B(DEC0), .R9_1(1'b0), .R9_2(1'b0), .R01(and_2_out), .R02(and_2_out),
    .QD(DEC3), .QA(DEC0), .QB(DEC1), .QC(DEC2));
  _7_Segment_Display #(.active("false")) u_7_segment_display_1 (
    .g(G2), .f(F2), .a(A2), .b(B2), .e(E2), .d(D2), .c(C2), .dp(P2));
  and and_1 (and_1_out, U0, U4);
  and and_2 (and_2_out, DEC1, U2);
  _7447 #(.ShowInternalStructure("true")) u_7447_2 (
    .pin1(U1), .pin2(U2), .pin3(P1), .pin4(P1), .pin5(P1), .pin6(U4), .pin7(U0), .pin15(F1), .pin14(G1),
    .pin13(A1), .pin12(B1), .pin11(C1), .pin10(D1), .pin9(E1));
  A7_CL74LS90 a7_cl74ls90_2 (
    .Input_A(in_1), .Input_B(U0), .R9_1(1'b0), .R9_2(1'b0), .R01(and_2_out), .R02(and_2_out), .QD(U4),
    .QA(U0), .QB(U1), .QC(U2));
  _7_Segment_Display #(.active("false")) u_7_segment_display_2 (
    .g(G1), .f(F1), .a(A1), .b(B1), .e(E1), .d(D1), .c(C1), .dp(P1));
  // also tied to VCC on the sheet: {P1, P2}

  // Notes on the sheet:
  //   DE 00 A 59
  //   7 SEGMENTOS ACTIVOS A BAJA
endmodule

module A3_Temp_Hores_Minuts (
  input  Entrada_H,
  input  Entrada_M,
  output G2H,
  output F2H,
  output A2H,
  output B2H,
  output G1H,
  output F1H,
  output A1H,
  output B1H,
  output G2M,
  output F2M,
  output A2M,
  output B2M,
  output G1M,
  output F1M,
  output A1M,
  output B1M,
  output E2H,
  output D2G,
  output C2H,
  output P2H,
  output E1H,
  output D1H,
  output C1H,
  output P1H,
  output E2M,
  output D2M,
  output C2M,
  output P2M,
  output E1M,
  output D1M,
  output C1M,
  output P1M,
  output [15:0] TB_MA
);

  _7_Segment_Display #(.active("false")) u_7_segment_display_1 (
    .g(G2H), .f(F2H), .a(A2H), .b(B2H), .e(E2H), .d(D2G), .c(C2H), .dp(P2H));
  _7_Segment_Display #(.active("false")) u_7_segment_display_2 (
    .g(G1H), .f(F1H), .a(A1H), .b(B1H), .e(E1H), .d(D1H), .c(C1H), .dp(P1H));
  A2_Tempo_hores a2_tempo_hores_1 (
    .in_1(Entrada_H), .F1(F1H), .G1(G1H), .P1(P1H), .U0(TB_MA[8]), .U1(TB_MA[9]), .U2(TB_MA[10]),
    .U4(TB_MA[11]), .DEC0(TB_MA[12]), .DEC1(TB_MA[13]), .DEC2(TB_MA[14]), .DEC3(TB_MA[15]), .A2(A2H),
    .B2(B2H), .C2(C2H), .D2(D2G), .E2(E2H), .F2(F2H), .G2(G2H), .P2(P2H), .A1(A1H), .B1(B1H), .C1(C1H),
    .D1(D1H), .E1(E1H));
  _7_Segment_Display #(.active("false")) u_7_segment_display_3 (
    .g(G2M), .f(F2M), .a(A2M), .b(B2M), .e(E2M), .d(D2M), .c(C2M), .dp(P2M));
  _7_Segment_Display #(.active("false")) u_7_segment_display_4 (
    .g(G1M), .f(F1M), .a(A1M), .b(B1M), .e(E1M), .d(D1M), .c(C1M), .dp(P1M));
  A1_Tempo_minuts a1_tempo_minuts_1 (
    .Min(Entrada_M), .D2(D2M), .E2(E2M), .F2(F2M), .G2(G2M), .P2(P2M), .A1(A1M), .B1(B1M), .C1(C1M),
    .D1(D1M), .E1(E1M), .F1(F1M), .G1(G1M), .U0(TB_MA[0]), .U1(TB_MA[1]), .U2(TB_MA[2]), .U4(TB_MA[3]),
    .P1(P1M), .DEC0(TB_MA[4]), .DEC1(TB_MA[5]), .DEC2(TB_MA[6]), .DEC3(TB_MA[7]), .A2(A2M), .B2(B2M), .C2(C2M));
endmodule

module A3_Display_HM (
  input  Power,
  input  [15:0] Countador,
  output A4,
  output B4,
  output C4,
  output D4,
  output E4,
  output F4,
  output G4,
  output A3,
  output B3,
  output C3,
  output D3,
  output E3,
  output F3,
  output G3,
  output A2,
  output B2,
  output C2,
  output D2,
  output E2,
  output F2,
  output G2,
  output A1,
  output B1,
  output C1,
  output D1,
  output E1,
  output F1,
  output G1,
  output out_31,
  output P1,
  output out_33,
  output out_34
);

  _7447 #(.ShowInternalStructure("true")) u_7447_1 (
    .pin1(Countador[13]), .pin2(Countador[14]), .pin3(Power), .pin4(Power), .pin5(Power),
    .pin6(Countador[15]), .pin7(Countador[12]), .pin15(F4), .pin14(G4), .pin13(A4), .pin12(B4), .pin11(C4),
    .pin10(D4), .pin9(E4));
  _7_Segment_Display #(.active("false")) u_7_segment_display_1 (
    .g(G4), .f(F4), .a(A4), .b(B4), .e(E4), .d(D4), .c(C4), .dp(Power));
  _7447 #(.ShowInternalStructure("true")) u_7447_2 (
    .pin1(Countador[9]), .pin2(Countador[10]), .pin3(Power), .pin4(Power), .pin5(Power),
    .pin6(Countador[11]), .pin7(Countador[8]), .pin15(F3), .pin14(G3), .pin13(A3), .pin12(B3), .pin11(C3),
    .pin10(D3), .pin9(E3));
  _7_Segment_Display #(.active("false")) u_7_segment_display_2 (
    .g(G3), .f(F3), .a(A3), .b(B3), .e(E3), .d(D3), .c(C3), .dp(Power));
  _7447 #(.ShowInternalStructure("true")) u_7447_3 (
    .pin1(Countador[5]), .pin2(Countador[6]), .pin3(Power), .pin4(Power), .pin5(Power), .pin6(Countador[7]),
    .pin7(Countador[4]), .pin15(F2), .pin14(G2), .pin13(A2), .pin12(B2), .pin11(C2), .pin10(D2), .pin9(E2));
  _7_Segment_Display #(.active("false")) u_7_segment_display_3 (
    .g(G2), .f(F2), .a(A2), .b(B2), .e(E2), .d(D2), .c(C2), .dp(Power));
  _7447 #(.ShowInternalStructure("true")) u_7447_4 (
    .pin1(Countador[1]), .pin2(Countador[2]), .pin3(Power), .pin4(Power), .pin5(Power), .pin6(Countador[3]),
    .pin7(Countador[0]), .pin15(F1), .pin14(G1), .pin13(A1), .pin12(B1), .pin11(C1), .pin10(D1), .pin9(E1));
  _7_Segment_Display #(.active("false")) u_7_segment_display_4 (
    .g(G1), .f(F1), .a(A1), .b(B1), .e(E1), .d(D1), .c(C1), .dp(Power));

  assign out_31 = Power;
  assign out_33 = Power;
  assign out_34 = Power;
  assign P1 = Power;

  // Notes on the sheet:
  //   7 SEGMENTOS ACTIVOS A BAJA
endmodule

module A4_Rellotge_Intern (
  input  Power,
  input  RESET,
  input  Entrada_manual_H,
  input  Entrada_Manual_M,
  output A6,
  output B6,
  output C6,
  output D6,
  output E6,
  output F6,
  output G6,
  output A4,
  output B4,
  output C4,
  output D4,
  output E4,
  output F4,
  output G4,
  output A2,
  output B2,
  output C2,
  output D2,
  output E2,
  output F2,
  output G2,
  output A5,
  output B5,
  output C5,
  output D5,
  output E5,
  output F5,
  output G5,
  output A3,
  output B3,
  output C3,
  output D3,
  output E3,
  output F3,
  output G3,
  output A1,
  output B1,
  output C1,
  output D1,
  output E1,
  output F1,
  output G1,
  output P6,
  output P4,
  output P2,
  output P5,
  output p3,
  output P1,
  output [15:0] Hora_Act_Bin_16B
);

  wire and_1_out, and_2_out, and_3_out, and_4_out, and_5_out, and_6_out, and_7_out, clock_1_out,
       n7447_5_pin1, n7447_5_pin2, n7447_5_pin6, n7447_5_pin7, n7447_6_pin1, n7447_6_pin2, n7447_6_pin6,
       n7447_6_pin7, nor_1_out, nor_2_out, or_1_out, or_2_out, or_3_out, or_4_out, or_5_out;

  A7_CL74LS90 a7_cl74ls90_1 (
    .Input_A(and_1_out), .Input_B(Hora_Act_Bin_16B[12]), .R9_1(1'b0), .R9_2(1'b0), .R01(or_1_out),
    .R02(or_1_out), .QD(Hora_Act_Bin_16B[15]), .QA(Hora_Act_Bin_16B[12]), .QB(Hora_Act_Bin_16B[13]),
    .QC(Hora_Act_Bin_16B[14]));
  _7447 #(.ShowInternalStructure("true")) u_7447_1 (
    .pin1(Hora_Act_Bin_16B[13]), .pin2(Hora_Act_Bin_16B[14]), .pin3(P1), .pin4(P1), .pin5(P1),
    .pin6(Hora_Act_Bin_16B[15]), .pin7(Hora_Act_Bin_16B[12]), .pin15(F6), .pin14(G6), .pin13(A6), .pin12(B6),
    .pin11(C6), .pin10(D6), .pin9(E6));
  _7_Segment_Display #(.active("false")) u_7_segment_display_1 (
    .g(G6), .f(F6), .a(A6), .b(B6), .e(E6), .d(D6), .c(C6), .dp(P1));
  and and_1 (and_1_out, Hora_Act_Bin_16B[8], Hora_Act_Bin_16B[11]);
  _7447 #(.ShowInternalStructure("true")) u_7447_2 (
    .pin1(Hora_Act_Bin_16B[9]), .pin2(Hora_Act_Bin_16B[10]), .pin3(P1), .pin4(P1), .pin5(P1),
    .pin6(Hora_Act_Bin_16B[11]), .pin7(Hora_Act_Bin_16B[8]), .pin15(F5), .pin14(G5), .pin13(A5), .pin12(B5),
    .pin11(C5), .pin10(D5), .pin9(E5));
  A7_CL74LS90 a7_cl74ls90_2 (
    .Input_A(nor_1_out), .Input_B(Hora_Act_Bin_16B[8]), .R9_1(1'b0), .R9_2(1'b0), .R01(or_1_out),
    .R02(or_1_out), .QD(Hora_Act_Bin_16B[11]), .QA(Hora_Act_Bin_16B[8]), .QB(Hora_Act_Bin_16B[9]),
    .QC(Hora_Act_Bin_16B[10]));
  and and_2 (and_2_out, Hora_Act_Bin_16B[13], Hora_Act_Bin_16B[10]);
  or or_1 (or_1_out, and_2_out, RESET);
  nor nor_1 (nor_1_out, and_3_out, Entrada_manual_H);
  _7_Segment_Display #(.active("false")) u_7_segment_display_2 (
    .g(G5), .f(F5), .a(A5), .b(B5), .e(E5), .d(D5), .c(C5), .dp(P1));
  and and_3 (and_3_out, Hora_Act_Bin_16B[6], Hora_Act_Bin_16B[5]);
  _7447 #(.ShowInternalStructure("true")) u_7447_3 (
    .pin1(Hora_Act_Bin_16B[5]), .pin2(Hora_Act_Bin_16B[6]), .pin3(P1), .pin4(P1), .pin5(P1),
    .pin6(Hora_Act_Bin_16B[7]), .pin7(Hora_Act_Bin_16B[4]), .pin15(F4), .pin14(G4), .pin13(A4), .pin12(B4),
    .pin11(C4), .pin10(D4), .pin9(E4));
  A7_CL74LS90 a7_cl74ls90_3 (
    .Input_A(and_4_out), .Input_B(Hora_Act_Bin_16B[4]), .R9_1(1'b0), .R9_2(1'b0), .R01(or_2_out),
    .R02(or_2_out), .QD(Hora_Act_Bin_16B[7]), .QA(Hora_Act_Bin_16B[4]), .QB(Hora_Act_Bin_16B[5]),
    .QC(Hora_Act_Bin_16B[6]));
  or or_2 (or_2_out, and_3_out, RESET);
  _7_Segment_Display #(.active("false")) u_7_segment_display_3 (
    .g(G4), .f(F4), .a(A4), .b(B4), .e(E4), .d(D4), .c(C4), .dp(P1));
  and and_4 (and_4_out, Hora_Act_Bin_16B[0], Hora_Act_Bin_16B[3]);
  _7447 #(.ShowInternalStructure("true")) u_7447_4 (
    .pin1(Hora_Act_Bin_16B[1]), .pin2(Hora_Act_Bin_16B[2]), .pin3(P1), .pin4(P1), .pin5(P1),
    .pin6(Hora_Act_Bin_16B[3]), .pin7(Hora_Act_Bin_16B[0]), .pin15(F3), .pin14(G3), .pin13(A3), .pin12(B3),
    .pin11(C3), .pin10(D3), .pin9(E3));
  A7_CL74LS90 a7_cl74ls90_4 (
    .Input_A(nor_2_out), .Input_B(Hora_Act_Bin_16B[0]), .R9_1(1'b0), .R9_2(1'b0), .R01(or_3_out),
    .R02(RESET), .QD(Hora_Act_Bin_16B[3]), .QA(Hora_Act_Bin_16B[0]), .QB(Hora_Act_Bin_16B[1]),
    .QC(Hora_Act_Bin_16B[2]));
  nor nor_2 (nor_2_out, and_5_out, Entrada_Manual_M);
  or or_3 (or_3_out, and_4_out, RESET);
  _7_Segment_Display #(.active("false")) u_7_segment_display_4 (
    .g(G3), .f(F3), .a(A3), .b(B3), .e(E3), .d(D3), .c(C3), .dp(P1));
  _7447 #(.ShowInternalStructure("true")) u_7447_5 (
    .pin1(n7447_5_pin1), .pin2(n7447_5_pin2), .pin3(P1), .pin4(P1), .pin5(P1), .pin6(n7447_5_pin6),
    .pin7(n7447_5_pin7), .pin15(F2), .pin14(G2), .pin13(A2), .pin12(B2), .pin11(C2), .pin10(D2), .pin9(E2));
  and and_5 (and_5_out, n7447_5_pin2, n7447_5_pin1);
  or or_4 (or_4_out, and_5_out, RESET);
  A7_CL74LS90 a7_cl74ls90_5 (
    .Input_A(and_6_out), .Input_B(n7447_5_pin7), .R9_1(1'b0), .R9_2(1'b0), .R01(or_4_out), .R02(or_4_out),
    .QD(n7447_5_pin6), .QA(n7447_5_pin7), .QB(n7447_5_pin1), .QC(n7447_5_pin2));
  _7_Segment_Display #(.active("false")) u_7_segment_display_5 (
    .g(G2), .f(F2), .a(A2), .b(B2), .e(E2), .d(D2), .c(C2), .dp(P1));
  _7447 #(.ShowInternalStructure("true")) u_7447_6 (
    .pin1(n7447_6_pin1), .pin2(n7447_6_pin2), .pin3(P1), .pin4(P1), .pin5(P1), .pin6(n7447_6_pin6),
    .pin7(n7447_6_pin7), .pin15(F1), .pin14(G1), .pin13(A1), .pin12(B1), .pin11(C1), .pin10(D1), .pin9(E1));
  and and_6 (and_6_out, n7447_6_pin7, n7447_6_pin6);
  A7_CL74LS90 a7_cl74ls90_6 (
    .Input_A(and_7_out), .Input_B(n7447_6_pin7), .R9_1(1'b0), .R9_2(1'b0), .R01(or_5_out), .R02(RESET),
    .QD(n7447_6_pin6), .QA(n7447_6_pin7), .QB(n7447_6_pin1), .QC(n7447_6_pin2));
  or or_5 (or_5_out, and_6_out, RESET);
  _7_Segment_Display #(.active("false")) u_7_segment_display_6 (
    .g(G1), .f(F1), .a(A1), .b(B1), .e(E1), .d(D1), .c(C1), .dp(P1));
  and and_7 (and_7_out, clock_1_out, Power);
  Clock clock_1 (.out(clock_1_out));

  assign P2 = P1;
  assign p3 = P1;
  assign P4 = P1;
  assign P5 = P1;
  assign P6 = P1;
  // also tied to VCC on the sheet: P1

  // Notes on the sheet:
  //   7 SEGMENTOS ACTIVOS A BAJA
  //   FREQUENCIA INICIAL A 2HZ
endmodule

module A5_Control_Botons_Leds (
  input  Boto_Prog,
  input  Avaria_Motor1,
  input  Boto_Auto,
  input  Avaria_Motor2,
  input  LJI,
  input  LJE,
  input  LH,
  input  LA,
  output LEDAVM1,
  output LEDAVM2,
  output L1_Prog,
  output L0_Auto,
  output Activador_SR_A,
  output Activador_SR_P,
  output LCJI,
  output LCJE,
  output LCH,
  output LJA
);

  wire and_1_out, and_2_out, and_3_out, and_4_out, and_5_out, and_6_out, and_7_out, and_8_out, and_9_out,
       clock_1_out, d_ff_1_qn, d_ff_2_qn, d_ff_3_q, d_ff_3_qn, d_ff_4_q, d_ff_4_qn, d_ff_5_q, d_ff_5_qn,
       d_ff_6_q, d_ff_6_qn, d_ff_7_q, d_ff_7_qn, d_ff_8_q, d_ff_8_qn, not_1_out, not_2_out, not_3_out,
       not_4_out, not_5_out, not_6_out, or_1_out, or_2_out, or_3_out, or_4_out, or_5_out, xor_1_out;

  D_Flip_Flop d_ff_1 (.D(d_ff_1_qn), .clk(Avaria_Motor1), .Q(LEDAVM1), .Qn(d_ff_1_qn));  // open: preset, reset
  D_Flip_Flop d_ff_2 (.D(d_ff_2_qn), .clk(Avaria_Motor2), .Q(LEDAVM2), .Qn(d_ff_2_qn));  // open: preset, reset
  not not_1 (not_1_out, or_1_out);
  or or_1 (or_1_out, LEDAVM1, LEDAVM2);
  not not_2 (not_2_out, or_1_out);
  and and_1 (and_1_out, d_ff_3_q, or_1_out);
  and and_2 (and_2_out, not_2_out, Boto_Auto);
  and and_3 (and_3_out, Boto_Prog, not_1_out);
  or or_2 (or_2_out, and_3_out, and_4_out);
  and and_4 (and_4_out, or_1_out, d_ff_4_q);
  D_Flip_Flop d_ff_3 (.D(d_ff_3_qn), .clk(or_3_out), .Q(d_ff_3_q), .Qn(d_ff_3_qn));  // open: preset, reset
  or or_3 (or_3_out, and_1_out, and_2_out);
  not not_3 (not_3_out, L1_Prog);
  not not_4 (not_4_out, L0_Auto);
  and and_5 (and_5_out, not_3_out, not_4_out);
  D_Flip_Flop d_ff_4 (.D(d_ff_4_qn), .clk(or_2_out), .Q(d_ff_4_q), .Qn(d_ff_4_qn));  // open: preset, reset
  D_Flip_Flop #(.trigger("falling")) d_ff_5 (
    .D(d_ff_5_qn), .clk(LJI), .Q(d_ff_5_q), .Qn(d_ff_5_qn), .reset(and_5_out));  // open: preset
  D_Flip_Flop #(.trigger("falling")) d_ff_6 (
    .D(d_ff_6_qn), .clk(LJE), .Q(d_ff_6_q), .Qn(d_ff_6_qn), .reset(and_5_out));  // open: preset
  D_Flip_Flop #(.trigger("falling")) d_ff_7 (
    .D(d_ff_7_qn), .clk(LH), .Q(d_ff_7_q), .Qn(d_ff_7_qn), .reset(and_5_out));  // open: preset
  D_Flip_Flop #(.trigger("falling")) d_ff_8 (
    .D(d_ff_8_qn), .clk(LA), .Q(d_ff_8_q), .Qn(d_ff_8_qn), .reset(and_5_out));  // open: preset
  Clock clock_1 (.out(clock_1_out));
  D_Flip_Flop #(.trigger("falling")) d_ff_9 (.Q(LJA), .preset(d_ff_8_q), .reset(and_5_out));  // open: D, clk, Qn
  not not_5 (not_5_out, d_ff_4_q);
  not not_6 (not_6_out, d_ff_3_q);
  D_Flip_Flop #(.trigger("falling")) d_ff_10 (.Q(LCJI), .preset(d_ff_5_q), .reset(and_5_out));  // open: D, clk, Qn
  D_Flip_Flop #(.trigger("falling")) d_ff_11 (.Q(LCJE), .preset(d_ff_6_q), .reset(and_5_out));  // open: D, clk, Qn
  D_Flip_Flop #(.trigger("falling")) d_ff_12 (.Q(LCH), .preset(d_ff_7_q), .reset(and_5_out));  // open: D, clk, Qn
  and and_6 (and_6_out, d_ff_4_q, not_6_out);
  and and_7 (and_7_out, L0_Auto, d_ff_4_q);
  and and_8 (and_8_out, not_5_out, d_ff_3_q);
  and and_9 (and_9_out, L1_Prog, d_ff_3_q);
  or or_4 (or_4_out, and_6_out, and_7_out);
  or or_5 (or_5_out, and_8_out, and_9_out);
  D_Flip_Flop d_ff_13 (.D(or_4_out), .clk(clock_1_out), .Q(L1_Prog));  // open: Qn, preset, reset
  D_Flip_Flop d_ff_14 (.D(or_5_out), .clk(clock_1_out), .Q(L0_Auto));  // open: Qn, preset, reset
  xor xor_1 (xor_1_out, d_ff_4_q, d_ff_3_q);
  and and_10 (Activador_SR_A, d_ff_3_q, xor_1_out);
  and and_11 (Activador_SR_P, xor_1_out, d_ff_4_q);

  // Notes on the sheet:
  //   BUG 04: Multiples senyals. Sol cutre més biestables
  //   Control d'errors (No podem tiendre els dos sistemes al mateix temps)
  //   HEM APLICAT MOORE
  //   Llum prog
  //   Llum auto
endmodule
module A6_Logica_Control (
  input  Boto_Prog,
  input  Avaria_Motor1,
  input  Boto_Auto,
  input  Avaria_Motor2,
  input  [15:0] Temps_JI,
  input  [15:0] Hora_Actual,
  input  [15:0] Hora_JI,
  input  [15:0] Temps_JE,
  input  [15:0] Hora_JE,
  input  [15:0] Hora_Hort,
  input  [15:0] Temps_H,
  input  [15:0] Hora_Arbres,
  input  [15:0] Temps_Comu,
  input  [15:0] Temps_A,
  output [15:0] TJICR,
  output [15:0] CRJI,
  output [15:0] TJECR,
  output [15:0] CRJE,
  output [15:0] THCR,
  output [15:0] CRH,
  output [15:0] TACR,
  output [15:0] CRA,
  output LED_JI,
  output LED_JE,
  output LED_H,
  output LED_A,
  output Motor1,
  output Motor2,
  output V1,
  output V2,
  output V3,
  output V4
);

  wire a4_rellotge_intern_1_a1, a4_rellotge_intern_1_a2, a4_rellotge_intern_1_a3, a4_rellotge_intern_1_a4,
       a4_rellotge_intern_1_a5, a4_rellotge_intern_1_a6, a4_rellotge_intern_1_b1, a4_rellotge_intern_1_b2,
       a4_rellotge_intern_1_b3, a4_rellotge_intern_1_b4, a4_rellotge_intern_1_b5, a4_rellotge_intern_1_b6,
       a4_rellotge_intern_1_c1, a4_rellotge_intern_1_c2, a4_rellotge_intern_1_c3, a4_rellotge_intern_1_c4,
       a4_rellotge_intern_1_c5, a4_rellotge_intern_1_c6, a4_rellotge_intern_1_d1, a4_rellotge_intern_1_d2,
       a4_rellotge_intern_1_d3, a4_rellotge_intern_1_d4, a4_rellotge_intern_1_d5, a4_rellotge_intern_1_d6,
       a4_rellotge_intern_1_e1, a4_rellotge_intern_1_e2, a4_rellotge_intern_1_e3, a4_rellotge_intern_1_e4,
       a4_rellotge_intern_1_e5, a4_rellotge_intern_1_e6, a4_rellotge_intern_1_f1, a4_rellotge_intern_1_f2,
       a4_rellotge_intern_1_f3, a4_rellotge_intern_1_f4, a4_rellotge_intern_1_f5, a4_rellotge_intern_1_f6,
       a4_rellotge_intern_1_g1, a4_rellotge_intern_1_g2, a4_rellotge_intern_1_g3, a4_rellotge_intern_1_g4,
       a4_rellotge_intern_1_g5, a4_rellotge_intern_1_g6, a4_rellotge_intern_1_p1, a4_rellotge_intern_1_p2,
       a4_rellotge_intern_1_p3, a4_rellotge_intern_1_p4, a4_rellotge_intern_1_p5, a4_rellotge_intern_1_p6,
       a4_rellotge_intern_2_a1, a4_rellotge_intern_2_a2, a4_rellotge_intern_2_a3, a4_rellotge_intern_2_a4,
       a4_rellotge_intern_2_a5, a4_rellotge_intern_2_a6, a4_rellotge_intern_2_b1, a4_rellotge_intern_2_b2,
       a4_rellotge_intern_2_b3, a4_rellotge_intern_2_b4, a4_rellotge_intern_2_b5, a4_rellotge_intern_2_b6,
       a4_rellotge_intern_2_c1, a4_rellotge_intern_2_c2, a4_rellotge_intern_2_c3, a4_rellotge_intern_2_c4,
       a4_rellotge_intern_2_c5, a4_rellotge_intern_2_c6, a4_rellotge_intern_2_d1, a4_rellotge_intern_2_d2,
       a4_rellotge_intern_2_d3, a4_rellotge_intern_2_d4, a4_rellotge_intern_2_d5, a4_rellotge_intern_2_d6,
       a4_rellotge_intern_2_e1, a4_rellotge_intern_2_e2, a4_rellotge_intern_2_e3, a4_rellotge_intern_2_e4,
       a4_rellotge_intern_2_e5, a4_rellotge_intern_2_e6, a4_rellotge_intern_2_f1, a4_rellotge_intern_2_f2,
       a4_rellotge_intern_2_f3, a4_rellotge_intern_2_f4, a4_rellotge_intern_2_f5, a4_rellotge_intern_2_f6,
       a4_rellotge_intern_2_g1, a4_rellotge_intern_2_g2, a4_rellotge_intern_2_g3, a4_rellotge_intern_2_g4,
       a4_rellotge_intern_2_g5, a4_rellotge_intern_2_g6, a4_rellotge_intern_2_p1, a4_rellotge_intern_2_p2,
       a4_rellotge_intern_2_p3, a4_rellotge_intern_2_p4, a4_rellotge_intern_2_p5, a4_rellotge_intern_2_p6,
       a4_rellotge_intern_3_a1, a4_rellotge_intern_3_a2, a4_rellotge_intern_3_a3, a4_rellotge_intern_3_a4,
       a4_rellotge_intern_3_a5, a4_rellotge_intern_3_a6, a4_rellotge_intern_3_b1, a4_rellotge_intern_3_b2,
       a4_rellotge_intern_3_b3, a4_rellotge_intern_3_b4, a4_rellotge_intern_3_b5, a4_rellotge_intern_3_b6,
       a4_rellotge_intern_3_c1, a4_rellotge_intern_3_c2, a4_rellotge_intern_3_c3, a4_rellotge_intern_3_c4,
       a4_rellotge_intern_3_c5, a4_rellotge_intern_3_c6, a4_rellotge_intern_3_d1, a4_rellotge_intern_3_d2,
       a4_rellotge_intern_3_d3, a4_rellotge_intern_3_d4, a4_rellotge_intern_3_d5, a4_rellotge_intern_3_d6,
       a4_rellotge_intern_3_e1, a4_rellotge_intern_3_e2, a4_rellotge_intern_3_e3, a4_rellotge_intern_3_e4,
       a4_rellotge_intern_3_e5, a4_rellotge_intern_3_e6, a4_rellotge_intern_3_f1, a4_rellotge_intern_3_f2,
       a4_rellotge_intern_3_f3, a4_rellotge_intern_3_f4, a4_rellotge_intern_3_f5, a4_rellotge_intern_3_f6,
       a4_rellotge_intern_3_g1, a4_rellotge_intern_3_g2, a4_rellotge_intern_3_g3, a4_rellotge_intern_3_g4,
       a4_rellotge_intern_3_g5, a4_rellotge_intern_3_g6, a4_rellotge_intern_3_p1, a4_rellotge_intern_3_p2,
       a4_rellotge_intern_3_p3, a4_rellotge_intern_3_p4, a4_rellotge_intern_3_p5, a4_rellotge_intern_3_p6,
       a4_rellotge_intern_4_a1, a4_rellotge_intern_4_a2, a4_rellotge_intern_4_a3, a4_rellotge_intern_4_a4,
       a4_rellotge_intern_4_a5, a4_rellotge_intern_4_a6, a4_rellotge_intern_4_b1, a4_rellotge_intern_4_b2,
       a4_rellotge_intern_4_b3, a4_rellotge_intern_4_b4, a4_rellotge_intern_4_b5, a4_rellotge_intern_4_b6,
       a4_rellotge_intern_4_c1, a4_rellotge_intern_4_c2, a4_rellotge_intern_4_c3, a4_rellotge_intern_4_c4,
       a4_rellotge_intern_4_c5, a4_rellotge_intern_4_c6, a4_rellotge_intern_4_d1, a4_rellotge_intern_4_d2,
       a4_rellotge_intern_4_d3, a4_rellotge_intern_4_d4, a4_rellotge_intern_4_d5, a4_rellotge_intern_4_d6,
       a4_rellotge_intern_4_e1, a4_rellotge_intern_4_e2, a4_rellotge_intern_4_e3, a4_rellotge_intern_4_e4,
       a4_rellotge_intern_4_e5, a4_rellotge_intern_4_e6, a4_rellotge_intern_4_f1, a4_rellotge_intern_4_f2,
       a4_rellotge_intern_4_f3, a4_rellotge_intern_4_f4, a4_rellotge_intern_4_f5, a4_rellotge_intern_4_f6,
       a4_rellotge_intern_4_g1, a4_rellotge_intern_4_g2, a4_rellotge_intern_4_g3, a4_rellotge_intern_4_g4,
       a4_rellotge_intern_4_g5, a4_rellotge_intern_4_g6, a4_rellotge_intern_4_p1, a4_rellotge_intern_4_p2,
       a4_rellotge_intern_4_p3, a4_rellotge_intern_4_p4, a4_rellotge_intern_4_p5, a4_rellotge_intern_4_p6,
       a4_rellotge_intern_5_a1, a4_rellotge_intern_5_a2, a4_rellotge_intern_5_a3, a4_rellotge_intern_5_a4,
       a4_rellotge_intern_5_a5, a4_rellotge_intern_5_a6, a4_rellotge_intern_5_b1, a4_rellotge_intern_5_b2,
       a4_rellotge_intern_5_b3, a4_rellotge_intern_5_b4, a4_rellotge_intern_5_b5, a4_rellotge_intern_5_b6,
       a4_rellotge_intern_5_c1, a4_rellotge_intern_5_c2, a4_rellotge_intern_5_c3, a4_rellotge_intern_5_c4,
       a4_rellotge_intern_5_c5, a4_rellotge_intern_5_c6, a4_rellotge_intern_5_d1, a4_rellotge_intern_5_d2,
       a4_rellotge_intern_5_d3, a4_rellotge_intern_5_d4, a4_rellotge_intern_5_d5, a4_rellotge_intern_5_d6,
       a4_rellotge_intern_5_e1, a4_rellotge_intern_5_e2, a4_rellotge_intern_5_e3, a4_rellotge_intern_5_e4,
       a4_rellotge_intern_5_e5, a4_rellotge_intern_5_e6, a4_rellotge_intern_5_f1, a4_rellotge_intern_5_f2,
       a4_rellotge_intern_5_f3, a4_rellotge_intern_5_f4, a4_rellotge_intern_5_f5, a4_rellotge_intern_5_f6,
       a4_rellotge_intern_5_g1, a4_rellotge_intern_5_g2, a4_rellotge_intern_5_g3, a4_rellotge_intern_5_g4,
       a4_rellotge_intern_5_g5, a4_rellotge_intern_5_g6, a4_rellotge_intern_5_p1, a4_rellotge_intern_5_p2,
       a4_rellotge_intern_5_p3, a4_rellotge_intern_5_p4, a4_rellotge_intern_5_p5, a4_rellotge_intern_5_p6,
       and_1_out, and_2_out, and_3_out, and_4_out, and_5_out, and_6_out, and_7_out, and_8_out, and_9_out,
       and_10_out, and_11_out, and_12_out, button_1_out, comparator_1_eq, comparator_2_eq, comparator_3_eq,
       comparator_4_eq, comparator_5_gt, comparator_6_eq, comparator_7_eq, comparator_8_eq, comparator_9_eq,
       comparator_10_eq, comparator_11_eq, d_ff_1_q, d_ff_1_qn, d_ff_2_q, d_ff_2_qn, d_ff_3_q, d_ff_4_q,
       d_ff_4_qn, d_ff_5_q, d_ff_5_qn, d_ff_6_qn, d_ff_7_qn, d_ff_8_qn, d_ff_9_q, d_ff_10_q, d_ff_11_q,
       d_ff_12_q, demultiplexer_1_out0, demultiplexer_1_out1, demultiplexer_1_out2, demultiplexer_1_out3,
       not_1_out, not_2_out, not_3_out, not_4_out, not_5_out, not_6_out, not_7_out, or_1_out, or_2_out,
       or_3_out;
  wire [2:0] d_ff_6_q;
  wire [15:0] a4_rellotge_intern_1_hora_act_bin_16b, a4_rellotge_intern_2_hora_act_bin_16b,
       a4_rellotge_intern_3_hora_act_bin_16b, a4_rellotge_intern_4_hora_act_bin_16b,
       a4_rellotge_intern_5_hora_act_bin_16b;

  D_Flip_Flop d_ff_1 (.D(d_ff_1_qn), .clk(Avaria_Motor1), .Q(d_ff_1_q), .Qn(d_ff_1_qn));  // open: preset, reset
  D_Flip_Flop d_ff_2 (.D(d_ff_2_qn), .clk(Avaria_Motor2), .Q(d_ff_2_q), .Qn(d_ff_2_qn));  // open: preset, reset
  or or_1 (or_1_out, d_ff_1_q, d_ff_2_q);
  not not_1 (not_1_out, or_1_out);
  not not_2 (not_2_out, or_1_out);
  not not_3 (not_3_out, comparator_6_eq);
  and and_1 (and_1_out, not_3_out, and_12_out);
  D_Flip_Flop d_ff_3 (.Q(d_ff_3_q), .preset(and_1_out), .reset(comparator_7_eq));  // open: D, clk, Qn
  and and_2 (and_2_out, Boto_Prog, not_1_out);
  and and_3 (and_3_out, or_1_out, d_ff_4_q);
  and and_4 (and_4_out, d_ff_5_q, or_1_out);
  or or_2 (or_2_out, and_4_out, and_5_out);
  and and_5 (and_5_out, not_2_out, Boto_Auto);
  not not_4 (not_4_out, and_12_out);
  Button button_1 (.out(button_1_out));
  D_Flip_Flop d_ff_4 (.D(d_ff_4_qn), .clk(or_3_out), .Q(d_ff_4_q), .Qn(d_ff_4_qn));  // open: preset, reset
  or or_3 (or_3_out, and_2_out, and_3_out);
  D_Flip_Flop d_ff_5 (.D(d_ff_5_qn), .clk(or_2_out), .Q(d_ff_5_q), .Qn(d_ff_5_qn));  // open: preset, reset
  _7_Segment_Display #(.active("false")) u_7_segment_display_1 (
    .g(a4_rellotge_intern_1_g6), .f(a4_rellotge_intern_1_f6), .a(a4_rellotge_intern_1_a6),
    .b(a4_rellotge_intern_1_b6), .e(a4_rellotge_intern_1_e6), .d(a4_rellotge_intern_1_d6),
    .c(a4_rellotge_intern_1_c6), .dp(a4_rellotge_intern_1_p6));
  D_Flip_Flop d_ff_6 (
    .D(d_ff_6_qn), .clk(comparator_7_eq), .Q(d_ff_6_q[0]), .Qn(d_ff_6_qn), .preset(button_1_out),
    .reset(not_4_out));
  _7_Segment_Display #(.active("false")) u_7_segment_display_2 (
    .g(a4_rellotge_intern_1_g5), .f(a4_rellotge_intern_1_f5), .a(a4_rellotge_intern_1_a5),
    .b(a4_rellotge_intern_1_b5), .e(a4_rellotge_intern_1_e5), .d(a4_rellotge_intern_1_d5),
    .c(a4_rellotge_intern_1_c5), .dp(a4_rellotge_intern_1_p5));
  _7_Segment_Display #(.active("false")) u_7_segment_display_3 (
    .g(a4_rellotge_intern_1_g4), .f(a4_rellotge_intern_1_f4), .a(a4_rellotge_intern_1_a4),
    .b(a4_rellotge_intern_1_b4), .e(a4_rellotge_intern_1_e4), .d(a4_rellotge_intern_1_d4),
    .c(a4_rellotge_intern_1_c4), .dp(a4_rellotge_intern_1_p4));
  Comparator #(.width(16)) comparator_1 (.a(Hora_JI), .b(Hora_Actual), .eq(comparator_1_eq));  // open: gt, lt
  Comparator #(.width(16)) comparator_2 (.a(Hora_JE), .b(Hora_Actual), .eq(comparator_2_eq));  // open: gt, lt
  Comparator #(.width(16)) comparator_3 (.a(Hora_Hort), .b(Hora_Actual), .eq(comparator_3_eq));  // open: gt, lt
  Comparator #(.width(16)) comparator_4 (.a(Hora_Arbres), .b(Hora_Actual), .eq(comparator_4_eq));  // open: gt, lt
  Comparator #(.width(16)) comparator_5 (.a(Temps_Comu), .b({16{1'b0}}), .gt(comparator_5_gt));  // open: eq, lt
  _7_Segment_Display #(.active("false")) u_7_segment_display_4 (
    .g(a4_rellotge_intern_1_g3), .f(a4_rellotge_intern_1_f3), .a(a4_rellotge_intern_1_a3),
    .b(a4_rellotge_intern_1_b3), .e(a4_rellotge_intern_1_e3), .d(a4_rellotge_intern_1_d3),
    .c(a4_rellotge_intern_1_c3), .dp(a4_rellotge_intern_1_p3));
  D_Flip_Flop d_ff_7 (
    .D(d_ff_7_qn), .clk(d_ff_6_qn), .Q(d_ff_6_q[1]), .Qn(d_ff_7_qn), .preset(button_1_out), .reset(not_4_out));
  not not_5 (not_5_out, d_ff_5_q);
  not not_6 (not_6_out, d_ff_4_q);
  and and_6 (and_6_out, d_ff_5_q, not_6_out);
  _7_Segment_Display #(.active("false")) u_7_segment_display_5 (
    .g(a4_rellotge_intern_1_g2), .f(a4_rellotge_intern_1_f2), .a(a4_rellotge_intern_1_a2),
    .b(a4_rellotge_intern_1_b2), .e(a4_rellotge_intern_1_e2), .d(a4_rellotge_intern_1_d2),
    .c(a4_rellotge_intern_1_c2), .dp(a4_rellotge_intern_1_p2));
  not not_7 (not_7_out, and_7_out);
  and and_7 (and_7_out, not_5_out, d_ff_4_q);
  and and_8 (and_8_out, comparator_1_eq, and_7_out);
  and and_9 (and_9_out, comparator_2_eq, and_7_out);
  and and_10 (and_10_out, comparator_3_eq, and_7_out);
  and and_11 (and_11_out, comparator_4_eq, and_7_out);
  and and_12 (and_12_out, comparator_5_gt, and_6_out);
  _7_Segment_Display #(.active("false")) u_7_segment_display_6 (
    .g(a4_rellotge_intern_1_g1), .f(a4_rellotge_intern_1_f1), .a(a4_rellotge_intern_1_a1),
    .b(a4_rellotge_intern_1_b1), .e(a4_rellotge_intern_1_e1), .d(a4_rellotge_intern_1_d1),
    .c(a4_rellotge_intern_1_c1), .dp(a4_rellotge_intern_1_p1));
  A4_Rellotge_Intern a4_rellotge_intern_1 (
    .Power(d_ff_3_q), .RESET(comparator_7_eq), .E4(a4_rellotge_intern_1_e4), .F4(a4_rellotge_intern_1_f4),
    .G4(a4_rellotge_intern_1_g4), .P4(a4_rellotge_intern_1_p4), .A3(a4_rellotge_intern_1_a3),
    .B3(a4_rellotge_intern_1_b3), .C3(a4_rellotge_intern_1_c3), .D3(a4_rellotge_intern_1_d3),
    .E3(a4_rellotge_intern_1_e3), .F3(a4_rellotge_intern_1_f3), .G3(a4_rellotge_intern_1_g3),
    .p3(a4_rellotge_intern_1_p3), .A2(a4_rellotge_intern_1_a2), .B2(a4_rellotge_intern_1_b2),
    .C2(a4_rellotge_intern_1_c2), .D2(a4_rellotge_intern_1_d2), .E2(a4_rellotge_intern_1_e2),
    .F2(a4_rellotge_intern_1_f2), .G2(a4_rellotge_intern_1_g2), .P2(a4_rellotge_intern_1_p2),
    .A1(a4_rellotge_intern_1_a1), .B1(a4_rellotge_intern_1_b1), .C1(a4_rellotge_intern_1_c1),
    .D1(a4_rellotge_intern_1_d1), .E1(a4_rellotge_intern_1_e1), .F1(a4_rellotge_intern_1_f1),
    .G1(a4_rellotge_intern_1_g1), .P1(a4_rellotge_intern_1_p1), .A6(a4_rellotge_intern_1_a6),
    .B6(a4_rellotge_intern_1_b6), .C6(a4_rellotge_intern_1_c6), .D6(a4_rellotge_intern_1_d6),
    .E6(a4_rellotge_intern_1_e6), .F6(a4_rellotge_intern_1_f6), .G6(a4_rellotge_intern_1_g6),
    .P6(a4_rellotge_intern_1_p6), .A5(a4_rellotge_intern_1_a5), .B5(a4_rellotge_intern_1_b5),
    .C5(a4_rellotge_intern_1_c5), .D5(a4_rellotge_intern_1_d5), .E5(a4_rellotge_intern_1_e5),
    .F5(a4_rellotge_intern_1_f5), .G5(a4_rellotge_intern_1_g5), .P5(a4_rellotge_intern_1_p5),
    .A4(a4_rellotge_intern_1_a4), .Hora_Act_Bin_16B(a4_rellotge_intern_1_hora_act_bin_16b),
    .B4(a4_rellotge_intern_1_b4), .C4(a4_rellotge_intern_1_c4), .D4(a4_rellotge_intern_1_d4));  // open: Entrada_Manual_M, Entrada_manual_H
  D_Flip_Flop d_ff_8 (
    .D(d_ff_8_qn), .clk(d_ff_7_qn), .Q(d_ff_6_q[2]), .Qn(d_ff_8_qn), .preset(button_1_out), .reset(not_4_out));
  Comparator #(.width(3)) comparator_6 (.a(d_ff_6_q), .b(3'b100), .eq(comparator_6_eq));  // open: gt, lt
  Comparator #(.width(16)) comparator_7 (
    .a(Temps_Comu), .b(a4_rellotge_intern_1_hora_act_bin_16b), .eq(comparator_7_eq));  // open: gt, lt
  Demultiplexer #(.enable("true"), .select(3)) demultiplexer_1 (
    .out0(demultiplexer_1_out0), .out1(demultiplexer_1_out1), .out2(demultiplexer_1_out2),
    .out3(demultiplexer_1_out3), .in(1'b1), .sel(d_ff_6_q), .en(and_1_out));  // open: out4, out5, out6, out7
  D_Flip_Flop d_ff_9 (.D(1'b0), .clk(1'b0), .Q(d_ff_9_q), .preset(and_8_out), .reset(comparator_8_eq));  // open: Qn
  D_Flip_Flop d_ff_10 (.D(1'b0), .clk(1'b0), .Q(d_ff_10_q), .preset(and_9_out), .reset(comparator_9_eq));  // open: Qn
  D_Flip_Flop d_ff_11 (.D(1'b0), .clk(1'b0), .Q(d_ff_11_q), .preset(and_10_out), .reset(comparator_10_eq));  // open: Qn
  D_Flip_Flop d_ff_12 (.D(1'b0), .clk(1'b0), .Q(d_ff_12_q), .preset(and_11_out), .reset(comparator_11_eq));  // open: Qn
  or or_4 (LED_JI, demultiplexer_1_out0, d_ff_9_q);
  or or_5 (LED_JE, demultiplexer_1_out1, d_ff_10_q);
  or or_6 (LED_H, demultiplexer_1_out2, d_ff_11_q);
  or or_7 (LED_A, demultiplexer_1_out3, d_ff_12_q);
  _7_Segment_Display #(.active("false")) u_7_segment_display_7 (
    .g(a4_rellotge_intern_2_g6), .f(a4_rellotge_intern_2_f6), .a(a4_rellotge_intern_2_a6),
    .b(a4_rellotge_intern_2_b6), .e(a4_rellotge_intern_2_e6), .d(a4_rellotge_intern_2_d6),
    .c(a4_rellotge_intern_2_c6), .dp(a4_rellotge_intern_2_p6));
  _7_Segment_Display #(.active("false")) u_7_segment_display_8 (
    .g(a4_rellotge_intern_3_g6), .f(a4_rellotge_intern_3_f6), .a(a4_rellotge_intern_3_a6),
    .b(a4_rellotge_intern_3_b6), .e(a4_rellotge_intern_3_e6), .d(a4_rellotge_intern_3_d6),
    .c(a4_rellotge_intern_3_c6), .dp(a4_rellotge_intern_3_p6));
  _7_Segment_Display #(.active("false")) u_7_segment_display_9 (
    .g(a4_rellotge_intern_4_g6), .f(a4_rellotge_intern_4_f6), .a(a4_rellotge_intern_4_a6),
    .b(a4_rellotge_intern_4_b6), .e(a4_rellotge_intern_4_e6), .d(a4_rellotge_intern_4_d6),
    .c(a4_rellotge_intern_4_c6), .dp(a4_rellotge_intern_4_p6));
  _7_Segment_Display #(.active("false")) u_7_segment_display_10 (
    .g(a4_rellotge_intern_5_g6), .f(a4_rellotge_intern_5_f6), .a(a4_rellotge_intern_5_a6),
    .b(a4_rellotge_intern_5_b6), .e(a4_rellotge_intern_5_e6), .d(a4_rellotge_intern_5_d6),
    .c(a4_rellotge_intern_5_c6), .dp(a4_rellotge_intern_5_p6));
  _7_Segment_Display #(.active("false")) u_7_segment_display_11 (
    .g(a4_rellotge_intern_2_g5), .f(a4_rellotge_intern_2_f5), .a(a4_rellotge_intern_2_a5),
    .b(a4_rellotge_intern_2_b5), .e(a4_rellotge_intern_2_e5), .d(a4_rellotge_intern_2_d5),
    .c(a4_rellotge_intern_2_c5), .dp(a4_rellotge_intern_2_p5));
  _7_Segment_Display #(.active("false")) u_7_segment_display_12 (
    .g(a4_rellotge_intern_3_g5), .f(a4_rellotge_intern_3_f5), .a(a4_rellotge_intern_3_a5),
    .b(a4_rellotge_intern_3_b5), .e(a4_rellotge_intern_3_e5), .d(a4_rellotge_intern_3_d5),
    .c(a4_rellotge_intern_3_c5), .dp(a4_rellotge_intern_3_p5));
  _7_Segment_Display #(.active("false")) u_7_segment_display_13 (
    .g(a4_rellotge_intern_4_g5), .f(a4_rellotge_intern_4_f5), .a(a4_rellotge_intern_4_a5),
    .b(a4_rellotge_intern_4_b5), .e(a4_rellotge_intern_4_e5), .d(a4_rellotge_intern_4_d5),
    .c(a4_rellotge_intern_4_c5), .dp(a4_rellotge_intern_4_p5));
  _7_Segment_Display #(.active("false")) u_7_segment_display_14 (
    .g(a4_rellotge_intern_5_g5), .f(a4_rellotge_intern_5_f5), .a(a4_rellotge_intern_5_a5),
    .b(a4_rellotge_intern_5_b5), .e(a4_rellotge_intern_5_e5), .d(a4_rellotge_intern_5_d5),
    .c(a4_rellotge_intern_5_c5), .dp(a4_rellotge_intern_5_p5));
  _7_Segment_Display #(.active("false")) u_7_segment_display_15 (
    .g(a4_rellotge_intern_2_g4), .f(a4_rellotge_intern_2_f4), .a(a4_rellotge_intern_2_a4),
    .b(a4_rellotge_intern_2_b4), .e(a4_rellotge_intern_2_e4), .d(a4_rellotge_intern_2_d4),
    .c(a4_rellotge_intern_2_c4), .dp(a4_rellotge_intern_2_p4));
  _7_Segment_Display #(.active("false")) u_7_segment_display_16 (
    .g(a4_rellotge_intern_2_g3), .f(a4_rellotge_intern_2_f3), .a(a4_rellotge_intern_2_a3),
    .b(a4_rellotge_intern_2_b3), .e(a4_rellotge_intern_2_e3), .d(a4_rellotge_intern_2_d3),
    .c(a4_rellotge_intern_2_c3), .dp(a4_rellotge_intern_2_p3));
  _7_Segment_Display #(.active("false")) u_7_segment_display_17 (
    .g(a4_rellotge_intern_3_g4), .f(a4_rellotge_intern_3_f4), .a(a4_rellotge_intern_3_a4),
    .b(a4_rellotge_intern_3_b4), .e(a4_rellotge_intern_3_e4), .d(a4_rellotge_intern_3_d4),
    .c(a4_rellotge_intern_3_c4), .dp(a4_rellotge_intern_3_p4));
  _7_Segment_Display #(.active("false")) u_7_segment_display_18 (
    .g(a4_rellotge_intern_3_g3), .f(a4_rellotge_intern_3_f3), .a(a4_rellotge_intern_3_a3),
    .b(a4_rellotge_intern_3_b3), .e(a4_rellotge_intern_3_e3), .d(a4_rellotge_intern_3_d3),
    .c(a4_rellotge_intern_3_c3), .dp(a4_rellotge_intern_3_p3));
  _7_Segment_Display #(.active("false")) u_7_segment_display_19 (
    .g(a4_rellotge_intern_4_g4), .f(a4_rellotge_intern_4_f4), .a(a4_rellotge_intern_4_a4),
    .b(a4_rellotge_intern_4_b4), .e(a4_rellotge_intern_4_e4), .d(a4_rellotge_intern_4_d4),
    .c(a4_rellotge_intern_4_c4), .dp(a4_rellotge_intern_4_p4));
  _7_Segment_Display #(.active("false")) u_7_segment_display_20 (
    .g(a4_rellotge_intern_4_g3), .f(a4_rellotge_intern_4_f3), .a(a4_rellotge_intern_4_a3),
    .b(a4_rellotge_intern_4_b3), .e(a4_rellotge_intern_4_e3), .d(a4_rellotge_intern_4_d3),
    .c(a4_rellotge_intern_4_c3), .dp(a4_rellotge_intern_4_p3));
  _7_Segment_Display #(.active("false")) u_7_segment_display_21 (
    .g(a4_rellotge_intern_5_g4), .f(a4_rellotge_intern_5_f4), .a(a4_rellotge_intern_5_a4),
    .b(a4_rellotge_intern_5_b4), .e(a4_rellotge_intern_5_e4), .d(a4_rellotge_intern_5_d4),
    .c(a4_rellotge_intern_5_c4), .dp(a4_rellotge_intern_5_p4));
  _7_Segment_Display #(.active("false")) u_7_segment_display_22 (
    .g(a4_rellotge_intern_5_g3), .f(a4_rellotge_intern_5_f3), .a(a4_rellotge_intern_5_a3),
    .b(a4_rellotge_intern_5_b3), .e(a4_rellotge_intern_5_e3), .d(a4_rellotge_intern_5_d3),
    .c(a4_rellotge_intern_5_c3), .dp(a4_rellotge_intern_5_p3));
  or or_8 (Motor1, LED_JE, LED_JI);
  or or_9 (Motor2, LED_A, LED_H);
  _7_Segment_Display #(.active("false")) u_7_segment_display_23 (
    .g(a4_rellotge_intern_2_g2), .f(a4_rellotge_intern_2_f2), .a(a4_rellotge_intern_2_a2),
    .b(a4_rellotge_intern_2_b2), .e(a4_rellotge_intern_2_e2), .d(a4_rellotge_intern_2_d2),
    .c(a4_rellotge_intern_2_c2), .dp(a4_rellotge_intern_2_p2));
  _7_Segment_Display #(.active("false")) u_7_segment_display_24 (
    .g(a4_rellotge_intern_3_g2), .f(a4_rellotge_intern_3_f2), .a(a4_rellotge_intern_3_a2),
    .b(a4_rellotge_intern_3_b2), .e(a4_rellotge_intern_3_e2), .d(a4_rellotge_intern_3_d2),
    .c(a4_rellotge_intern_3_c2), .dp(a4_rellotge_intern_3_p2));
  _7_Segment_Display #(.active("false")) u_7_segment_display_25 (
    .g(a4_rellotge_intern_4_g2), .f(a4_rellotge_intern_4_f2), .a(a4_rellotge_intern_4_a2),
    .b(a4_rellotge_intern_4_b2), .e(a4_rellotge_intern_4_e2), .d(a4_rellotge_intern_4_d2),
    .c(a4_rellotge_intern_4_c2), .dp(a4_rellotge_intern_4_p2));
  _7_Segment_Display #(.active("false")) u_7_segment_display_26 (
    .g(a4_rellotge_intern_5_g2), .f(a4_rellotge_intern_5_f2), .a(a4_rellotge_intern_5_a2),
    .b(a4_rellotge_intern_5_b2), .e(a4_rellotge_intern_5_e2), .d(a4_rellotge_intern_5_d2),
    .c(a4_rellotge_intern_5_c2), .dp(a4_rellotge_intern_5_p2));
  _7_Segment_Display #(.active("false")) u_7_segment_display_27 (
    .g(a4_rellotge_intern_2_g1), .f(a4_rellotge_intern_2_f1), .a(a4_rellotge_intern_2_a1),
    .b(a4_rellotge_intern_2_b1), .e(a4_rellotge_intern_2_e1), .d(a4_rellotge_intern_2_d1),
    .c(a4_rellotge_intern_2_c1), .dp(a4_rellotge_intern_2_p1));
  A4_Rellotge_Intern a4_rellotge_intern_2 (
    .Power(d_ff_9_q), .RESET(not_7_out), .E4(a4_rellotge_intern_2_e4), .F4(a4_rellotge_intern_2_f4),
    .G4(a4_rellotge_intern_2_g4), .P4(a4_rellotge_intern_2_p4), .A3(a4_rellotge_intern_2_a3),
    .B3(a4_rellotge_intern_2_b3), .C3(a4_rellotge_intern_2_c3), .D3(a4_rellotge_intern_2_d3),
    .E3(a4_rellotge_intern_2_e3), .F3(a4_rellotge_intern_2_f3), .G3(a4_rellotge_intern_2_g3),
    .p3(a4_rellotge_intern_2_p3), .A2(a4_rellotge_intern_2_a2), .B2(a4_rellotge_intern_2_b2),
    .C2(a4_rellotge_intern_2_c2), .D2(a4_rellotge_intern_2_d2), .E2(a4_rellotge_intern_2_e2),
    .F2(a4_rellotge_intern_2_f2), .G2(a4_rellotge_intern_2_g2), .P2(a4_rellotge_intern_2_p2),
    .A1(a4_rellotge_intern_2_a1), .B1(a4_rellotge_intern_2_b1), .C1(a4_rellotge_intern_2_c1),
    .D1(a4_rellotge_intern_2_d1), .E1(a4_rellotge_intern_2_e1), .F1(a4_rellotge_intern_2_f1),
    .G1(a4_rellotge_intern_2_g1), .P1(a4_rellotge_intern_2_p1), .A6(a4_rellotge_intern_2_a6),
    .B6(a4_rellotge_intern_2_b6), .C6(a4_rellotge_intern_2_c6), .D6(a4_rellotge_intern_2_d6),
    .E6(a4_rellotge_intern_2_e6), .F6(a4_rellotge_intern_2_f6), .G6(a4_rellotge_intern_2_g6),
    .P6(a4_rellotge_intern_2_p6), .A5(a4_rellotge_intern_2_a5), .B5(a4_rellotge_intern_2_b5),
    .C5(a4_rellotge_intern_2_c5), .D5(a4_rellotge_intern_2_d5), .E5(a4_rellotge_intern_2_e5),
    .F5(a4_rellotge_intern_2_f5), .G5(a4_rellotge_intern_2_g5), .P5(a4_rellotge_intern_2_p5),
    .A4(a4_rellotge_intern_2_a4), .Hora_Act_Bin_16B(a4_rellotge_intern_2_hora_act_bin_16b),
    .B4(a4_rellotge_intern_2_b4), .C4(a4_rellotge_intern_2_c4), .D4(a4_rellotge_intern_2_d4));  // open: Entrada_Manual_M, Entrada_manual_H
  _7_Segment_Display #(.active("false")) u_7_segment_display_28 (
    .g(a4_rellotge_intern_3_g1), .f(a4_rellotge_intern_3_f1), .a(a4_rellotge_intern_3_a1),
    .b(a4_rellotge_intern_3_b1), .e(a4_rellotge_intern_3_e1), .d(a4_rellotge_intern_3_d1),
    .c(a4_rellotge_intern_3_c1), .dp(a4_rellotge_intern_3_p1));
  A4_Rellotge_Intern a4_rellotge_intern_3 (
    .Power(d_ff_10_q), .RESET(not_7_out), .E4(a4_rellotge_intern_3_e4), .F4(a4_rellotge_intern_3_f4),
    .G4(a4_rellotge_intern_3_g4), .P4(a4_rellotge_intern_3_p4), .A3(a4_rellotge_intern_3_a3),
    .B3(a4_rellotge_intern_3_b3), .C3(a4_rellotge_intern_3_c3), .D3(a4_rellotge_intern_3_d3),
    .E3(a4_rellotge_intern_3_e3), .F3(a4_rellotge_intern_3_f3), .G3(a4_rellotge_intern_3_g3),
    .p3(a4_rellotge_intern_3_p3), .A2(a4_rellotge_intern_3_a2), .B2(a4_rellotge_intern_3_b2),
    .C2(a4_rellotge_intern_3_c2), .D2(a4_rellotge_intern_3_d2), .E2(a4_rellotge_intern_3_e2),
    .F2(a4_rellotge_intern_3_f2), .G2(a4_rellotge_intern_3_g2), .P2(a4_rellotge_intern_3_p2),
    .A1(a4_rellotge_intern_3_a1), .B1(a4_rellotge_intern_3_b1), .C1(a4_rellotge_intern_3_c1),
    .D1(a4_rellotge_intern_3_d1), .E1(a4_rellotge_intern_3_e1), .F1(a4_rellotge_intern_3_f1),
    .G1(a4_rellotge_intern_3_g1), .P1(a4_rellotge_intern_3_p1), .A6(a4_rellotge_intern_3_a6),
    .B6(a4_rellotge_intern_3_b6), .C6(a4_rellotge_intern_3_c6), .D6(a4_rellotge_intern_3_d6),
    .E6(a4_rellotge_intern_3_e6), .F6(a4_rellotge_intern_3_f6), .G6(a4_rellotge_intern_3_g6),
    .P6(a4_rellotge_intern_3_p6), .A5(a4_rellotge_intern_3_a5), .B5(a4_rellotge_intern_3_b5),
    .C5(a4_rellotge_intern_3_c5), .D5(a4_rellotge_intern_3_d5), .E5(a4_rellotge_intern_3_e5),
    .F5(a4_rellotge_intern_3_f5), .G5(a4_rellotge_intern_3_g5), .P5(a4_rellotge_intern_3_p5),
    .A4(a4_rellotge_intern_3_a4), .Hora_Act_Bin_16B(a4_rellotge_intern_3_hora_act_bin_16b),
    .B4(a4_rellotge_intern_3_b4), .C4(a4_rellotge_intern_3_c4), .D4(a4_rellotge_intern_3_d4));  // open: Entrada_Manual_M, Entrada_manual_H
  _7_Segment_Display #(.active("false")) u_7_segment_display_29 (
    .g(a4_rellotge_intern_4_g1), .f(a4_rellotge_intern_4_f1), .a(a4_rellotge_intern_4_a1),
    .b(a4_rellotge_intern_4_b1), .e(a4_rellotge_intern_4_e1), .d(a4_rellotge_intern_4_d1),
    .c(a4_rellotge_intern_4_c1), .dp(a4_rellotge_intern_4_p1));
  _7_Segment_Display #(.active("false")) u_7_segment_display_30 (
    .g(a4_rellotge_intern_5_g1), .f(a4_rellotge_intern_5_f1), .a(a4_rellotge_intern_5_a1),
    .b(a4_rellotge_intern_5_b1), .e(a4_rellotge_intern_5_e1), .d(a4_rellotge_intern_5_d1),
    .c(a4_rellotge_intern_5_c1), .dp(a4_rellotge_intern_5_p1));
  A4_Rellotge_Intern a4_rellotge_intern_4 (
    .Power(d_ff_11_q), .RESET(not_7_out), .E4(a4_rellotge_intern_4_e4), .F4(a4_rellotge_intern_4_f4),
    .G4(a4_rellotge_intern_4_g4), .P4(a4_rellotge_intern_4_p4), .A3(a4_rellotge_intern_4_a3),
    .B3(a4_rellotge_intern_4_b3), .C3(a4_rellotge_intern_4_c3), .D3(a4_rellotge_intern_4_d3),
    .E3(a4_rellotge_intern_4_e3), .F3(a4_rellotge_intern_4_f3), .G3(a4_rellotge_intern_4_g3),
    .p3(a4_rellotge_intern_4_p3), .A2(a4_rellotge_intern_4_a2), .B2(a4_rellotge_intern_4_b2),
    .C2(a4_rellotge_intern_4_c2), .D2(a4_rellotge_intern_4_d2), .E2(a4_rellotge_intern_4_e2),
    .F2(a4_rellotge_intern_4_f2), .G2(a4_rellotge_intern_4_g2), .P2(a4_rellotge_intern_4_p2),
    .A1(a4_rellotge_intern_4_a1), .B1(a4_rellotge_intern_4_b1), .C1(a4_rellotge_intern_4_c1),
    .D1(a4_rellotge_intern_4_d1), .E1(a4_rellotge_intern_4_e1), .F1(a4_rellotge_intern_4_f1),
    .G1(a4_rellotge_intern_4_g1), .P1(a4_rellotge_intern_4_p1), .A6(a4_rellotge_intern_4_a6),
    .B6(a4_rellotge_intern_4_b6), .C6(a4_rellotge_intern_4_c6), .D6(a4_rellotge_intern_4_d6),
    .E6(a4_rellotge_intern_4_e6), .F6(a4_rellotge_intern_4_f6), .G6(a4_rellotge_intern_4_g6),
    .P6(a4_rellotge_intern_4_p6), .A5(a4_rellotge_intern_4_a5), .B5(a4_rellotge_intern_4_b5),
    .C5(a4_rellotge_intern_4_c5), .D5(a4_rellotge_intern_4_d5), .E5(a4_rellotge_intern_4_e5),
    .F5(a4_rellotge_intern_4_f5), .G5(a4_rellotge_intern_4_g5), .P5(a4_rellotge_intern_4_p5),
    .A4(a4_rellotge_intern_4_a4), .Hora_Act_Bin_16B(a4_rellotge_intern_4_hora_act_bin_16b),
    .B4(a4_rellotge_intern_4_b4), .C4(a4_rellotge_intern_4_c4), .D4(a4_rellotge_intern_4_d4));  // open: Entrada_Manual_M, Entrada_manual_H
  A4_Rellotge_Intern a4_rellotge_intern_5 (
    .Power(d_ff_12_q), .RESET(not_7_out), .E4(a4_rellotge_intern_5_e4), .F4(a4_rellotge_intern_5_f4),
    .G4(a4_rellotge_intern_5_g4), .P4(a4_rellotge_intern_5_p4), .A3(a4_rellotge_intern_5_a3),
    .B3(a4_rellotge_intern_5_b3), .C3(a4_rellotge_intern_5_c3), .D3(a4_rellotge_intern_5_d3),
    .E3(a4_rellotge_intern_5_e3), .F3(a4_rellotge_intern_5_f3), .G3(a4_rellotge_intern_5_g3),
    .p3(a4_rellotge_intern_5_p3), .A2(a4_rellotge_intern_5_a2), .B2(a4_rellotge_intern_5_b2),
    .C2(a4_rellotge_intern_5_c2), .D2(a4_rellotge_intern_5_d2), .E2(a4_rellotge_intern_5_e2),
    .F2(a4_rellotge_intern_5_f2), .G2(a4_rellotge_intern_5_g2), .P2(a4_rellotge_intern_5_p2),
    .A1(a4_rellotge_intern_5_a1), .B1(a4_rellotge_intern_5_b1), .C1(a4_rellotge_intern_5_c1),
    .D1(a4_rellotge_intern_5_d1), .E1(a4_rellotge_intern_5_e1), .F1(a4_rellotge_intern_5_f1),
    .G1(a4_rellotge_intern_5_g1), .P1(a4_rellotge_intern_5_p1), .A6(a4_rellotge_intern_5_a6),
    .B6(a4_rellotge_intern_5_b6), .C6(a4_rellotge_intern_5_c6), .D6(a4_rellotge_intern_5_d6),
    .E6(a4_rellotge_intern_5_e6), .F6(a4_rellotge_intern_5_f6), .G6(a4_rellotge_intern_5_g6),
    .P6(a4_rellotge_intern_5_p6), .A5(a4_rellotge_intern_5_a5), .B5(a4_rellotge_intern_5_b5),
    .C5(a4_rellotge_intern_5_c5), .D5(a4_rellotge_intern_5_d5), .E5(a4_rellotge_intern_5_e5),
    .F5(a4_rellotge_intern_5_f5), .G5(a4_rellotge_intern_5_g5), .P5(a4_rellotge_intern_5_p5),
    .A4(a4_rellotge_intern_5_a4), .Hora_Act_Bin_16B(a4_rellotge_intern_5_hora_act_bin_16b),
    .B4(a4_rellotge_intern_5_b4), .C4(a4_rellotge_intern_5_c4), .D4(a4_rellotge_intern_5_d4));  // open: Entrada_Manual_M, Entrada_manual_H
  Comparator #(.width(16)) comparator_8 (
    .a(Temps_JI), .b(a4_rellotge_intern_2_hora_act_bin_16b), .eq(comparator_8_eq));  // open: gt, lt
  Comparator #(.width(16)) comparator_9 (
    .a(Temps_JE), .b(a4_rellotge_intern_3_hora_act_bin_16b), .eq(comparator_9_eq));  // open: gt, lt
  Comparator #(.width(16)) comparator_10 (
    .a(Temps_H), .b(a4_rellotge_intern_4_hora_act_bin_16b), .eq(comparator_10_eq));  // open: gt, lt
  Comparator #(.width(16)) comparator_11 (
    .a(Temps_A), .b(a4_rellotge_intern_5_hora_act_bin_16b), .eq(comparator_11_eq));  // open: gt, lt
  Multiplexer #(.width(16)) multiplexer_1 (.in0(Temps_JI), .in1(Temps_Comu), .out(TJICR), .sel(and_6_out));
  Multiplexer #(.width(16)) multiplexer_2 (
    .in0(a4_rellotge_intern_2_hora_act_bin_16b), .in1(a4_rellotge_intern_1_hora_act_bin_16b), .out(CRJI),
    .sel(and_6_out));
  Multiplexer #(.width(16)) multiplexer_3 (.in0(Temps_JE), .in1(Temps_Comu), .out(TJECR), .sel(and_6_out));
  Multiplexer #(.width(16)) multiplexer_4 (
    .in0(a4_rellotge_intern_3_hora_act_bin_16b), .in1(a4_rellotge_intern_1_hora_act_bin_16b), .out(CRJE),
    .sel(and_6_out));
  Multiplexer #(.width(16)) multiplexer_5 (.in0(Temps_H), .in1(Temps_Comu), .out(THCR), .sel(and_6_out));
  Multiplexer #(.width(16)) multiplexer_6 (
    .in0(a4_rellotge_intern_4_hora_act_bin_16b), .in1(a4_rellotge_intern_1_hora_act_bin_16b), .out(CRH),
    .sel(and_6_out));
  Multiplexer #(.width(16)) multiplexer_7 (.in0(Temps_A), .in1(Temps_Comu), .out(TACR), .sel(and_6_out));
  Multiplexer #(.width(16)) multiplexer_8 (
    .in0(a4_rellotge_intern_5_hora_act_bin_16b), .in1(a4_rellotge_intern_1_hora_act_bin_16b), .out(CRA),
    .sel(and_6_out));

  assign V1 = LED_JI;
  assign V2 = LED_JE;
  assign V3 = LED_H;
  assign V4 = LED_A;

  // Notes on the sheet:
  //   MODO AUTO
  //   Activador SIS Reg JI
  //   Activador SIS Reg JE
  //   Activador SIS Reg Hort
  //   Activador SIS Reg Arbres
  //   MODO PROGRAMADO
  //   ACTIVACIONS I NOTIFICACIÓNS
  //   CRONOMETRES
endmodule

module A7_CL74LS90 (
  input  R9_1,
  input  R9_2,
  input  Input_A,
  input  Input_B,
  input  R01,
  input  R02,
  output QA,
  output QB,
  output QC,
  output QD
);

  wire and_1_out, j_k_ff_4_qn, nand_1_out, nand_2_out, not_1_out, not_2_out, not_3_out, not_4_out, or_1_out,
       or_2_out;

  nand nand_1 (nand_1_out, R9_1, R9_2);
  nand nand_2 (nand_2_out, R01, R02);
  not not_1 (not_1_out, nand_1_out);
  J_K_Flip_Flop #(.trigger("falling")) j_k_ff_1 (
    .J(1'b1), .K(1'b1), .clk(Input_A), .Q(QA), .preset(not_1_out), .reset(not_2_out));  // open: Qn
  not not_2 (not_2_out, nand_2_out);
  J_K_Flip_Flop #(.trigger("falling")) j_k_ff_2 (
    .J(j_k_ff_4_qn), .K(1'b1), .clk(Input_B), .Q(QB), .reset(or_1_out));  // open: Qn, preset
  or or_1 (or_1_out, ~nand_2_out, ~nand_1_out);  // OR_Gate
  J_K_Flip_Flop #(.trigger("falling")) j_k_ff_3 (
    .J(1'b1), .K(1'b1), .clk(QB), .Q(QC), .reset(or_2_out));  // open: Qn, preset
  or or_2 (or_2_out, ~nand_2_out, ~nand_1_out);  // OR_Gate
  not not_3 (not_3_out, nand_1_out);
  J_K_Flip_Flop #(.trigger("falling")) j_k_ff_4 (
    .J(and_1_out), .K(QD), .clk(Input_B), .Q(QD), .Qn(j_k_ff_4_qn), .preset(not_3_out), .reset(not_4_out));
  and and_1 (and_1_out, QC, QB);
  not not_4 (not_4_out, nand_2_out);
endmodule

module B0_CTRL_Temperatura (
  input  Mes,
  input  Menys,
  input  Mode,
  input  [7:0] Display_Bits,
  input  ON_OFF_SIS,
  output A3,
  output B3,
  output C3,
  output D3,
  output E3,
  output F3,
  output G3,
  output A2,
  output B2,
  output C2,
  output D2,
  output E2,
  output F2,
  output G2,
  output A1,
  output B1,
  output C1,
  output D1,
  output E1,
  output F1,
  output G1,
  output [7:0] Sort_Temp,
  output P3,
  output P2,
  output P1
);

  wire and_1_out, and_2_out, and_3_out, and_4_out, and_5_out, clock_1_out, comparator_1_lt, d_ff_1_q,
       d_ff_1_qn, d_ff_2_q, not_1_out, not_2_out, not_3_out, or_1_out, or_2_out, or_3_out, subtractor_1_bout;
  wire [1:0] multiplexer_2_out;
  wire [3:0] b3_algoritme_double_dabble_1_sg0, b3_algoritme_double_dabble_1_sg1;
  wire [7:0] adder_1_out, multiplexer_1_out, multiplexer_3_out, subtractor_1_out;

  Clock clock_1 (.out(clock_1_out));
  not not_1 (not_1_out, Mode);
  and and_1 (and_1_out, Mode, clock_1_out, ON_OFF_SIS);
  and and_2 (and_2_out, not_1_out, clock_1_out);
  D_Flip_Flop #(.trigger("falling")) d_ff_1 (
    .D(d_ff_1_qn), .clk(or_1_out), .Q(d_ff_1_q), .Qn(d_ff_1_qn));  // open: preset, reset
  or or_1 (or_1_out, and_1_out, and_2_out);
  and and_3 (and_3_out, comparator_1_lt, Mes);
  and and_4 (and_4_out, Menys, not_2_out);
  or or_2 (or_2_out, and_3_out, and_4_out);
  not not_2 (not_2_out, subtractor_1_bout);
  D_Flip_Flop #(.trigger("falling")) d_ff_2 (.Q(d_ff_2_q), .preset(d_ff_1_q));  // open: D, clk, Qn, reset
  Comparator comparator_1 (.a(Sort_Temp), .b(8'h1e), .lt(comparator_1_lt));  // open: gt, eq
  Adder adder_1 (.a(Sort_Temp), .b(8'h1), .out(adder_1_out));  // open: cin, cout
  Subtractor subtractor_1 (.a(Sort_Temp), .b(8'h1), .out(subtractor_1_out), .bout(subtractor_1_bout));  // open: bin
  not not_3 (not_3_out, d_ff_2_q);
  Multiplexer #(.width(8)) multiplexer_1 (.in0(8'h15), .in1(Display_Bits), .out(multiplexer_1_out), .sel(Mode));
  Multiplexer #(.width(2)) multiplexer_2 (.in0({Menys, Mes}), .in1(2'b11), .out(multiplexer_2_out), .sel(not_3_out));
  Multiplexer #(.select(2), .width(8)) multiplexer_3 (
    .in0(Sort_Temp), .in1(adder_1_out), .in2(subtractor_1_out), .in3(multiplexer_1_out),
    .out(multiplexer_3_out), .sel(multiplexer_2_out));
  and and_5 (and_5_out, or_1_out, not_3_out);
  Register #(.trigger("falling")) register_1 (.D(multiplexer_3_out), .clk(or_3_out), .Q(Sort_Temp));  // open: en, clr
  or or_3 (or_3_out, or_2_out, and_5_out);
  B3_Algoritme_Double_Dabble b3_algoritme_double_dabble_1 (
    .Entrada(Sort_Temp), .SG1(b3_algoritme_double_dabble_1_sg1), .SG0(b3_algoritme_double_dabble_1_sg0));  // open: SG2
  _7447 #(.ShowInternalStructure("true")) u_7447_1 (
    .pin1(b3_algoritme_double_dabble_1_sg1[1]), .pin2(b3_algoritme_double_dabble_1_sg1[2]), .pin3(B1),
    .pin5(B1), .pin6(b3_algoritme_double_dabble_1_sg1[3]), .pin7(b3_algoritme_double_dabble_1_sg1[0]),
    .pin15(F3), .pin14(G3), .pin13(A3), .pin12(B3), .pin11(C3), .pin10(D3), .pin9(E3));  // open: pin4
  _7_Segment_Display #(.active("false")) u_7_segment_display_1 (
    .g(G3), .f(F3), .a(A3), .b(B3), .e(E3), .d(D3), .c(C3), .dp(B1));
  _7447 #(.ShowInternalStructure("true")) u_7447_2 (
    .pin1(b3_algoritme_double_dabble_1_sg0[1]), .pin2(b3_algoritme_double_dabble_1_sg0[2]), .pin3(B1),
    .pin4(B1), .pin5(B1), .pin6(b3_algoritme_double_dabble_1_sg0[3]),
    .pin7(b3_algoritme_double_dabble_1_sg0[0]), .pin15(F2), .pin14(G2), .pin13(A2), .pin12(B2), .pin11(C2),
    .pin10(D2), .pin9(E2));
  _7_Segment_Display #(.active("false")) u_7_segment_display_2 (
    .g(G2), .f(F2), .a(A2), .b(B2), .e(E2), .d(D2), .c(C2), .dp(B1));
  not not_4 (A1, B1);
  _7_Segment_Display #(.active("false")) u_7_segment_display_3 (
    .g(B1), .f(A1), .a(A1), .b(B1), .e(A1), .d(A1), .c(B1), .dp(B1));

  assign C1 = B1;
  assign D1 = A1;
  assign E1 = A1;
  assign F1 = A1;
  assign G1 = B1;
  assign P1 = B1;
  assign P2 = A1;
  assign P3 = B1;
  // also tied to VCC on the sheet: B1

  // Notes on the sheet:
  //   Comportament (Entrada o sortida)
  //   (valor màxim)
  //   (valor inicial)
  //   7 SEGMENTOS ACTIVOS A BAJA
endmodule

module B2_CTRL_HumetatRelativa (
  input  Mes,
  input  Menys,
  input  Mode,
  input  [7:0] Display_Bits,
  input  ON_OFF_SIS,
  output A3,
  output B3,
  output C3,
  output D3,
  output E3,
  output F3,
  output G3,
  output A1,
  output B1,
  output C1,
  output D1,
  output E1,
  output F1,
  output G1,
  output A2,
  output B2,
  output C2,
  output D2,
  output E2,
  output F2,
  output G2,
  output [7:0] Sort_Temp,
  output P3,
  output P1,
  output P2
);

  wire and_1_out, and_2_out, and_3_out, and_4_out, and_5_out, clock_1_out, comparator_1_lt, d_ff_1_q,
       d_ff_1_qn, d_ff_2_q, not_1_out, not_2_out, not_3_out, or_1_out, or_2_out, or_3_out, subtractor_1_bout;
  wire [1:0] multiplexer_2_out;
  wire [3:0] b3_algoritme_double_dabble_1_sg0, b3_algoritme_double_dabble_1_sg1,
       b3_algoritme_double_dabble_1_sg2;
  wire [7:0] adder_1_out, multiplexer_1_out, multiplexer_3_out, subtractor_1_out;

  Clock clock_1 (.out(clock_1_out));
  not not_1 (not_1_out, Mode);
  and and_1 (and_1_out, Mode, clock_1_out, ON_OFF_SIS);
  and and_2 (and_2_out, not_1_out, clock_1_out);
  D_Flip_Flop #(.trigger("falling")) d_ff_1 (
    .D(d_ff_1_qn), .clk(or_1_out), .Q(d_ff_1_q), .Qn(d_ff_1_qn));  // open: preset, reset
  or or_1 (or_1_out, and_1_out, and_2_out);
  and and_3 (and_3_out, comparator_1_lt, Mes);
  and and_4 (and_4_out, Menys, not_2_out);
  or or_2 (or_2_out, and_3_out, and_4_out);
  not not_2 (not_2_out, subtractor_1_bout);
  D_Flip_Flop #(.trigger("falling")) d_ff_2 (.Q(d_ff_2_q), .preset(d_ff_1_q));  // open: D, clk, Qn, reset
  Comparator comparator_1 (.a(Sort_Temp), .b(8'h64), .lt(comparator_1_lt));  // open: gt, eq
  Adder adder_1 (.a(Sort_Temp), .b(8'h1), .out(adder_1_out));  // open: cin, cout
  Subtractor subtractor_1 (.a(Sort_Temp), .b(8'h1), .out(subtractor_1_out), .bout(subtractor_1_bout));  // open: bin
  not not_3 (not_3_out, d_ff_2_q);
  Multiplexer #(.width(8)) multiplexer_1 (.in0(8'h32), .in1(Display_Bits), .out(multiplexer_1_out), .sel(Mode));
  Multiplexer #(.width(2)) multiplexer_2 (.in0({Menys, Mes}), .in1(2'b11), .out(multiplexer_2_out), .sel(not_3_out));
  Multiplexer #(.select(2), .width(8)) multiplexer_3 (
    .in0(Sort_Temp), .in1(adder_1_out), .in2(subtractor_1_out), .in3(multiplexer_1_out),
    .out(multiplexer_3_out), .sel(multiplexer_2_out));
  and and_5 (and_5_out, or_1_out, not_3_out);
  Register #(.trigger("falling")) register_1 (.D(multiplexer_3_out), .clk(or_3_out), .Q(Sort_Temp));  // open: en, clr
  or or_3 (or_3_out, or_2_out, and_5_out);
  B3_Algoritme_Double_Dabble b3_algoritme_double_dabble_1 (
    .Entrada(Sort_Temp), .SG2(b3_algoritme_double_dabble_1_sg2), .SG1(b3_algoritme_double_dabble_1_sg1),
    .SG0(b3_algoritme_double_dabble_1_sg0));
  _7447 #(.ShowInternalStructure("true")) u_7447_1 (
    .pin1(b3_algoritme_double_dabble_1_sg2[1]), .pin2(b3_algoritme_double_dabble_1_sg2[2]), .pin3(P1),
    .pin5(P1), .pin6(b3_algoritme_double_dabble_1_sg2[3]), .pin7(b3_algoritme_double_dabble_1_sg2[0]),
    .pin15(F3), .pin14(G3), .pin13(A3), .pin12(B3), .pin11(C3), .pin10(D3), .pin9(E3));  // open: pin4
  _7_Segment_Display #(.active("false")) u_7_segment_display_1 (
    .g(G3), .f(F3), .a(A3), .b(B3), .e(E3), .d(D3), .c(C3), .dp(P1));
  _7447 #(.ShowInternalStructure("true")) u_7447_2 (
    .pin1(b3_algoritme_double_dabble_1_sg1[1]), .pin2(b3_algoritme_double_dabble_1_sg1[2]), .pin3(P1),
    .pin4(P1), .pin5(P1), .pin6(b3_algoritme_double_dabble_1_sg1[3]),
    .pin7(b3_algoritme_double_dabble_1_sg1[0]), .pin15(F2), .pin14(G2), .pin13(A2), .pin12(B2), .pin11(C2),
    .pin10(D2), .pin9(E2));
  _7_Segment_Display #(.active("false")) u_7_segment_display_2 (
    .g(G2), .f(F2), .a(A2), .b(B2), .e(E2), .d(D2), .c(C2), .dp(P1));
  _7447 #(.ShowInternalStructure("true")) u_7447_3 (
    .pin1(b3_algoritme_double_dabble_1_sg0[1]), .pin2(b3_algoritme_double_dabble_1_sg0[2]), .pin3(P1),
    .pin4(P1), .pin5(P1), .pin6(b3_algoritme_double_dabble_1_sg0[3]),
    .pin7(b3_algoritme_double_dabble_1_sg0[0]), .pin15(F1), .pin14(G1), .pin13(A1), .pin12(B1), .pin11(C1),
    .pin10(D1), .pin9(E1));
  _7_Segment_Display #(.active("false")) u_7_segment_display_3 (
    .g(G1), .f(F1), .a(A1), .b(B1), .e(E1), .d(D1), .c(C1), .dp(P1));

  assign P2 = P1;
  assign P3 = P1;
  // also tied to VCC on the sheet: P1

  // Notes on the sheet:
  //   Comportament (Entrada o sortida)
  //   (valor màxim)
  //   (valor inicial)
endmodule

module B2_Mates_Double_Dabble (
  input  A3,
  input  A2,
  input  A1,
  input  A0,
  output Q3,
  output Q2,
  output Q1,
  output Q0
);

  wire adder_1_cout, and_1_out, and_2_out, and_3_out, not_1_out, or_1_out, or_2_out, xor_2_out;

  or or_1 (or_1_out, A1, A0);
  and and_1 (and_1_out, A2, or_1_out);
  or or_2 (or_2_out, A3, and_1_out);
  xor xor_1 (Q0, or_2_out, A0);
  and and_2 (and_2_out, or_2_out, Q0);
  not not_1 (not_1_out, A1);
  and and_3 (and_3_out, not_1_out, and_2_out);
  xor xor_2 (xor_2_out, or_2_out, and_3_out);
  xor xor_3 (Q1, and_2_out, A1);
  Adder #(.width(1)) adder_1 (.a(A2), .b(xor_2_out), .out(Q2), .cout(adder_1_cout));  // open: cin
  xor xor_4 (Q3, A3, adder_1_cout);
endmodule

module B3_Algoritme_Double_Dabble (
  input  [7:0] Entrada,
  output [3:0] SG2,
  output [3:0] SG1,
  output [3:0] SG0
);

  wire b2_mates_double_dabble_1_q0, b2_mates_double_dabble_1_q1, b2_mates_double_dabble_1_q2,
       b2_mates_double_dabble_1_q3, b2_mates_double_dabble_2_q0, b2_mates_double_dabble_2_q1,
       b2_mates_double_dabble_2_q2, b2_mates_double_dabble_2_q3, b2_mates_double_dabble_3_q0,
       b2_mates_double_dabble_3_q1, b2_mates_double_dabble_3_q2, b2_mates_double_dabble_3_q3,
       b2_mates_double_dabble_4_q0, b2_mates_double_dabble_4_q1, b2_mates_double_dabble_4_q2,
       b2_mates_double_dabble_4_q3, b2_mates_double_dabble_5_q0, b2_mates_double_dabble_5_q1,
       b2_mates_double_dabble_5_q2;

  B2_Mates_Double_Dabble b2_mates_double_dabble_1 (
    .A3(1'b0), .A2(Entrada[7]), .A1(Entrada[6]), .A0(Entrada[5]), .Q3(b2_mates_double_dabble_1_q3),
    .Q2(b2_mates_double_dabble_1_q2), .Q1(b2_mates_double_dabble_1_q1), .Q0(b2_mates_double_dabble_1_q0));
  B2_Mates_Double_Dabble b2_mates_double_dabble_2 (
    .A3(b2_mates_double_dabble_1_q2), .A2(b2_mates_double_dabble_1_q1), .A1(b2_mates_double_dabble_1_q0),
    .A0(Entrada[4]), .Q3(b2_mates_double_dabble_2_q3), .Q2(b2_mates_double_dabble_2_q2),
    .Q1(b2_mates_double_dabble_2_q1), .Q0(b2_mates_double_dabble_2_q0));
  B2_Mates_Double_Dabble b2_mates_double_dabble_3 (
    .A3(b2_mates_double_dabble_2_q2), .A2(b2_mates_double_dabble_2_q1), .A1(b2_mates_double_dabble_2_q0),
    .A0(Entrada[3]), .Q3(b2_mates_double_dabble_3_q3), .Q2(b2_mates_double_dabble_3_q2),
    .Q1(b2_mates_double_dabble_3_q1), .Q0(b2_mates_double_dabble_3_q0));
  B2_Mates_Double_Dabble b2_mates_double_dabble_4 (
    .A3(b2_mates_double_dabble_3_q2), .A2(b2_mates_double_dabble_3_q1), .A1(b2_mates_double_dabble_3_q0),
    .A0(Entrada[2]), .Q3(b2_mates_double_dabble_4_q3), .Q2(b2_mates_double_dabble_4_q2),
    .Q1(b2_mates_double_dabble_4_q1), .Q0(b2_mates_double_dabble_4_q0));
  B2_Mates_Double_Dabble b2_mates_double_dabble_5 (
    .A3(1'b0), .A2(b2_mates_double_dabble_1_q3), .A1(b2_mates_double_dabble_2_q3),
    .A0(b2_mates_double_dabble_3_q3), .Q3(SG2[1]), .Q2(b2_mates_double_dabble_5_q2),
    .Q1(b2_mates_double_dabble_5_q1), .Q0(b2_mates_double_dabble_5_q0));
  B2_Mates_Double_Dabble b2_mates_double_dabble_6 (
    .A3(b2_mates_double_dabble_5_q2), .A2(b2_mates_double_dabble_5_q1), .A1(b2_mates_double_dabble_5_q0),
    .A0(b2_mates_double_dabble_4_q3), .Q3(SG2[0]), .Q2(SG1[3]), .Q1(SG1[2]), .Q0(SG1[1]));
  B2_Mates_Double_Dabble b2_mates_double_dabble_7 (
    .A3(b2_mates_double_dabble_4_q2), .A2(b2_mates_double_dabble_4_q1), .A1(b2_mates_double_dabble_4_q0),
    .A0(Entrada[1]), .Q3(SG1[0]), .Q2(SG0[3]), .Q1(SG0[2]), .Q0(SG0[1]));

  assign SG0[0] = Entrada[0];
  assign SG2[3:2] = 2'b00;
endmodule

module B4_Logica_Control (
  input  ON_OFF_ENT,
  input  Avaria_MQ_Temp,
  input  Avaria_SEN_Temp,
  input  [7:0] Temperatura_Prog,
  input  [7:0] Temperatura_Real,
  input  Avaria_MQ_Hum,
  input  Avaria_SENS_Hum,
  input  [7:0] Humetat_Programada,
  input  [7:0] Humetat_Real,
  output ON_OFF_SORT,
  output LED_3S,
  output Mes_Temp,
  output Aire_Calent,
  output Aire_Fred,
  output Menys_Temp,
  output Mes_Hum,
  output Humidificador,
  output Deshumi,
  output Menys_Hum
);

  wire and_1_out, and_2_out, and_3_out, and_4_out, and_5_out, and_6_out, and_7_out, and_8_out, button_1_out,
       button_2_out, CLK_out, comparator_1_gt, comparator_1_lt, comparator_2_gt, comparator_2_lt, d_ff_1_qn,
       d_ff_2_q, d_ff_2_qn, d_ff_3_q, d_ff_3_qn, not_1_out, not_2_out, not_3_out, not_4_out, not_5_out,
       or_1_out;

  D_Flip_Flop d_ff_1 (.D(d_ff_1_qn), .clk(ON_OFF_ENT), .Q(ON_OFF_SORT), .Qn(d_ff_1_qn));  // open: preset, reset
  Clock CLK (.out(CLK_out));
  not not_1 (not_1_out, Avaria_MQ_Temp);
  not not_2 (not_2_out, Avaria_SEN_Temp);
  not not_3 (not_3_out, Avaria_MQ_Hum);
  not not_4 (not_4_out, Avaria_SENS_Hum);
  and and_1 (and_1_out, not_1_out, not_2_out);
  Button button_1 (.out(button_1_out));
  and and_2 (and_2_out, ON_OFF_SORT, CLK_out);
  Button button_2 (.out(button_2_out));
  Comparator comparator_1 (
    .a(Temperatura_Prog), .b(Temperatura_Real), .gt(comparator_1_gt), .lt(comparator_1_lt));  // open: eq
  or or_1 (or_1_out, comparator_1_lt, comparator_1_gt);
  not not_5 (not_5_out, or_1_out);
  and and_3 (and_3_out, not_3_out, not_4_out);
  Comparator comparator_2 (
    .a(Humetat_Programada), .b(Humetat_Real), .gt(comparator_2_gt), .lt(comparator_2_lt));  // open: eq
  D_Flip_Flop d_ff_2 (
    .D(d_ff_2_qn), .clk(and_2_out), .Q(d_ff_2_q), .Qn(d_ff_2_qn), .preset(button_1_out), .reset(button_2_out));
  and and_4 (and_4_out, not_5_out, and_3_out);
  D_Flip_Flop d_ff_3 (
    .D(d_ff_3_qn), .clk(d_ff_2_qn), .Q(d_ff_3_q), .Qn(d_ff_3_qn), .preset(button_1_out), .reset(button_2_out));
  and and_5 (and_5_out, ON_OFF_SORT, comparator_1_gt);
  and and_6 (and_6_out, comparator_1_lt, ON_OFF_SORT);
  and and_7 (and_7_out, ON_OFF_SORT, comparator_2_gt);
  and and_8 (and_8_out, ON_OFF_SORT, comparator_2_lt);
  and and_9 (LED_3S, d_ff_2_q, d_ff_3_q);
  and and_10 (Aire_Calent, and_1_out, and_5_out);
  and and_11 (Aire_Fred, and_1_out, and_6_out);
  and and_12 (Humidificador, and_4_out, and_7_out);
  and and_13 (Deshumi, and_8_out, and_4_out);
  and and_14 (Mes_Temp, LED_3S, and_1_out, and_5_out);
  and and_15 (Menys_Temp, and_6_out, and_1_out, LED_3S);
  and and_16 (Mes_Hum, LED_3S, and_4_out, and_7_out);
  and and_17 (Menys_Hum, LED_3S, and_4_out, and_8_out);

  // Notes on the sheet:
  //   3 = true
endmodule

module C0_SIS_ALERTAS (
  input  Al0,
  input  Al1,
  input  Al2,
  input  AL4,
  input  AL5,
  input  M1,
  input  M2,
  input  ST,
  input  SH,
  input  MQT,
  input  MQH,
  output Police,
  output Jardiner,
  output Mecanic,
  output Propietari
);

  wire or_1_out, or_2_out, or_3_out;

  or or_1 (or_1_out, M1, M2);
  or or_2 (or_2_out, ST, SH);
  or or_3 (or_3_out, MQT, MQH);
  or or_4 (Police, Al1, Al2, Al0, AL4, AL5);
  or or_5 (Jardiner, or_2_out, or_1_out);
  or or_6 (Mecanic, or_3_out, or_1_out);
  or or_7 (Propietari, or_2_out, Police);
endmodule

module TV_AL (
  input  SistemaSeguretat,
  input  AvariaMotor,
  input  AvariaSensorsTH,
  input  AvariaMaqTH,
  output Police,
  output Jardiner,
  output Mecanic,
  output Propietari
);

  or or_1 (Jardiner, AvariaSensorsTH, AvariaMotor);
  or or_2 (Mecanic, AvariaMaqTH, AvariaMotor);
  or or_3 (Propietari, AvariaSensorsTH, SistemaSeguretat);

  assign Police = SistemaSeguretat;
endmodule

module TV_MV (
  input  REGANT_JI,
  input  REGANT_JE,
  input  REGANT_H,
  input  REGANT_A,
  output Motor1,
  output Motor2,
  output V1,
  output V2,
  output V3,
  output V4
);

  or or_1 (Motor1, REGANT_JE, REGANT_JI);
  or or_2 (Motor2, REGANT_A, REGANT_H);

  assign V1 = REGANT_JI;
  assign V2 = REGANT_JE;
  assign V3 = REGANT_H;
  assign V4 = REGANT_A;
endmodule
